// Logisim project cpu24.circ as structural Verilog: 33 circuits, main circuit ◇单周期MIPS
module \单周期MIPS  (
  input  IR1,
  input  IR2,
  input  IR3,
  output RegWrite,
  output MemWrite,
  output [31:0] PC,
  output [31:0] IR,
  output [31:0] RDin,
  output [31:0] MDin,
  output [31:0] LedData
);

  wire and_1_out, and_2_out, and_3_out, and_4_out, and_5_out, and_6_out, CLK, clock_1_out, comparator_2_eq,
       comparator_2_lt, comparator_4_eq, d_ff_1_q, Go, Halt, IR1_t, IR2_t, IR3_t, IRA, IRB, IRC, JAL, JR,
       mips_alu_1_equal, nand_1_out, not_1_out, not_2_out, not_3_out, not_4_out, or_4_out, pos, Rst, sh,
       SignedExt, syscall, W1, W2, W3, \单周期硬布线控制器_1_alu_src , \单周期硬布线控制器_1_beq , \单周期硬布线控制器_1_bgtz ,
       \单周期硬布线控制器_1_bne , \单周期硬布线控制器_1_jmp , \单周期硬布线控制器_1_memtoreg , \单周期硬布线控制器_1_regdst , \单周期硬布线控制器_1_v ;
  wire [3:0] \单周期硬布线控制器_1_alu_op ;
  wire [4:0] multiplexer_4_out, multiplexer_5_out, multiplexer_6_out, multiplexer_7_out, multiplexer_10_out;
  wire [9:0] mips_alu_1_result_2;
  wire [12:0] CNT_num;
  wire [15:0] ram_1_data, \总周期数 ;
  wire [27:0] shifter_1_out;
  wire [31:0] adder_2_out, mips_alu_1_result, multiplexer_1_out, multiplexer_2_out, multiplexer_3_out,
       multiplexer_8_out, multiplexer_9_out, multiplexer_12_out, multiplexer_13_out, PC_4, R1, R2,
       shifter_2_out, \符号扩展_1_out_2 ;
  wire [31:16] ram_1_data_2;

  Button button_1 (.out(Rst));
  Button _1 (.out(IRA));
  Button _2 (.out(IRB));
  Button _3 (.out(IRC));
  Button \u_继续运行  (.out(Go));
  LED #(.active("true")) led_1 (.in(W1));
  LED #(.active("true")) led_2 (.in(W2));
  LED #(.active("true")) led_3 (.in(W3));
  Hex_Digit_Display hex_digit_display_1 (.value(LedData[31:28]));  // open: dp
  Multiplexer #(.select(1), .width(32), .disabled("Z"), .enable("false")) multiplexer_1 (
    .in0(PC_4), .in1(adder_2_out), .out(multiplexer_1_out), .sel(or_4_out));
  Multiplexer #(.select(1), .width(32), .disabled("Z"), .enable("false")) multiplexer_2 (
    .in0(multiplexer_1_out), .in1(multiplexer_3_out), .out(multiplexer_2_out), .sel(\单周期硬布线控制器_1_jmp ));
  Multiplexer #(.select(1), .width(32), .disabled("Z"), .enable("false")) multiplexer_3 (
    .in0({PC_4[31:28], shifter_1_out}), .in1(R1), .out(multiplexer_3_out), .sel(JR));
  Hex_Digit_Display hex_digit_display_2 (.value(LedData[27:24]));  // open: dp
  Hex_Digit_Display hex_digit_display_3 (.value(LedData[23:20]));  // open: dp
  // Probe on multiplexer_2_out
  Register #(.width(32), .trigger("rising"), .Select("low")) u_PC (
    .D(multiplexer_2_out), .en(not_1_out), .Q(PC), .clk(CLK), .clr(Rst));
  not not_1 (not_1_out, Halt);
  Hex_Digit_Display hex_digit_display_4 (.value(LedData[19:16]));  // open: dp
  Hex_Digit_Display hex_digit_display_5 (.value(LedData[15:12]));  // open: dp
  Adder #(.width(32)) adder_1 (.a(PC), .b(32'h4), .out(PC_4));  // open: cin, cout
  // Probe on PC_4
  Hex_Digit_Display hex_digit_display_6 (.value(LedData[11:8]));  // open: dp
  Hex_Digit_Display hex_digit_display_7 (.value(LedData[7:4]));  // open: dp
  // Probe on \总周期数 
  ROM #(.addrWidth(10), .dataWidth(32), .Select("high")) rom_1 (.addr(PC[11:2]), .data(IR));
  Hex_Digit_Display hex_digit_display_8 (.value(LedData[3:0]));  // open: dp
  // Mips_Probe mips_probe_1: pin names not known; wires that end beside it: IR
  D_Flip_Flop #(.trigger("high"), .Pre_Clr_Positions("LEGACY"), .NegatePresetClear("false"), .enable("true"), .NewFFLayout("false")) d_ff_1 (.Q(d_ff_1_q));  // open: clk, D, Qn, preset, en, reset
  // Probe on 13'hc
  Comparator #(.width(6), .mode("twosComplement")) comparator_1 (
    .a(6'b101001), .b(IR[31:26]), .eq(sh));  // open: gt, lt
  Multiplexer #(.select(1), .width(5), .disabled("Z"), .enable("false")) multiplexer_4 (
    .in0(IR[20:16]), .in1(IR[15:11]), .out(multiplexer_4_out), .sel(\单周期硬布线控制器_1_regdst ));
  Shifter #(.width(28), .shift("ll")) shifter_1 (.in({2'b00, IR[25:0]}), .\dist (5'b00010), .out(shifter_1_out));
  // Probe on CNT_num
  Comparator #(.width(13), .mode("twosComplement")) comparator_2 (
    .a(CNT_num), .b(13'hc), .eq(comparator_2_eq), .lt(comparator_2_lt));  // open: gt
  Clock #(.highDuration(1), .lowDuration(1)) clock_1 (.out(clock_1_out));
  or or_1 (IR1_t, IR1, IRA);
  \单周期硬布线控制器  \u_单周期硬布线控制器_1  (
    .Func(IR[5:0]), .OP(IR[31:26]), .ALU_OP(\单周期硬布线控制器_1_alu_op ), .MemWrite(MemWrite),
    .ALU_SRC(\单周期硬布线控制器_1_alu_src ), .RegWrite(RegWrite), .SysCALL(syscall), .SignedExt(SignedExt),
    .RegDst(\单周期硬布线控制器_1_regdst ), .JR(JR), .JMP(\单周期硬布线控制器_1_jmp ), .Beq(\单周期硬布线控制器_1_beq ), .JAL(JAL),
    .Bne(\单周期硬布线控制器_1_bne ), .BGTZ(\单周期硬布线控制器_1_bgtz ), .V(\单周期硬布线控制器_1_v ), .MemToReg(\单周期硬布线控制器_1_memtoreg ));
  Multiplexer #(.select(1), .width(5), .disabled("Z"), .enable("false")) multiplexer_5 (
    .in0(IR[25:21]), .in1(5'b00010), .out(multiplexer_5_out), .sel(syscall));
  Multiplexer #(.select(1), .width(5), .disabled("Z"), .enable("false")) multiplexer_6 (
    .in0(IR[20:16]), .in1(5'b00100), .out(multiplexer_6_out), .sel(syscall));
  // Probe on multiplexer_7_out
  Multiplexer #(.select(1), .width(5), .disabled("Z"), .enable("false")) multiplexer_7 (
    .in0(multiplexer_4_out), .in1({5{1'b1}}), .out(multiplexer_7_out), .sel(JAL));
  \符号扩展  \u_符号扩展_1  (.in_1(IR[15:0]), .out_2(\符号扩展_1_out_2 ));
  // Probe on IR[15:0]
  nand nand_1 (nand_1_out, d_ff_1_q, comparator_2_eq);
  Counter #(.width(13), .max('h1fff), .ongoal("stay"), .trigger("rising"), .behavior("old")) counter_1 (
    .count(comparator_2_lt), .Q(CNT_num), .clk(clock_1_out));  // open: load, D, carry, clr, preset
  or or_2 (IR2_t, IR2, IRB);
  Multiplexer #(.select(1), .width(32), .disabled("Z"), .enable("false")) multiplexer_8 (
    .in0({{16{1'b0}}, IR[15:0]}), .in1(\符号扩展_1_out_2 ), .out(multiplexer_8_out), .sel(SignedExt));
  MIPS_Regifile mips_regifile_1 (
    .Din(RDin), .Clk(CLK), .R1(R1), .R2(R2), .WE(RegWrite), .W_num(multiplexer_7_out),
    .R1_num(multiplexer_5_out), .R2_num(multiplexer_6_out));
  // Probe on \符号扩展_1_out_2 
  assign CLK = nand_1_out ? clock_1_out : 1'bz;  // Controlled_Buffer controlled_buffer_1
  Pull_Resistor #(.pull(1)) pull_resistor_1 (.node(CLK));
  or or_3 (IR3_t, IR3, IRC);
  Multiplexer #(.select(1), .width(32), .disabled("Z"), .enable("false")) multiplexer_9 (
    .in0(R2), .in1(multiplexer_8_out), .out(multiplexer_9_out), .sel(\单周期硬布线控制器_1_alu_src ));
  Multiplexer #(.select(1), .width(5), .disabled("Z"), .enable("false")) multiplexer_10 (
    .in0(IR[10:6]), .in1(R1[4:0]), .out(multiplexer_10_out), .sel(\单周期硬布线控制器_1_v ));
  Shifter #(.width(32), .shift("ll")) shifter_2 (.in(\符号扩展_1_out_2 ), .\dist (5'b00010), .out(shifter_2_out));
  and and_1 (and_1_out, \单周期硬布线控制器_1_beq , mips_alu_1_equal);
  and and_2 (and_2_out, \单周期硬布线控制器_1_bne , not_2_out);
  not not_2 (not_2_out, mips_alu_1_equal);
  MIPS_ALU mips_alu_1 (
    .X(R1), .Y(multiplexer_9_out), .AluOP(\单周期硬布线控制器_1_alu_op ), .Equal(mips_alu_1_equal),
    .Result({mips_alu_1_result[31:12], mips_alu_1_result_2, mips_alu_1_result[1:0]}),
    .shamt(multiplexer_10_out));  // open: Result_2
  Multiplexer #(.select(1), .width(32), .disabled("Z"), .enable("false")) multiplexer_11 (
    .in0(R2), .in1(multiplexer_12_out), .out(MDin), .sel(sh));
  Adder #(.width(32)) adder_2 (.a(shifter_2_out), .b(PC_4), .out(adder_2_out));  // open: cin, cout
  Multiplexer #(.select(1), .width(32), .disabled("Z"), .enable("false")) multiplexer_12 (
    .in0({ram_1_data_2, R2[15:0]}), .in1({R2[15:0], ram_1_data}), .out(multiplexer_12_out),
    .sel(mips_alu_1_result[1]));
  Comparator #(.width(32), .mode("twosComplement")) comparator_3 (.a(R1), .b({32{1'b0}}), .gt(pos));  // open: eq, lt
  or or_4 (or_4_out, and_1_out, and_2_out, and_3_out);
  and and_3 (and_3_out, \单周期硬布线控制器_1_bgtz , pos);
  Multiplexer #(.select(1), .width(32), .disabled("Z"), .enable("false")) multiplexer_13 (
    .in0({mips_alu_1_result[31:12], mips_alu_1_result_2, mips_alu_1_result[1:0]}),
    .in1({ram_1_data_2, ram_1_data}), .out(multiplexer_13_out), .sel(\单周期硬布线控制器_1_memtoreg ));
  RAM #(.addrWidth(10), .dataWidth(32), .bus("separate"), .Select("high")) ram_1 (
    .addr(mips_alu_1_result_2), .din(MDin), .data({ram_1_data_2, ram_1_data}), .str(MemWrite), .clk(CLK),
    .ld(\单周期硬布线控制器_1_memtoreg ), .clr(Rst));  // open: sel
  // Probe on R1
  Comparator #(.width(32), .mode("twosComplement")) comparator_4 (
    .a(R1), .b(32'ha), .eq(comparator_4_eq));  // open: gt, lt
  // Probe on R2
  not not_3 (not_3_out, comparator_4_eq);
  and and_4 (and_4_out, not_3_out, syscall);
  and and_5 (and_5_out, syscall, comparator_4_eq);
  Multiplexer #(.select(1), .width(32), .disabled("Z"), .enable("false")) multiplexer_14 (
    .in0(multiplexer_13_out), .in1(PC_4), .out(RDin), .sel(JAL));
  Register #(.width(32), .trigger("rising"), .Select("low")) register_1 (
    .D(R2), .en(and_4_out), .Q(LedData), .clk(CLK), .clr(Rst));
  Register #(.width(1), .trigger("rising"), .Select("low")) register_2 (
    .D(and_5_out), .en(and_5_out), .Q(Halt), .clk(CLK), .clr(Go));
  and and_6 (and_6_out, CLK, not_4_out);
  not not_4 (not_4_out, Halt);
  Counter #(.width(16), .max('hffff), .ongoal("wrap"), .trigger("rising"), .behavior("new")) counter_2 (
    .Q(\总周期数 ), .clk(and_6_out), .clr(Rst));  // open: load, D, count, carry, preset, down

  // Notes on the sheet:
  //   中断源
  //   中断等待指示
  //   总复位信号应将除ROM以外所有存储组件全部清零
  //   数码管输出
  //   PC+4
  //   数码管输出应该用寄存器锁存，否则显示数据只能一闪而过
  //   指令存储器
  //   contents of rom_1 (hex, n*v repeats v):
  //   20110001 8100005 20110001 20120002 20130003 8100009 20110001 20120002 20130003 810000d 20110001
  //   20120002 20130003 8100011 20110001 20120002 20130003 c1000fa 20100001 20110001 118fc0 112020
  //   20020022 c 118882 12200001 8100015 112020 20020022 c 20110001 118880 112020 20020022 c 12200001
  //   810001f 20110001 118fc0 112020 20020022 c 1188c3 112020 20020022 c 118903 112020 20020022 c 118903
  //   112020 20020022 c 118903 112020 20020022 c 118903 112020 20020022 c 118903 112020 20020022 c 118903
  //   112020 20020022 c 118903 112020 20020022 c 20100001 109fc0 139fc3 8021 2012000c 24160003 26100001
  //   3210000f 20080008 20090001 139900 2709825 132020 20020022 c 1094022 1500fff9 22100001 2018000f
  //   2188024 108700 20080008 20090001 139902 2709825 132021 20020022 c 1094022 1500fff9 108702 2c9b022
  //   12c00001 8100050 4020 1084027 84400 3508ffff 82021 20020022 c 2010ffff 20110000 ae300000 22100001
  //   22310004 ae300000 22100001 22310004 ae300000 22100001 22310004 ae300000 22100001 22310004 ae300000
  //   22100001 22310004 ae300000 22100001 22310004 ae300000 22100001 22310004 ae300000 22100001 22310004
  //   ae300000 22100001 22310004 ae300000 22100001 22310004 ae300000 22100001 22310004 ae300000 22100001
  //   22310004 ae300000 22100001 22310004 ae300000 22100001 22310004 ae300000 22100001 22310004 ae300000
  //   22100001 22310004 22100001 8020 2011003c 8e130000 8e340000 274402a 11000002 ae330000 ae140000
  //   2231fffc 1611fff8 102020 20020022 c 22100004 2011003c 1611fff2 2002000a c 20080001 20090003 20110876
  //   112020 20020022 c 200b0008 1118804 1318804 112020 20020022 c 216bffff 1560fff9 2002000a c 20080001
  //   20090003 20110876 118d00 112020 20020022 c 200b0008 1118807 1318807 112020 20020022 c 216bffff
  //   1560fff9 2002000a c 20090000 200b0020 20110001 20120001 a5310000 112020 20020022 c 2328820 21290002
  //   216bffff 1560fff8 200b0010 20090000 8d310000 112020 20020022 c 21290004 216bffff 1560fff9 2002000a c
  //   2011000f 112020 20020022 c 2231ffff 1e20fffb 2002000a c 2002000a c 20100000 22100001 102020 20020022
  //   c 22100002 102020 20020022 c 22100003 102020 20020022 c 22100004 102020 20020022 c 22100005 102020
  //   20020022 c 22100006 102020 20020022 c 22100007 102020 20020022 c 22100008 102020 20020022 20020022 c
  //   3e00008
  //   OP
  //   Func
  //   rs
  //   指令字
  //   rt
  //   rd
  //   s
  //   控制位
  //   暂停节拍，不能为0
  //   JMP
  //   JR
  //   OP
  //   Func
  //   RegDst
  //   戳工具置1进入计数暂停模式，ctrl+k时钟自动运行到对应节拍暂停
  //   ctrl+k关闭时钟连续运行，将控制位置零，进入单步调试模式调试
  //   用这个时钟源需要去掉电路中的其他时钟源
  //   Beq
  //   Bgtz
  //   Bne
  //   MemToReg
  //   MemWrite
  //   AluOP
  //   AluSrcB
  //   RegWrite
  //   JAL
  //   V
  //   Syscall
  //   Sign_ext
  //   可计数暂停的时钟源
  //   为方便自动评测，需要输出PC，IR，寄存器堆写如数据RDin
  //   RAM写使能MemWrite、RAM写入数据MDin等信号
endmodule

// 单周期硬布线控制器
module \单周期硬布线控制器  (
  input  [5:0] OP,
  input  [5:0] Func,
  output [3:0] ALU_OP,
  output MemToReg,
  output MemWrite,
  output ALU_SRC,
  output RegWrite,
  output SysCALL,
  output SignedExt,
  output RegDst,
  output Beq,
  output Bne,
  output JR,
  output JMP,
  output JAL,
  output BGTZ,
  output V
);

  \运算控制器自动生成  \u_运算控制器自动生成_1  (
    .OP0(OP[0]), .OP1(OP[1]), .OP2(OP[2]), .OP3(OP[3]), .OP4(OP[4]), .OP5(OP[5]), .F0(Func[0]), .F1(Func[1]),
    .F2(Func[2]), .F3(Func[3]), .F4(Func[4]), .F5(Func[5]), .S0(ALU_OP[0]), .S1(ALU_OP[1]), .S2(ALU_OP[2]),
    .S3(ALU_OP[3]));
  \控制信号自动生成  \u_控制信号自动生成_1  (
    .OP0(OP[0]), .OP1(OP[1]), .OP2(OP[2]), .OP3(OP[3]), .OP4(OP[4]), .OP5(OP[5]), .F0(Func[0]), .F1(Func[1]),
    .F2(Func[2]), .F3(Func[3]), .F4(Func[4]), .F5(Func[5]), .MemToReg(MemToReg), .MemWrite(MemWrite),
    .ALU_SRC(ALU_SRC), .RegWrite(RegWrite), .SysCALL(SysCALL), .SignedExt(SignedExt), .RegDst(RegDst),
    .BEQ(Beq), .BNE(Bne), .JR(JR), .JUMP(JMP), .JAL(JAL), .BGTZ(BGTZ), .V(V));

  // Other names for the same wires on the sheet: OP_CODE[5:0] = OP

  // Notes on the sheet:
  //   运算器控制器，根据指令生成运算器功能选择信号
  //   控制信号生成，产生数据通路需要的其他控制信号
endmodule

// 运算器控制器
module \运算控制器自动生成  (
  input  OP0,
  input  OP1,
  input  OP2,
  input  OP3,
  input  OP4,
  input  OP5,
  input  F0,
  input  F1,
  input  F2,
  input  F3,
  input  F4,
  input  F5,
  output S0,
  output S1,
  output S2,
  output S3
);

  wire and_1_out, and_2_out, and_3_out, and_4_out, and_5_out, and_6_out, and_7_out, and_8_out, and_9_out,
       and_10_out, and_11_out, and_12_out, and_13_out, and_14_out, and_15_out, and_16_out, and_17_out,
       and_18_out, and_19_out, and_20_out, and_21_out, and_22_out, and_23_out, and_24_out, and_25_out,
       and_26_out, and_27_out, and_28_out, and_29_out, and_30_out, and_31_out, and_32_out, and_33_out,
       and_34_out, and_35_out, and_36_out, and_37_out, not_1_out, not_2_out, not_3_out, not_4_out, not_5_out,
       not_6_out, not_7_out, not_8_out, not_9_out, not_10_out, not_11_out, not_12_out, not_13_out,
       not_14_out, not_15_out, not_16_out, not_17_out, not_18_out, not_19_out, not_20_out, not_21_out,
       not_22_out, not_23_out, not_24_out, not_25_out, not_26_out, not_27_out, not_28_out, not_29_out,
       not_30_out, not_31_out, not_32_out, not_33_out, not_34_out, not_35_out, not_36_out, not_37_out,
       not_38_out, not_39_out, not_40_out, not_41_out, not_42_out, not_43_out, not_44_out, not_45_out,
       not_46_out, not_47_out, not_48_out, not_49_out, not_50_out, not_51_out, not_52_out, not_53_out,
       not_54_out, not_55_out, not_56_out, not_57_out, not_58_out, not_59_out, not_60_out, not_61_out,
       not_62_out, not_63_out, not_64_out, not_65_out, not_66_out, not_67_out, not_68_out, not_69_out,
       not_70_out, not_71_out, not_72_out, not_73_out, not_74_out, not_75_out, not_76_out, not_77_out,
       not_78_out, not_79_out, not_80_out, not_81_out, not_82_out, not_83_out, not_84_out, not_85_out,
       not_86_out, not_87_out, not_88_out, not_89_out, not_90_out, not_91_out, not_92_out, not_93_out,
       not_94_out, not_95_out, not_96_out, not_97_out, not_98_out, not_99_out, not_100_out, not_101_out,
       not_102_out, not_103_out, not_104_out, not_105_out, not_106_out, not_107_out, not_108_out,
       not_109_out, not_110_out, not_111_out, not_112_out, not_113_out, not_114_out, not_115_out,
       not_116_out, not_117_out, not_118_out, not_119_out, not_120_out, not_121_out, not_122_out,
       not_123_out, not_124_out, not_125_out, not_126_out, not_127_out, not_128_out, not_129_out,
       not_130_out, not_131_out, not_132_out, not_133_out, not_134_out, not_135_out, not_136_out,
       not_137_out, not_138_out, not_139_out, not_140_out, not_141_out, not_142_out, not_143_out,
       not_144_out, not_145_out, not_146_out, not_147_out, not_148_out, not_149_out, not_150_out,
       not_151_out, not_152_out, not_153_out, not_154_out, not_155_out, not_156_out, not_157_out,
       not_158_out, not_159_out, not_160_out, not_161_out, not_162_out, not_163_out, not_164_out,
       not_165_out, not_166_out, not_167_out, not_168_out, not_169_out, not_170_out, not_171_out,
       not_172_out, not_173_out, not_174_out, not_175_out, not_176_out, not_177_out, not_178_out,
       not_179_out, not_180_out, not_181_out, not_182_out, not_183_out, not_184_out, not_185_out,
       not_186_out, not_187_out, not_188_out, not_189_out, not_190_out, not_191_out, not_192_out,
       not_193_out, not_194_out, not_195_out, not_196_out, not_197_out, not_198_out, not_199_out,
       not_200_out, not_201_out, not_202_out, not_203_out, not_204_out, not_205_out, not_206_out,
       not_207_out, not_208_out, not_209_out, not_210_out, not_211_out, not_212_out, not_213_out,
       not_214_out, not_215_out, not_216_out, not_217_out, not_218_out, not_219_out, not_220_out,
       not_221_out, not_222_out, not_223_out, not_224_out, not_225_out, not_226_out, not_227_out,
       not_228_out, not_229_out, not_230_out, not_231_out, not_232_out, not_233_out, not_234_out,
       not_235_out, not_236_out, not_237_out, not_238_out, not_239_out, not_240_out, not_241_out,
       not_242_out, not_243_out, not_244_out, not_245_out, not_246_out, not_247_out, not_248_out,
       not_249_out, not_250_out, not_251_out;

  not not_1 (not_1_out, OP5);
  not not_2 (not_2_out, OP4);
  not not_3 (not_3_out, OP3);
  not not_4 (not_4_out, OP2);
  not not_5 (not_5_out, OP1);
  not not_6 (not_6_out, OP0);
  not not_7 (not_7_out, F5);
  not not_8 (not_8_out, F4);
  not not_9 (not_9_out, F3);
  not not_10 (not_10_out, F2);
  not not_11 (not_11_out, OP5);
  not not_12 (not_12_out, OP4);
  not not_13 (not_13_out, OP3);
  not not_14 (not_14_out, OP2);
  not not_15 (not_15_out, OP1);
  not not_16 (not_16_out, OP0);
  not not_17 (not_17_out, F4);
  not not_18 (not_18_out, F3);
  not not_19 (not_19_out, F2);
  not not_20 (not_20_out, F1);
  not not_21 (not_21_out, F0);
  not not_22 (not_22_out, OP5);
  not not_23 (not_23_out, OP4);
  not not_24 (not_24_out, OP3);
  not not_25 (not_25_out, OP2);
  not not_26 (not_26_out, OP1);
  not not_27 (not_27_out, OP0);
  not not_28 (not_28_out, F4);
  not not_29 (not_29_out, F3);
  not not_30 (not_30_out, F2);
  not not_31 (not_31_out, F1);
  not not_32 (not_32_out, OP5);
  not not_33 (not_33_out, OP4);
  not not_34 (not_34_out, OP3);
  not not_35 (not_35_out, OP2);
  not not_36 (not_36_out, OP1);
  not not_37 (not_37_out, OP0);
  not not_38 (not_38_out, F4);
  not not_39 (not_39_out, F3);
  not not_40 (not_40_out, F1);
  not not_41 (not_41_out, F0);
  not not_42 (not_42_out, OP5);
  not not_43 (not_43_out, OP4);
  not not_44 (not_44_out, OP3);
  not not_45 (not_45_out, OP2);
  not not_46 (not_46_out, OP1);
  not not_47 (not_47_out, OP0);
  not not_48 (not_48_out, F4);
  not not_49 (not_49_out, F2);
  not not_50 (not_50_out, F0);
  not not_51 (not_51_out, OP5);
  not not_52 (not_52_out, OP4);
  not not_53 (not_53_out, OP2);
  not not_54 (not_54_out, OP1);
  not not_55 (not_55_out, OP0);
  not not_56 (not_56_out, OP5);
  not not_57 (not_57_out, OP4);
  not not_58 (not_58_out, OP1);
  not not_59 (not_59_out, OP0);
  not not_60 (not_60_out, OP5);
  not not_61 (not_61_out, OP4);
  not not_62 (not_62_out, OP2);
  not not_63 (not_63_out, OP1);
  not not_64 (not_64_out, OP5);
  not not_65 (not_65_out, OP4);
  not not_66 (not_66_out, OP2);
  not not_67 (not_67_out, OP0);
  not not_68 (not_68_out, OP4);
  not not_69 (not_69_out, OP3);
  not not_70 (not_70_out, OP2);
  not not_71 (not_71_out, OP4);
  not not_72 (not_72_out, OP2);
  not not_73 (not_73_out, OP5);
  not not_74 (not_74_out, OP4);
  not not_75 (not_75_out, OP3);
  not not_76 (not_76_out, OP2);
  not not_77 (not_77_out, OP1);
  not not_78 (not_78_out, OP0);
  not not_79 (not_79_out, F5);
  not not_80 (not_80_out, F4);
  not not_81 (not_81_out, F3);
  not not_82 (not_82_out, OP4);
  not not_83 (not_83_out, OP2);
  not not_84 (not_84_out, OP1);
  not not_85 (not_85_out, OP5);
  not not_86 (not_86_out, OP4);
  not not_87 (not_87_out, OP3);
  not not_88 (not_88_out, OP2);
  not not_89 (not_89_out, OP1);
  not not_90 (not_90_out, OP0);
  not not_91 (not_91_out, F5);
  not not_92 (not_92_out, F4);
  not not_93 (not_93_out, F3);
  not not_94 (not_94_out, F2);
  not not_95 (not_95_out, F0);
  not not_96 (not_96_out, OP5);
  not not_97 (not_97_out, OP4);
  not not_98 (not_98_out, OP3);
  not not_99 (not_99_out, OP2);
  not not_100 (not_100_out, OP1);
  not not_101 (not_101_out, OP0);
  not not_102 (not_102_out, F4);
  not not_103 (not_103_out, F3);
  not not_104 (not_104_out, F2);
  not not_105 (not_105_out, F0);
  not not_106 (not_106_out, OP5);
  not not_107 (not_107_out, OP4);
  not not_108 (not_108_out, OP3);
  not not_109 (not_109_out, OP2);
  not not_110 (not_110_out, OP1);
  not not_111 (not_111_out, OP0);
  not not_112 (not_112_out, F4);
  not not_113 (not_113_out, F3);
  not not_114 (not_114_out, F1);
  not not_115 (not_115_out, F0);
  not not_116 (not_116_out, OP5);
  not not_117 (not_117_out, OP4);
  not not_118 (not_118_out, OP3);
  not not_119 (not_119_out, OP2);
  not not_120 (not_120_out, OP1);
  not not_121 (not_121_out, OP0);
  not not_122 (not_122_out, F4);
  not not_123 (not_123_out, F3);
  not not_124 (not_124_out, OP5);
  not not_125 (not_125_out, OP4);
  not not_126 (not_126_out, OP3);
  not not_127 (not_127_out, OP2);
  not not_128 (not_128_out, OP1);
  not not_129 (not_129_out, OP0);
  not not_130 (not_130_out, F4);
  not not_131 (not_131_out, F2);
  not not_132 (not_132_out, F0);
  not not_133 (not_133_out, OP5);
  not not_134 (not_134_out, OP4);
  not not_135 (not_135_out, OP1);
  not not_136 (not_136_out, OP0);
  not not_137 (not_137_out, OP5);
  not not_138 (not_138_out, OP4);
  not not_139 (not_139_out, OP2);
  not not_140 (not_140_out, OP0);
  not not_141 (not_141_out, OP5);
  not not_142 (not_142_out, OP4);
  not not_143 (not_143_out, OP3);
  not not_144 (not_144_out, OP2);
  not not_145 (not_145_out, OP1);
  not not_146 (not_146_out, OP0);
  not not_147 (not_147_out, F4);
  not not_148 (not_148_out, F3);
  not not_149 (not_149_out, F2);
  not not_150 (not_150_out, F1);
  not not_151 (not_151_out, F0);
  not not_152 (not_152_out, OP5);
  not not_153 (not_153_out, OP4);
  not not_154 (not_154_out, OP3);
  not not_155 (not_155_out, OP2);
  not not_156 (not_156_out, OP1);
  not not_157 (not_157_out, OP0);
  not not_158 (not_158_out, F4);
  not not_159 (not_159_out, F3);
  not not_160 (not_160_out, F2);
  not not_161 (not_161_out, F1);
  not not_162 (not_162_out, OP5);
  not not_163 (not_163_out, OP4);
  not not_164 (not_164_out, OP3);
  not not_165 (not_165_out, OP2);
  not not_166 (not_166_out, OP1);
  not not_167 (not_167_out, OP0);
  not not_168 (not_168_out, F4);
  not not_169 (not_169_out, F3);
  not not_170 (not_170_out, F2);
  not not_171 (not_171_out, F0);
  not not_172 (not_172_out, OP5);
  not not_173 (not_173_out, OP4);
  not not_174 (not_174_out, OP3);
  not not_175 (not_175_out, OP2);
  not not_176 (not_176_out, OP1);
  not not_177 (not_177_out, OP0);
  not not_178 (not_178_out, F4);
  not not_179 (not_179_out, F3);
  not not_180 (not_180_out, F1);
  not not_181 (not_181_out, F0);
  not not_182 (not_182_out, OP5);
  not not_183 (not_183_out, OP4);
  not not_184 (not_184_out, OP3);
  not not_185 (not_185_out, OP2);
  not not_186 (not_186_out, OP1);
  not not_187 (not_187_out, OP0);
  not not_188 (not_188_out, F4);
  not not_189 (not_189_out, F2);
  not not_190 (not_190_out, OP5);
  not not_191 (not_191_out, OP4);
  not not_192 (not_192_out, OP2);
  not not_193 (not_193_out, OP1);
  not not_194 (not_194_out, OP0);
  not not_195 (not_195_out, OP5);
  not not_196 (not_196_out, OP4);
  not not_197 (not_197_out, OP1);
  not not_198 (not_198_out, OP0);
  not not_199 (not_199_out, OP5);
  not not_200 (not_200_out, OP4);
  not not_201 (not_201_out, OP2);
  not not_202 (not_202_out, OP1);
  not not_203 (not_203_out, OP4);
  not not_204 (not_204_out, OP3);
  not not_205 (not_205_out, OP2);
  not not_206 (not_206_out, OP4);
  not not_207 (not_207_out, OP2);
  not not_208 (not_208_out, OP4);
  not not_209 (not_209_out, OP2);
  not not_210 (not_210_out, OP1);
  not not_211 (not_211_out, OP5);
  not not_212 (not_212_out, OP4);
  not not_213 (not_213_out, OP3);
  not not_214 (not_214_out, OP2);
  not not_215 (not_215_out, OP1);
  not not_216 (not_216_out, OP0);
  not not_217 (not_217_out, F4);
  not not_218 (not_218_out, F3);
  not not_219 (not_219_out, F1);
  not not_220 (not_220_out, OP5);
  not not_221 (not_221_out, OP4);
  not not_222 (not_222_out, OP3);
  not not_223 (not_223_out, OP2);
  not not_224 (not_224_out, OP1);
  not not_225 (not_225_out, OP0);
  not not_226 (not_226_out, F4);
  not not_227 (not_227_out, F3);
  not not_228 (not_228_out, OP5);
  not not_229 (not_229_out, OP4);
  not not_230 (not_230_out, OP3);
  not not_231 (not_231_out, OP2);
  not not_232 (not_232_out, OP1);
  not not_233 (not_233_out, OP0);
  not not_234 (not_234_out, F4);
  not not_235 (not_235_out, F2);
  not not_236 (not_236_out, F0);
  not not_237 (not_237_out, OP5);
  not not_238 (not_238_out, OP4);
  not not_239 (not_239_out, OP3);
  not not_240 (not_240_out, OP2);
  not not_241 (not_241_out, OP1);
  not not_242 (not_242_out, OP0);
  not not_243 (not_243_out, F4);
  not not_244 (not_244_out, F2);
  not not_245 (not_245_out, OP5);
  not not_246 (not_246_out, OP4);
  not not_247 (not_247_out, OP2);
  not not_248 (not_248_out, OP0);
  not not_249 (not_249_out, OP5);
  not not_250 (not_250_out, OP4);
  not not_251 (not_251_out, OP1);
  and and_1 (and_1_out, not_1_out, not_2_out, not_3_out, not_4_out, not_5_out, not_6_out, not_7_out, not_8_out, not_9_out, not_10_out, F1, F0);
  and and_2 (and_2_out, not_11_out, not_12_out, not_13_out, not_14_out, not_15_out, not_16_out, F5, not_17_out, not_18_out, not_19_out, not_20_out, not_21_out);
  and and_3 (and_3_out, not_22_out, not_23_out, not_24_out, not_25_out, not_26_out, not_27_out, F5, not_28_out, not_29_out, not_30_out, not_31_out, F0);
  and and_4 (and_4_out, not_32_out, not_33_out, not_34_out, not_35_out, not_36_out, not_37_out, F5, not_38_out, not_39_out, F2, not_40_out, not_41_out);
  and and_5 (and_5_out, not_42_out, not_43_out, not_44_out, not_45_out, not_46_out, not_47_out, F5, not_48_out, F3, not_49_out, F1, not_50_out);
  and and_6 (and_6_out, not_51_out, not_52_out, OP3, not_53_out, not_54_out, not_55_out);
  and and_7 (and_7_out, not_56_out, not_57_out, OP3, OP2, not_58_out, not_59_out);
  and and_8 (and_8_out, not_60_out, not_61_out, OP3, not_62_out, not_63_out, OP0);
  and and_9 (and_9_out, not_64_out, not_65_out, OP3, not_66_out, OP1, not_67_out);
  and and_10 (and_10_out, OP5, not_68_out, not_69_out, not_70_out, OP1, OP0);
  and and_11 (and_11_out, OP5, not_71_out, OP3, not_72_out, OP1, OP0);
  and and_12 (and_12_out, not_73_out, not_74_out, not_75_out, not_76_out, not_77_out, not_78_out, not_79_out, not_80_out, not_81_out, F2, F1, F0);
  and and_13 (and_13_out, OP5, not_82_out, OP3, not_83_out, not_84_out, OP0);
  and and_14 (and_14_out, not_85_out, not_86_out, not_87_out, not_88_out, not_89_out, not_90_out, not_91_out, not_92_out, not_93_out, not_94_out, F1, not_95_out);
  and and_15 (and_15_out, not_96_out, not_97_out, not_98_out, not_99_out, not_100_out, not_101_out, F5, not_102_out, not_103_out, not_104_out, F1, not_105_out);
  and and_16 (and_16_out, not_106_out, not_107_out, not_108_out, not_109_out, not_110_out, not_111_out, F5, not_112_out, not_113_out, F2, not_114_out, not_115_out);
  and and_17 (and_17_out, not_116_out, not_117_out, not_118_out, not_119_out, not_120_out, not_121_out, F5, not_122_out, not_123_out, F2, F1, F0);
  and and_18 (and_18_out, not_124_out, not_125_out, not_126_out, not_127_out, not_128_out, not_129_out, F5, not_130_out, F3, not_131_out, F1, not_132_out);
  and and_19 (and_19_out, not_133_out, not_134_out, OP3, OP2, not_135_out, not_136_out);
  and and_20 (and_20_out, not_137_out, not_138_out, OP3, not_139_out, OP1, not_140_out);
  and and_21 (and_21_out, not_141_out, not_142_out, not_143_out, not_144_out, not_145_out, not_146_out, F5, not_147_out, not_148_out, not_149_out, not_150_out, not_151_out);
  and and_22 (and_22_out, not_152_out, not_153_out, not_154_out, not_155_out, not_156_out, not_157_out, F5, not_158_out, not_159_out, not_160_out, not_161_out, F0);
  and and_23 (and_23_out, not_162_out, not_163_out, not_164_out, not_165_out, not_166_out, not_167_out, F5, not_168_out, not_169_out, not_170_out, F1, not_171_out);
  and and_24 (and_24_out, not_172_out, not_173_out, not_174_out, not_175_out, not_176_out, not_177_out, F5, not_178_out, not_179_out, F2, not_180_out, not_181_out);
  and and_25 (and_25_out, not_182_out, not_183_out, not_184_out, not_185_out, not_186_out, not_187_out, F5, not_188_out, F3, not_189_out, F1, F0);
  and and_26 (and_26_out, not_190_out, not_191_out, OP3, not_192_out, not_193_out, not_194_out);
  and and_27 (and_27_out, not_195_out, not_196_out, OP3, OP2, not_197_out, not_198_out);
  and and_28 (and_28_out, not_199_out, not_200_out, OP3, not_201_out, not_202_out, OP0);
  and and_29 (and_29_out, OP5, not_203_out, not_204_out, not_205_out, OP1, OP0);
  and and_30 (and_30_out, OP5, not_206_out, OP3, not_207_out, OP1, OP0);
  and and_31 (and_31_out, OP5, not_208_out, OP3, not_209_out, not_210_out, OP0);
  and and_32 (and_32_out, not_211_out, not_212_out, not_213_out, not_214_out, not_215_out, not_216_out, F5, not_217_out, not_218_out, F2, not_219_out, F0);
  and and_33 (and_33_out, not_220_out, not_221_out, not_222_out, not_223_out, not_224_out, not_225_out, F5, not_226_out, not_227_out, F2, F1, F0);
  and and_34 (and_34_out, not_228_out, not_229_out, not_230_out, not_231_out, not_232_out, not_233_out, F5, not_234_out, F3, not_235_out, F1, not_236_out);
  and and_35 (and_35_out, not_237_out, not_238_out, not_239_out, not_240_out, not_241_out, not_242_out, F5, not_243_out, F3, not_244_out, F1, F0);
  and and_36 (and_36_out, not_245_out, not_246_out, OP3, not_247_out, OP1, not_248_out);
  and and_37 (and_37_out, not_249_out, not_250_out, OP3, OP2, not_251_out, OP0);
  or or_1 (S1, and_14_out, and_15_out, and_16_out, and_17_out, and_18_out, and_19_out, and_20_out);
  or or_2 (S2, and_21_out, and_22_out, and_23_out, and_24_out, and_25_out, and_26_out, and_27_out, and_28_out, and_29_out, and_30_out, and_31_out);
  or or_3 (S3, and_32_out, and_33_out, and_34_out, and_35_out, and_36_out, and_37_out);
  or or_4 (S0, and_1_out, and_2_out, and_3_out, and_4_out, and_5_out, and_6_out, and_7_out, and_8_out, and_9_out, and_10_out, and_11_out, and_12_out, and_13_out);
endmodule

// 控制信号生成
module \控制信号自动生成  (
  input  OP0,
  input  OP1,
  input  OP2,
  input  OP3,
  input  OP4,
  input  OP5,
  input  F0,
  input  F1,
  input  F2,
  input  F3,
  input  F4,
  input  F5,
  output MemToReg,
  output MemWrite,
  output ALU_SRC,
  output RegWrite,
  output SysCALL,
  output SignedExt,
  output RegDst,
  output BEQ,
  output BNE,
  output JR,
  output JUMP,
  output JAL,
  output BGTZ,
  output V
);

  wire and_1_out, and_2_out, and_4_out, and_5_out, and_6_out, and_7_out, and_8_out, and_9_out, and_10_out,
       and_11_out, and_12_out, and_13_out, and_14_out, and_15_out, and_16_out, and_18_out, and_19_out,
       and_20_out, and_21_out, and_22_out, and_23_out, and_24_out, and_25_out, and_26_out, and_27_out,
       and_31_out, and_32_out, and_35_out, and_36_out, not_1_out, not_2_out, not_3_out, not_4_out, not_5_out,
       not_6_out, not_7_out, not_8_out, not_9_out, not_10_out, not_11_out, not_12_out, not_13_out,
       not_14_out, not_15_out, not_16_out, not_17_out, not_18_out, not_19_out, not_20_out, not_21_out,
       not_22_out, not_23_out, not_24_out, not_25_out, not_26_out, not_27_out, not_28_out, not_29_out,
       not_30_out, not_31_out, not_32_out, not_33_out, not_34_out, not_35_out, not_36_out, not_37_out,
       not_38_out, not_39_out, not_40_out, not_41_out, not_42_out, not_43_out, not_44_out, not_45_out,
       not_46_out, not_47_out, not_48_out, not_49_out, not_50_out, not_51_out, not_52_out, not_53_out,
       not_54_out, not_55_out, not_56_out, not_57_out, not_58_out, not_59_out, not_60_out, not_61_out,
       not_62_out, not_63_out, not_64_out, not_65_out, not_66_out, not_67_out, not_68_out, not_69_out,
       not_70_out, not_71_out, not_72_out, not_73_out, not_74_out, not_75_out, not_76_out, not_77_out,
       not_78_out, not_79_out, not_80_out, not_81_out, not_82_out, not_83_out, not_84_out, not_85_out,
       not_86_out, not_87_out, not_88_out, not_89_out, not_90_out, not_91_out, not_92_out, not_93_out,
       not_94_out, not_95_out, not_96_out, not_97_out, not_98_out, not_99_out, not_100_out, not_101_out,
       not_102_out, not_103_out, not_104_out, not_105_out, not_106_out, not_107_out, not_108_out,
       not_109_out, not_110_out, not_111_out, not_112_out, not_113_out, not_114_out, not_115_out,
       not_116_out, not_117_out, not_118_out, not_119_out, not_120_out, not_121_out, not_122_out,
       not_123_out, not_124_out, not_125_out, not_126_out, not_127_out, not_128_out, not_129_out,
       not_130_out, not_131_out, not_132_out, not_133_out, not_134_out, not_135_out, not_136_out,
       not_137_out, not_138_out, not_139_out, not_140_out, not_141_out, not_142_out, not_143_out,
       not_144_out, not_145_out, not_146_out, not_147_out, not_148_out, not_149_out, not_150_out,
       not_151_out, not_152_out, not_153_out, not_154_out, not_155_out, not_156_out, not_157_out,
       not_158_out, not_159_out, not_160_out, not_161_out, not_162_out, not_163_out, not_164_out,
       not_165_out, not_166_out, not_167_out, not_168_out, not_169_out, not_170_out, not_171_out,
       not_172_out, not_173_out, not_174_out, not_175_out, not_176_out, not_177_out, not_178_out,
       not_179_out, not_180_out, not_181_out, not_182_out, not_183_out, not_184_out, not_185_out,
       not_186_out, not_187_out, not_188_out, not_189_out, not_190_out, not_191_out, not_192_out,
       not_193_out, not_194_out, not_195_out, not_196_out, not_197_out, not_198_out, not_199_out,
       not_200_out, not_201_out, not_202_out, not_203_out, not_204_out, not_205_out, not_206_out,
       not_207_out, not_208_out, not_209_out, not_210_out, not_211_out, not_212_out, not_213_out,
       not_214_out, not_215_out, not_216_out;

  not not_1 (not_1_out, OP4);
  not not_2 (not_2_out, OP3);
  not not_3 (not_3_out, OP2);
  not not_4 (not_4_out, OP4);
  not not_5 (not_5_out, OP2);
  not not_6 (not_6_out, OP1);
  not not_7 (not_7_out, OP2);
  not not_8 (not_8_out, OP4);
  not not_9 (not_9_out, OP0);
  not not_10 (not_10_out, OP2);
  not not_11 (not_11_out, OP4);
  not not_12 (not_12_out, OP5);
  not not_13 (not_13_out, OP1);
  not not_14 (not_14_out, OP4);
  not not_15 (not_15_out, OP5);
  not not_16 (not_16_out, OP1);
  not not_17 (not_17_out, OP2);
  not not_18 (not_18_out, OP4);
  not not_19 (not_19_out, OP2);
  not not_20 (not_20_out, OP4);
  not not_21 (not_21_out, OP0);
  not not_22 (not_22_out, OP1);
  not not_23 (not_23_out, OP2);
  not not_24 (not_24_out, OP4);
  not not_25 (not_25_out, OP5);
  not not_26 (not_26_out, F0);
  not not_27 (not_27_out, F1);
  not not_28 (not_28_out, F3);
  not not_29 (not_29_out, F4);
  not not_30 (not_30_out, OP0);
  not not_31 (not_31_out, OP1);
  not not_32 (not_32_out, OP2);
  not not_33 (not_33_out, OP4);
  not not_34 (not_34_out, OP5);
  not not_35 (not_35_out, F0);
  not not_36 (not_36_out, F2);
  not not_37 (not_37_out, F3);
  not not_38 (not_38_out, F4);
  not not_39 (not_39_out, OP0);
  not not_40 (not_40_out, OP1);
  not not_41 (not_41_out, OP2);
  not not_42 (not_42_out, OP4);
  not not_43 (not_43_out, OP5);
  not not_44 (not_44_out, F1);
  not not_45 (not_45_out, F3);
  not not_46 (not_46_out, F4);
  not not_47 (not_47_out, OP0);
  not not_48 (not_48_out, OP1);
  not not_49 (not_49_out, OP2);
  not not_50 (not_50_out, OP4);
  not not_51 (not_51_out, OP5);
  not not_52 (not_52_out, F2);
  not not_53 (not_53_out, F4);
  not not_54 (not_54_out, OP0);
  not not_55 (not_55_out, OP1);
  not not_56 (not_56_out, OP2);
  not not_57 (not_57_out, OP4);
  not not_58 (not_58_out, OP5);
  not not_59 (not_59_out, F3);
  not not_60 (not_60_out, F4);
  not not_61 (not_61_out, F5);
  not not_62 (not_62_out, OP0);
  not not_63 (not_63_out, OP1);
  not not_64 (not_64_out, OP2);
  not not_65 (not_65_out, OP4);
  not not_66 (not_66_out, OP5);
  not not_67 (not_67_out, F3);
  not not_68 (not_68_out, F4);
  not not_69 (not_69_out, OP0);
  not not_70 (not_70_out, OP2);
  not not_71 (not_71_out, OP4);
  not not_72 (not_72_out, OP5);
  not not_73 (not_73_out, OP1);
  not not_74 (not_74_out, OP4);
  not not_75 (not_75_out, OP5);
  not not_76 (not_76_out, OP2);
  not not_77 (not_77_out, OP3);
  not not_78 (not_78_out, OP4);
  not not_79 (not_79_out, OP0);
  not not_80 (not_80_out, OP1);
  not not_81 (not_81_out, OP2);
  not not_82 (not_82_out, OP3);
  not not_83 (not_83_out, OP4);
  not not_84 (not_84_out, OP5);
  not not_85 (not_85_out, F0);
  not not_86 (not_86_out, F1);
  not not_87 (not_87_out, F4);
  not not_88 (not_88_out, F5);
  not not_89 (not_89_out, OP0);
  not not_90 (not_90_out, OP2);
  not not_91 (not_91_out, OP4);
  not not_92 (not_92_out, OP5);
  not not_93 (not_93_out, OP1);
  not not_94 (not_94_out, OP3);
  not not_95 (not_95_out, OP4);
  not not_96 (not_96_out, OP5);
  not not_97 (not_97_out, OP1);
  not not_98 (not_98_out, OP2);
  not not_99 (not_99_out, OP4);
  not not_100 (not_100_out, OP2);
  not not_101 (not_101_out, OP4);
  not not_102 (not_102_out, OP0);
  not not_103 (not_103_out, OP1);
  not not_104 (not_104_out, OP2);
  not not_105 (not_105_out, OP3);
  not not_106 (not_106_out, OP4);
  not not_107 (not_107_out, OP5);
  not not_108 (not_108_out, F0);
  not not_109 (not_109_out, F1);
  not not_110 (not_110_out, F3);
  not not_111 (not_111_out, F4);
  not not_112 (not_112_out, OP0);
  not not_113 (not_113_out, OP1);
  not not_114 (not_114_out, OP2);
  not not_115 (not_115_out, OP3);
  not not_116 (not_116_out, OP4);
  not not_117 (not_117_out, OP5);
  not not_118 (not_118_out, F0);
  not not_119 (not_119_out, F2);
  not not_120 (not_120_out, F3);
  not not_121 (not_121_out, F4);
  not not_122 (not_122_out, OP0);
  not not_123 (not_123_out, OP1);
  not not_124 (not_124_out, OP2);
  not not_125 (not_125_out, OP3);
  not not_126 (not_126_out, OP4);
  not not_127 (not_127_out, OP5);
  not not_128 (not_128_out, F1);
  not not_129 (not_129_out, F3);
  not not_130 (not_130_out, F4);
  not not_131 (not_131_out, OP0);
  not not_132 (not_132_out, OP1);
  not not_133 (not_133_out, OP2);
  not not_134 (not_134_out, OP3);
  not not_135 (not_135_out, OP4);
  not not_136 (not_136_out, OP5);
  not not_137 (not_137_out, F2);
  not not_138 (not_138_out, F4);
  not not_139 (not_139_out, OP0);
  not not_140 (not_140_out, OP1);
  not not_141 (not_141_out, OP2);
  not not_142 (not_142_out, OP3);
  not not_143 (not_143_out, OP4);
  not not_144 (not_144_out, OP5);
  not not_145 (not_145_out, F3);
  not not_146 (not_146_out, F4);
  not not_147 (not_147_out, F5);
  not not_148 (not_148_out, OP0);
  not not_149 (not_149_out, OP1);
  not not_150 (not_150_out, OP2);
  not not_151 (not_151_out, OP3);
  not not_152 (not_152_out, OP4);
  not not_153 (not_153_out, OP5);
  not not_154 (not_154_out, F3);
  not not_155 (not_155_out, F4);
  not not_156 (not_156_out, OP0);
  not not_157 (not_157_out, OP1);
  not not_158 (not_158_out, OP3);
  not not_159 (not_159_out, OP4);
  not not_160 (not_160_out, OP5);
  not not_161 (not_161_out, OP1);
  not not_162 (not_162_out, OP3);
  not not_163 (not_163_out, OP4);
  not not_164 (not_164_out, OP5);
  not not_165 (not_165_out, OP0);
  not not_166 (not_166_out, OP1);
  not not_167 (not_167_out, OP2);
  not not_168 (not_168_out, OP3);
  not not_169 (not_169_out, OP4);
  not not_170 (not_170_out, OP5);
  not not_171 (not_171_out, F0);
  not not_172 (not_172_out, F1);
  not not_173 (not_173_out, F2);
  not not_174 (not_174_out, F4);
  not not_175 (not_175_out, F5);
  not not_176 (not_176_out, OP0);
  not not_177 (not_177_out, OP2);
  not not_178 (not_178_out, OP3);
  not not_179 (not_179_out, OP4);
  not not_180 (not_180_out, OP5);
  not not_181 (not_181_out, F0);
  not not_182 (not_182_out, F1);
  not not_183 (not_183_out, F2);
  not not_184 (not_184_out, F4);
  not not_185 (not_185_out, F5);
  not not_186 (not_186_out, OP2);
  not not_187 (not_187_out, OP3);
  not not_188 (not_188_out, OP4);
  not not_189 (not_189_out, OP5);
  not not_190 (not_190_out, OP2);
  not not_191 (not_191_out, OP3);
  not not_192 (not_192_out, OP4);
  not not_193 (not_193_out, OP5);
  not not_194 (not_194_out, OP3);
  not not_195 (not_195_out, OP4);
  not not_196 (not_196_out, OP5);
  not not_197 (not_197_out, OP0);
  not not_198 (not_198_out, OP1);
  not not_199 (not_199_out, OP2);
  not not_200 (not_200_out, OP3);
  not not_201 (not_201_out, OP4);
  not not_202 (not_202_out, OP5);
  not not_203 (not_203_out, F0);
  not not_204 (not_204_out, F1);
  not not_205 (not_205_out, F3);
  not not_206 (not_206_out, F4);
  not not_207 (not_207_out, F5);
  not not_208 (not_208_out, OP0);
  not not_209 (not_209_out, OP1);
  not not_210 (not_210_out, OP2);
  not not_211 (not_211_out, OP3);
  not not_212 (not_212_out, OP4);
  not not_213 (not_213_out, OP5);
  not not_214 (not_214_out, F3);
  not not_215 (not_215_out, F4);
  not not_216 (not_216_out, F5);
  and and_1 (and_1_out, OP5, not_1_out, not_2_out, not_3_out, OP1, OP0);
  and and_2 (and_2_out, OP5, not_4_out, OP3, not_5_out, not_6_out, OP0);
  and and_3 (MemWrite, OP0, not_7_out, OP3, not_8_out, OP5);
  and and_4 (and_4_out, not_9_out, not_10_out, OP3, not_11_out, not_12_out);
  and and_5 (and_5_out, not_13_out, OP3, not_14_out, not_15_out);
  and and_6 (and_6_out, OP0, not_16_out, not_17_out, OP3, not_18_out);
  and and_7 (and_7_out, OP0, OP1, not_19_out, not_20_out, OP5);
  and and_8 (and_8_out, not_21_out, not_22_out, not_23_out, not_24_out, not_25_out, not_26_out, not_27_out, not_28_out, not_29_out);
  and and_9 (and_9_out, not_30_out, not_31_out, not_32_out, not_33_out, not_34_out, not_35_out, not_36_out, not_37_out, not_38_out);
  and and_10 (and_10_out, not_39_out, not_40_out, not_41_out, not_42_out, not_43_out, not_44_out, not_45_out, not_46_out, F5);
  and and_11 (and_11_out, not_47_out, not_48_out, not_49_out, not_50_out, not_51_out, F1, not_52_out, F3, not_53_out, F5);
  and and_12 (and_12_out, not_54_out, not_55_out, not_56_out, not_57_out, not_58_out, F0, F1, not_59_out, not_60_out, not_61_out);
  and and_13 (and_13_out, not_62_out, not_63_out, not_64_out, not_65_out, not_66_out, F0, F1, F2, not_67_out, not_68_out);
  and and_14 (and_14_out, not_69_out, not_70_out, OP3, not_71_out, not_72_out);
  and and_15 (and_15_out, not_73_out, OP3, not_74_out, not_75_out);
  and and_16 (and_16_out, OP0, OP1, not_76_out, not_77_out, not_78_out);
  and and_17 (SysCALL, not_79_out, not_80_out, not_81_out, not_82_out, not_83_out, not_84_out, not_85_out, not_86_out, F2, F3, not_87_out, not_88_out);
  and and_18 (and_18_out, not_89_out, not_90_out, OP3, not_91_out, not_92_out);
  and and_19 (and_19_out, not_93_out, OP2, not_94_out, not_95_out, not_96_out);
  and and_20 (and_20_out, OP0, not_97_out, not_98_out, OP3, not_99_out);
  and and_21 (and_21_out, OP0, OP1, not_100_out, not_101_out, OP5);
  and and_22 (and_22_out, not_102_out, not_103_out, not_104_out, not_105_out, not_106_out, not_107_out, not_108_out, not_109_out, not_110_out, not_111_out);
  and and_23 (and_23_out, not_112_out, not_113_out, not_114_out, not_115_out, not_116_out, not_117_out, not_118_out, not_119_out, not_120_out, not_121_out);
  and and_24 (and_24_out, not_122_out, not_123_out, not_124_out, not_125_out, not_126_out, not_127_out, not_128_out, not_129_out, not_130_out, F5);
  and and_25 (and_25_out, not_131_out, not_132_out, not_133_out, not_134_out, not_135_out, not_136_out, F1, not_137_out, F3, not_138_out, F5);
  and and_26 (and_26_out, not_139_out, not_140_out, not_141_out, not_142_out, not_143_out, not_144_out, F0, F1, not_145_out, not_146_out, not_147_out);
  and and_27 (and_27_out, not_148_out, not_149_out, not_150_out, not_151_out, not_152_out, not_153_out, F0, F1, F2, not_154_out, not_155_out);
  and and_28 (BEQ, not_156_out, not_157_out, OP2, not_158_out, not_159_out, not_160_out);
  and and_29 (BNE, OP0, not_161_out, OP2, not_162_out, not_163_out, not_164_out);
  and and_30 (JR, not_165_out, not_166_out, not_167_out, not_168_out, not_169_out, not_170_out, not_171_out, not_172_out, not_173_out, F3, not_174_out, not_175_out);
  and and_31 (and_31_out, not_176_out, not_177_out, not_178_out, not_179_out, not_180_out, not_181_out, not_182_out, not_183_out, F3, not_184_out, not_185_out);
  and and_32 (and_32_out, OP1, not_186_out, not_187_out, not_188_out, not_189_out);
  and and_33 (JAL, OP0, OP1, not_190_out, not_191_out, not_192_out, not_193_out);
  and and_34 (BGTZ, OP0, OP1, OP2, not_194_out, not_195_out, not_196_out);
  and and_35 (and_35_out, not_197_out, not_198_out, not_199_out, not_200_out, not_201_out, not_202_out, not_203_out, not_204_out, F2, not_205_out, not_206_out, not_207_out);
  and and_36 (and_36_out, not_208_out, not_209_out, not_210_out, not_211_out, not_212_out, not_213_out, F0, F1, F2, not_214_out, not_215_out, not_216_out);
  or or_1 (MemToReg, and_1_out, and_2_out);
  or or_2 (ALU_SRC, and_4_out, and_5_out, and_6_out, and_7_out);
  or or_3 (RegWrite, and_8_out, and_9_out, and_10_out, and_11_out, and_12_out, and_13_out, and_14_out, and_15_out, and_16_out);
  or or_4 (SignedExt, and_18_out, and_19_out, and_20_out, and_21_out);
  or or_5 (RegDst, and_22_out, and_23_out, and_24_out, and_25_out, and_26_out, and_27_out);
  or or_6 (JUMP, and_31_out, and_32_out);
  or or_7 (V, and_35_out, and_36_out);
endmodule

// ALU
module MIPS_ALU (
  input  [4:0] shamt,
  input  [31:0] X,
  input  [31:0] Y,
  input  [3:0] AluOP,
  output Equal,
  output [31:0] Result,
  output [31:0] Result_2
);

  wire [0:0] comparator_1_lt, comparator_2_lt;
  wire [31:0] adder_1_out, AND_out, divider_1_out, divider_1_rem, multiplier_1_cout, multiplier_1_out,
       NOR_out, OR_out, shifter_1_out, shifter_2_out, shifter_3_out, subtractor_1_out, XOR_out;

  assign AND_out = X & Y;  // AND_Gate AND, 32 bits wide
  assign OR_out = X | Y;  // OR_Gate OR, 32 bits wide
  Shifter #(.width(32), .shift("ll")) shifter_1 (.in(Y), .\dist (shamt), .out(shifter_1_out));
  Shifter #(.width(32), .shift("ar")) shifter_2 (.in(Y), .\dist (shamt), .out(shifter_2_out));
  Shifter #(.width(32), .shift("lr")) shifter_3 (.in(Y), .\dist (shamt), .out(shifter_3_out));
  Multiplier #(.width(32)) multiplier_1 (.a(X), .b(Y), .out(multiplier_1_out), .cout(multiplier_1_cout));  // open: cin
  Divider #(.width(32)) divider_1 (.a(X), .b(Y), .out(divider_1_out), .rem(divider_1_rem));  // open: upper
  Adder #(.width(32)) adder_1 (.a(X), .b(Y), .out(adder_1_out));  // open: cin, cout
  Subtractor #(.width(32)) subtractor_1 (.a(X), .b(Y), .out(subtractor_1_out));  // open: bin, bout
  assign XOR_out = X ^ Y;  // XOR_Gate XOR, 32 bits wide
  assign NOR_out = ~(X | Y);  // NOR_Gate NOR, 32 bits wide
  Comparator #(.width(32), .mode("twosComplement")) comparator_1 (
    .a(X), .b(Y), .eq(Equal), .lt(comparator_1_lt[0]));  // open: gt
  Comparator #(.width(32), .mode("unsigned")) comparator_2 (.a(X), .b(Y), .lt(comparator_2_lt[0]));  // open: gt, eq
  Multiplexer #(.select(4), .width(32), .disabled("Z"), .enable("false")) multiplexer_1 (
    .in0(shifter_1_out), .in1(shifter_2_out), .in2(shifter_3_out), .in3(multiplier_1_out),
    .in4(divider_1_out), .in5(adder_1_out), .in6(subtractor_1_out), .in7(AND_out), .in8(OR_out),
    .in9(XOR_out), .in10(NOR_out), .in11({{31{1'b0}}, comparator_1_lt[0]}),
    .in12({{31{1'b0}}, comparator_2_lt[0]}), .in13({32{1'b0}}), .in14({32{1'b0}}), .in15({32{1'b0}}),
    .out(Result), .sel(AluOP));
  Multiplexer #(.select(4), .width(32), .disabled("Z"), .enable("false")) multiplexer_2 (
    .in0({32{1'b0}}), .in1({32{1'b0}}), .in2({32{1'b0}}), .in3(multiplier_1_cout), .in4(divider_1_rem),
    .in5({32{1'b0}}), .in6({32{1'b0}}), .in7({32{1'b0}}), .in8({32{1'b0}}), .in9({32{1'b0}}),
    .in10({32{1'b0}}), .in11({32{1'b0}}), .in12({32{1'b0}}), .in13({32{1'b0}}), .in14({32{1'b0}}),
    .in15({32{1'b0}}), .out(Result_2), .sel(AluOP));

  // Other names for the same wires on the sheet: Result2[31:0] = Result_2; S[3:0] = AluOP

  // Notes on the sheet:
  //   不要改变此引脚区域内容，也不要改变ALU封装形式
  //   输入引脚
  //   输出引脚
endmodule

module MIPS_Regifile (
  input  [31:0] Din,
  input  Clk,
  input  WE,
  input  [4:0] R1_num,
  input  [4:0] W_num,
  input  [4:0] R2_num,
  output [31:0] R1,
  output [31:0] R2
);

  // RegisterFile registerfile_1: pin names not known; wires that end beside it: Din, Clk, WE, W_num, R1_num, R2_num, R1, R2
endmodule

module \MIPS_Regfile_上升沿  (
  input  [31:0] Din,
  input  Clk,
  input  WE,
  input  [4:0] R1_num,
  input  [4:0] W_num,
  input  [4:0] R2_num,
  output [31:0] R1,
  output [31:0] R2
);

  // RegisterFile registerfile_1: pin names not known; wires that end beside it: Din, Clk, WE, W_num, R1_num, R2_num, R1, R2
endmodule

module \理想流水线  (
  output RegWrite,
  output MemWrite,
  output [31:0] IF_PC,
  output [31:0] ID_PC,
  output [31:0] EX_PC,
  output [31:0] M_PC,
  output [31:0] WB_PC,
  output [31:0] RDin,
  output [31:0] MDin,
  output [31:0] LedData
);

  wire and_1_out, and_2_out, and_3_out, and_4_out, and_5_out, and_6_out, CLK, clock_1_out, clock_2_out,
       comparator_1_eq, comparator_3_eq, comparator_3_lt, comparator_4_gt, d_ff_1_q, ex_mem_1_jal_2,
       ex_mem_1_memtoreg_2, ex_mem_1_regwrite_2, ex_mem_1_sh_2, ex_mem_1_syscall_2, Go, Halt,
       id_ex_1_alusrcb_2, id_ex_1_beq_2, id_ex_1_bgtz_2, id_ex_1_bne_2, id_ex_1_jal_2, id_ex_1_memtoreg_2,
       id_ex_1_memwrite_2, id_ex_1_regwrite_2, id_ex_1_sh_2, id_ex_1_syscall_2, id_ex_1_v_2, IR1, IR2, IR3,
       JAL, JR, mem_wb_1_jal_2, mem_wb_1_memtoreg_2, mips_alu_1_equal, nand_1_out, not_1_out, not_2_out,
       not_3_out, not_4_out, or_1_out, Rst, sh, SignedExt, syscall, W1, W2, W3, \单周期硬布线控制器_1_alu_src ,
       \单周期硬布线控制器_1_beq , \单周期硬布线控制器_1_bgtz , \单周期硬布线控制器_1_bne , \单周期硬布线控制器_1_jmp , \单周期硬布线控制器_1_memtoreg ,
       \单周期硬布线控制器_1_memwrite , \单周期硬布线控制器_1_regdst , \单周期硬布线控制器_1_regwrite , \单周期硬布线控制器_1_syscall ,
       \单周期硬布线控制器_1_v ;
  wire [3:0] id_ex_1_aluop_2, \单周期硬布线控制器_1_alu_op ;
  wire [4:0] ex_mem_1_writereg_2, id_ex_1_rs_2, id_ex_1_s_2, id_ex_1_writereg_2, multiplexer_4_out,
       multiplexer_5_out, multiplexer_6_out, multiplexer_10_out, WR, WriteReg;
  wire [12:0] CNT_num;
  wire [15:0] \LoadUse次数 , R2, ram_1_data, \总周期数 , \插入气泡数 , \无条件分支数 , \条件分支成功数 ;
  wire [25:0] if_id_1_rd_out_2;
  wire [27:0] shifter_1_out;
  wire [31:0] adder_2_out, EX_IR, ex_mem_1_pc_4_2, ex_mem_1_result_2, ex_mem_1_rs_2, ex_mem_1_rt_2,
       id_ex_1_ext_2, id_ex_1_pc_4_2, id_ex_1_rt_2, id_ex_1_sign_ext_2, ID_IR, if_id_1_pc_4_out, IF_IR,
       MEM_IR, mem_wb_1_pc_4_2, mem_wb_1_rd_2, mem_wb_1_result_2, mips_alu_1_result, mips_probe_3_p1,
       mips_regifile_1_r1, mips_regifile_1_r2, multiplexer_1_out, multiplexer_2_out, multiplexer_3_out,
       multiplexer_8_out, multiplexer_9_out, multiplexer_12_out, multiplexer_13_out, PC_4, R1, RS, RT,
       shifter_2_out, WB_IR, \符号扩展_1_out_2 ;
  wire [31:5] id_ex_1_rs_2_2;
  wire [31:16] ram_1_data_2;
  wire [31:26] if_id_1_rd_out;

  Button \u_总复位  (.out(Rst));
  Button _1 (.out(IR1));
  Button _2 (.out(IR2));
  Button _3 (.out(IR3));
  // Probe on \总周期数 
  // Probe on \总周期数 
  Button \u_继续运行  (.out(Go));
  LED #(.active("true")) led_1 (.in(W1));
  LED #(.active("true")) led_2 (.in(W2));
  LED #(.active("true")) led_3 (.in(W3));
  Multiplexer #(.select(1), .width(32), .disabled("Z"), .enable("false")) multiplexer_1 (
    .in0(PC_4), .in1(adder_2_out), .out(multiplexer_1_out), .sel(or_1_out));
  Multiplexer #(.select(1), .width(32), .disabled("Z"), .enable("false")) multiplexer_2 (
    .in0({PC_4[31:28], shifter_1_out}), .in1(R1), .out(multiplexer_2_out), .sel(JR));
  Hex_Digit_Display hex_digit_display_1 (.value(LedData[31:28]));  // open: dp
  // Probe on IF_PC[19:0]
  // Mips_Probe mips_probe_1: pin names not known; wires that end beside it: IF_IR
  Register #(.width(32), .trigger("rising"), .Select("low")) PC (
    .D(multiplexer_3_out), .en(not_1_out), .Q(IF_PC), .clk(CLK), .clr(Rst));
  Multiplexer #(.select(1), .width(32), .disabled("Z"), .enable("false")) multiplexer_3 (
    .in0(multiplexer_1_out), .in1(multiplexer_2_out), .out(multiplexer_3_out), .sel(\单周期硬布线控制器_1_jmp ));
  not not_1 (not_1_out, Halt);
  Hex_Digit_Display hex_digit_display_2 (.value(LedData[27:24]));  // open: dp
  Hex_Digit_Display hex_digit_display_3 (.value(LedData[23:20]));  // open: dp
  // Probe on ID_PC[19:0]
  // Mips_Probe mips_probe_2: pin names not known; wires that end beside it: ID_IR
  Adder #(.width(32)) adder_1 (.a(IF_PC), .b(32'h4), .out(PC_4));  // open: cin, cout
  Hex_Digit_Display hex_digit_display_4 (.value(LedData[19:16]));  // open: dp
  Hex_Digit_Display hex_digit_display_5 (.value(LedData[15:12]));  // open: dp
  // Mips_Probe mips_probe_3: pin names not known; wires that end beside it: mips_probe_3_p1
  Hex_Digit_Display hex_digit_display_6 (.value(LedData[11:8]));  // open: dp
  Hex_Digit_Display hex_digit_display_7 (.value(LedData[7:4]));  // open: dp
  Clock #(.highDuration(1), .lowDuration(1)) clock_1 (.out(clock_1_out));
  // Probe on EX_PC[19:0]
  // Mips_Probe mips_probe_4: pin names not known; wires that end beside it: clock_1_out, EX_IR, CLK
  ROM #(.addrWidth(10), .dataWidth(32), .Select("high")) rom_1 (.addr(IF_PC[11:2]), .data(mips_probe_3_p1));
  Hex_Digit_Display hex_digit_display_8 (.value(LedData[3:0]));  // open: dp
  IF_ID if_id_1 (
    .RD_in(mips_probe_3_p1), .PC_4_in(PC_4), .RD_out({if_id_1_rd_out, if_id_1_rd_out_2}),
    .PC_4_out(if_id_1_pc_4_out), .CLK(CLK), .PC(IF_PC), .PC_2(ID_PC));
  // Probe on RS
  Comparator #(.width(32), .mode("twosComplement")) comparator_1 (
    .a(RS), .b(32'ha), .eq(comparator_1_eq));  // open: gt, lt
  // Probe on \总周期数 
  // Probe on M_PC[19:0]
  // Mips_Probe mips_probe_5: pin names not known; wires that end beside it: MEM_IR
  Comparator #(.width(6), .mode("twosComplement")) comparator_2 (
    .a(6'b011101), .b(if_id_1_rd_out), .eq(sh));  // open: gt, lt
  Multiplexer #(.select(1), .width(5), .disabled("Z"), .enable("false")) multiplexer_4 (
    .in0(if_id_1_rd_out_2[20:16]), .in1(if_id_1_rd_out_2[15:11]), .out(multiplexer_4_out),
    .sel(\单周期硬布线控制器_1_regdst ));
  Shifter #(.width(28), .shift("ll")) shifter_1 (
    .in({2'b00, if_id_1_rd_out_2}), .\dist (5'b00010), .out(shifter_1_out));
  not not_2 (not_2_out, comparator_1_eq);
  and and_1 (and_1_out, not_2_out, syscall);
  and and_2 (and_2_out, syscall, comparator_1_eq);
  // Probe on \总周期数 
  // Probe on \无条件分支数 
  // Probe on \条件分支成功数 
  // Probe on \插入气泡数 
  // Probe on \LoadUse次数 
  \单周期硬布线控制器  \u_单周期硬布线控制器_1  (
    .Func(if_id_1_rd_out_2[5:0]), .OP(if_id_1_rd_out), .ALU_OP(\单周期硬布线控制器_1_alu_op ),
    .MemWrite(\单周期硬布线控制器_1_memwrite ), .ALU_SRC(\单周期硬布线控制器_1_alu_src ), .RegWrite(\单周期硬布线控制器_1_regwrite ),
    .SysCALL(\单周期硬布线控制器_1_syscall ), .SignedExt(SignedExt), .RegDst(\单周期硬布线控制器_1_regdst ), .JR(JR),
    .JMP(\单周期硬布线控制器_1_jmp ), .Beq(\单周期硬布线控制器_1_beq ), .JAL(JAL), .Bne(\单周期硬布线控制器_1_bne ),
    .BGTZ(\单周期硬布线控制器_1_bgtz ), .V(\单周期硬布线控制器_1_v ), .MemToReg(\单周期硬布线控制器_1_memtoreg ));
  Multiplexer #(.select(1), .width(5), .disabled("Z"), .enable("false")) multiplexer_5 (
    .in0(if_id_1_rd_out_2[25:21]), .in1(5'b00010), .out(multiplexer_5_out), .sel(\单周期硬布线控制器_1_syscall ));
  Multiplexer #(.select(1), .width(5), .disabled("Z"), .enable("false")) multiplexer_6 (
    .in0(if_id_1_rd_out_2[20:16]), .in1(5'b00100), .out(multiplexer_6_out), .sel(\单周期硬布线控制器_1_syscall ));
  Multiplexer #(.select(1), .width(5), .disabled("Z"), .enable("false")) multiplexer_7 (
    .in0(multiplexer_4_out), .in1({5{1'b1}}), .out(WR), .sel(JAL));
  \符号扩展  \u_符号扩展_1  (.in_1(if_id_1_rd_out_2[15:0]), .out_2(\符号扩展_1_out_2 ));
  // Probe on RT
  Register #(.width(32), .trigger("rising"), .Select("low")) register_1 (
    .D(RT), .en(and_1_out), .Q(LedData), .clk(CLK), .clr(Rst));
  Register #(.width(1), .trigger("rising"), .Select("low")) register_2 (
    .D(and_2_out), .en(and_2_out), .Q(Halt), .clk(CLK), .clr(Go));
  // Probe on IF_PC[11:0]
  // Probe on WB_PC[19:0]
  // Mips_Probe mips_probe_6: pin names not known; wires that end beside it: WB_IR
  // Probe on EX_PC[11:0]
  // Probe on ID_PC[11:0]
  MIPS_Regifile mips_regifile_1 (
    .Din(RDin), .Clk(CLK), .R1(mips_regifile_1_r1), .R2(mips_regifile_1_r2), .WE(RegWrite), .W_num(WriteReg),
    .R1_num(multiplexer_5_out), .R2_num(multiplexer_6_out));
  Multiplexer #(.select(1), .width(32), .disabled("Z"), .enable("false")) multiplexer_8 (
    .in0({{16{1'b0}}, if_id_1_rd_out_2[15:0]}), .in1(\符号扩展_1_out_2 ), .out(multiplexer_8_out), .sel(SignedExt));
  and and_3 (and_3_out, CLK, not_3_out);
  not not_3 (not_3_out, Halt);
  // Probe on M_PC[11:0]
  D_Flip_Flop #(.trigger("high"), .Pre_Clr_Positions("LEGACY"), .NegatePresetClear("false"), .enable("true"), .NewFFLayout("false")) d_ff_1 (.Q(d_ff_1_q));  // open: clk, D, Qn, preset, en, reset
  // Probe on 13'hc
  ID_EX id_ex_1 (
    .Beq(\单周期硬布线控制器_1_beq ), .Bgtz(\单周期硬布线控制器_1_bgtz ), .Bne(\单周期硬布线控制器_1_bne ),
    .MemToReg(\单周期硬布线控制器_1_memtoreg ), .MemWrite(\单周期硬布线控制器_1_memwrite ), .AluOP(\单周期硬布线控制器_1_alu_op ),
    .AluSrcB(\单周期硬布线控制器_1_alu_src ), .JAL(JAL), .V(\单周期硬布线控制器_1_v ), .RS(mips_regifile_1_r1),
    .RT(mips_regifile_1_r2), .WriteReg(WR), .Sign_ext(\符号扩展_1_out_2 ), .Beq_2(id_ex_1_beq_2),
    .Bgtz_2(id_ex_1_bgtz_2), .Bne_2(id_ex_1_bne_2), .MemToReg_2(id_ex_1_memtoreg_2),
    .MemWrite_2(id_ex_1_memwrite_2), .AluOP_2(id_ex_1_aluop_2), .AluSrcB_2(id_ex_1_alusrcb_2),
    .JAL_2(id_ex_1_jal_2), .V_2(id_ex_1_v_2), .RS_2({id_ex_1_rs_2_2, id_ex_1_rs_2}), .RT_2(id_ex_1_rt_2),
    .WriteReg_2(id_ex_1_writereg_2), .Sign_ext_2(id_ex_1_sign_ext_2), .CLK(CLK),
    .RegWrite(\单周期硬布线控制器_1_regwrite ), .RegWrite_2(id_ex_1_regwrite_2), .ext(multiplexer_8_out),
    .ext_2(id_ex_1_ext_2), .S(if_id_1_rd_out_2[10:6]), .S_2(id_ex_1_s_2), .PC_4(if_id_1_pc_4_out),
    .PC_4_2(id_ex_1_pc_4_2), .PC(ID_PC), .PC_2(EX_PC), .syscall(\单周期硬布线控制器_1_syscall ),
    .syscall_2(id_ex_1_syscall_2), .sh(sh), .sh_2(id_ex_1_sh_2));
  Counter #(.width(16), .max('hffff), .ongoal("wrap"), .trigger("rising"), .behavior("new")) counter_1 (
    .Q(\总周期数 ), .clk(and_3_out), .clr(Rst));  // open: load, D, count, carry, preset, down
  // Probe on WB_PC[11:0]
  Comparator #(.width(13), .mode("twosComplement")) comparator_3 (
    .a(CNT_num), .b(13'hc), .eq(comparator_3_eq), .lt(comparator_3_lt));  // open: gt
  Clock #(.highDuration(1), .lowDuration(1)) clock_2 (.out(clock_2_out));
  Comparator #(.width(32), .mode("twosComplement")) comparator_4 (
    .a({id_ex_1_rs_2_2, id_ex_1_rs_2}), .b({32{1'b0}}), .gt(comparator_4_gt));  // open: eq, lt
  Multiplexer #(.select(1), .width(32), .disabled("Z"), .enable("false")) multiplexer_9 (
    .in0(id_ex_1_rt_2), .in1(id_ex_1_ext_2), .out(multiplexer_9_out), .sel(id_ex_1_alusrcb_2));
  nand nand_1 (nand_1_out, d_ff_1_q, comparator_3_eq);
  Counter #(.width(13), .max('h1fff), .ongoal("stay"), .trigger("rising"), .behavior("old")) counter_2 (
    .count(comparator_3_lt), .Q(CNT_num), .clk(clock_2_out));  // open: load, D, carry, clr, preset
  Multiplexer #(.select(1), .width(5), .disabled("Z"), .enable("false")) multiplexer_10 (
    .in0(id_ex_1_s_2), .in1(id_ex_1_rs_2), .out(multiplexer_10_out), .sel(id_ex_1_v_2));
  Shifter #(.width(32), .shift("ll")) shifter_2 (.in(id_ex_1_sign_ext_2), .\dist (5'b00010), .out(shifter_2_out));
  assign CLK = nand_1_out ? clock_2_out : 1'bz;  // Controlled_Buffer controlled_buffer_1
  and and_4 (and_4_out, id_ex_1_beq_2, mips_alu_1_equal);
  and and_5 (and_5_out, id_ex_1_bne_2, not_4_out);
  not not_4 (not_4_out, mips_alu_1_equal);
  and and_6 (and_6_out, id_ex_1_bgtz_2, comparator_4_gt);
  MIPS_ALU mips_alu_1 (
    .X({id_ex_1_rs_2_2, id_ex_1_rs_2}), .Y(multiplexer_9_out), .AluOP(id_ex_1_aluop_2),
    .Equal(mips_alu_1_equal), .Result(mips_alu_1_result), .shamt(multiplexer_10_out));  // open: Result_2
  Adder #(.width(32)) adder_2 (.a(shifter_2_out), .b(id_ex_1_pc_4_2), .out(adder_2_out));  // open: cin, cout
  Pull_Resistor #(.pull(1)) pull_resistor_1 (.node(CLK));
  or or_1 (or_1_out, and_4_out, and_5_out, and_6_out);
  EX_MEM ex_mem_1 (
    .MemToReg(id_ex_1_memtoreg_2), .MemWrite(id_ex_1_memwrite_2), .RegWrite(id_ex_1_regwrite_2),
    .JAL(id_ex_1_jal_2), .Result(mips_alu_1_result), .WriteReg(id_ex_1_writereg_2), .PC_4(id_ex_1_pc_4_2),
    .MemToReg_2(ex_mem_1_memtoreg_2), .MemWrite_2(MemWrite), .RegWrite_2(ex_mem_1_regwrite_2),
    .JAL_2(ex_mem_1_jal_2), .Result_2(ex_mem_1_result_2), .WriteReg_2(ex_mem_1_writereg_2),
    .PC_4_2(ex_mem_1_pc_4_2), .CLK(CLK), .RT(id_ex_1_rt_2), .RT_2(ex_mem_1_rt_2), .PC(EX_PC), .PC_2(M_PC),
    .syscall(id_ex_1_syscall_2), .syscall_2(ex_mem_1_syscall_2), .RS({id_ex_1_rs_2_2, id_ex_1_rs_2}),
    .RS_2(ex_mem_1_rs_2), .sh(id_ex_1_sh_2), .sh_2(ex_mem_1_sh_2));  // open: CLR, en
  Multiplexer #(.select(1), .width(32), .disabled("Z"), .enable("false")) multiplexer_11 (
    .in0(ex_mem_1_rt_2), .in1(multiplexer_12_out), .out(MDin), .sel(ex_mem_1_sh_2));
  Multiplexer #(.select(1), .width(32), .disabled("Z"), .enable("false")) multiplexer_12 (
    .in0({ram_1_data_2, R2}), .in1({R2, ram_1_data}), .out(multiplexer_12_out), .sel(ex_mem_1_result_2[1]));
  RAM #(.addrWidth(10), .dataWidth(32), .bus("separate"), .Select("high")) ram_1 (
    .addr(ex_mem_1_result_2[11:2]), .din(MDin), .data({ram_1_data_2, ram_1_data}), .str(MemWrite), .clk(CLK),
    .ld(ex_mem_1_memtoreg_2), .clr(Rst));  // open: sel
  MEM_WB mem_wb_1 (
    .MemToReg(ex_mem_1_memtoreg_2), .RegWrite(ex_mem_1_regwrite_2), .JAL(ex_mem_1_jal_2),
    .RD({ram_1_data_2, ram_1_data}), .WriteReg(ex_mem_1_writereg_2), .PC_4(ex_mem_1_pc_4_2),
    .MemToReg_2(mem_wb_1_memtoreg_2), .RegWrite_2(RegWrite), .JAL_2(mem_wb_1_jal_2), .RD_2(mem_wb_1_rd_2),
    .WriteReg_2(WriteReg), .PC_4_2(mem_wb_1_pc_4_2), .CLK(CLK), .Result(ex_mem_1_result_2),
    .Result_2(mem_wb_1_result_2), .PC(M_PC), .PC_2(WB_PC), .syscall(ex_mem_1_syscall_2), .syscall_2(syscall),
    .RT(MDin), .RT_2(RT), .RS(ex_mem_1_rs_2), .RS_2(RS));  // open: CLR, en
  Multiplexer #(.select(1), .width(32), .disabled("Z"), .enable("false")) multiplexer_13 (
    .in0(mem_wb_1_result_2), .in1(mem_wb_1_rd_2), .out(multiplexer_13_out), .sel(mem_wb_1_memtoreg_2));
  Multiplexer #(.select(1), .width(32), .disabled("Z"), .enable("false")) multiplexer_14 (
    .in0(multiplexer_13_out), .in1(mem_wb_1_pc_4_2), .out(RDin), .sel(mem_wb_1_jal_2));

  // Other names for the same wires on the sheet: MEM_PC[31:0] = M_PC

  // Notes on the sheet:
  //   中断源
  //   时空图监测，可删除
  //   BranchTaken
  //   中断等待指示
  //   取指令（IF）
  //   PC+4
  //   数码管输出
  //   指令存储器
  //   contents of rom_1 (hex, n*v repeats v):
  //   20100000 20110000 20120000 20130000 36100000 36310001 36520002 36730003 ae100000 ae110004 ae120008
  //   ae13000c 2002000a 20110000 20120000 20130000 c
  //   指令字
  //   OP
  //   Func
  //   rs
  //   rt
  //   rd
  //   s
  //   译码（ID）
  //   JMP
  //   JR
  //   OP
  //   Func
  //   RegDst
  //   Sign_ext
  //   Beq
  //   Bgtz
  //   Bne
  //   MemToReg
  //   MemWrite
  //   AluOP
  //   AluSrcB
  //   RegWrite
  //   JAL
  //   V
  //   Syscall
  //   控制位
  //   流水调试日志用
  //   暂停节拍，不能为0
  //   戳工具置1进入计数暂停模式，ctrl+k时钟自动运行到对应节拍暂停
  //   ctrl+k关闭时钟连续运行，将控制位置零，进入单步调试模式调试
  //   用这个时钟源需要去掉电路中的其他时钟源
  //   执行（EX）
  //   可计数暂停的时钟源
  //   访存（MEM）
  //   为方便自动评测，需要输出流水线各段保存的PC值，注意是PC不是PC+4，另外ID段寄存器写入信息，Mem段内存写入信息也要输出
  //   写回（WB）
endmodule

module \气泡流水线  (
  output RegWrite,
  output MemWrite,
  output [31:0] IF_PC,
  output [31:0] ID_PC,
  output [31:0] EX_PC,
  output [31:0] M_PC,
  output [31:0] WB_PC,
  output [31:0] RDin,
  output [31:0] MDin,
  output [31:0] LedData
);

  wire and_2_out, and_3_out, and_4_out, and_5_out, and_6_out, and_7_out, BranchTaken, CLK, clock_1_out,
       clock_2_out, comparator_1_eq, comparator_3_eq, comparator_3_lt, comparator_4_gt, d_ff_1_q,
       ex_mem_1_jal_2, ex_mem_1_memtoreg_2, ex_mem_1_regwrite_2, ex_mem_1_sh_2, ex_mem_1_syscall_2, Go, Halt,
       HS, id_ex_bubble_1_alusrcb_2, id_ex_bubble_1_beq_2, id_ex_bubble_1_bgtz_2, id_ex_bubble_1_bne_2,
       id_ex_bubble_1_jal_2, id_ex_bubble_1_memtoreg_2, id_ex_bubble_1_memwrite_2, id_ex_bubble_1_regwrite_2,
       id_ex_bubble_1_sh_2, id_ex_bubble_1_syscall_2, id_ex_bubble_1_v_2, IR1, IR2, IR3, JAL, JMP, JR,
       mem_wb_1_jal_2, mem_wb_1_memtoreg_2, mips_alu_1_equal, nand_1_out, not_1_out, not_2_out, not_3_out,
       not_4_out, not_5_out, not_6_out, not_7_out, or_1_out, or_2_out, or_3_out, Rst, sh, SignedExt, stall,
       syscall, W1, W2, W3, \单周期硬布线控制器_1_alu_src , \单周期硬布线控制器_1_beq , \单周期硬布线控制器_1_bgtz , \单周期硬布线控制器_1_bne ,
       \单周期硬布线控制器_1_jmp , \单周期硬布线控制器_1_jr , \单周期硬布线控制器_1_memtoreg , \单周期硬布线控制器_1_memwrite ,
       \单周期硬布线控制器_1_regdst , \单周期硬布线控制器_1_regwrite , \单周期硬布线控制器_1_syscall , \单周期硬布线控制器_1_v ,
       \气泡流水线相关处理逻辑_1_flush ;
  wire [3:0] id_ex_bubble_1_aluop_2, \单周期硬布线控制器_1_alu_op ;
  wire [4:0] ex_mem_1_writereg_2, id_ex_bubble_1_s_2, id_ex_bubble_1_writereg_2, ID_R1, ID_R2,
       multiplexer_4_out, multiplexer_10_out, WR, WriteReg;
  wire [5:0] if_id_bubble_1_rd_out;
  wire [12:0] CNT_num;
  wire [15:0] \LoadUse次数 , ram_1_data, \总周期数 , \插入气泡数 , \无条件分支数 , \条件分支成功数 ;
  wire [25:0] if_id_bubble_1_rd_out_2;
  wire [27:0] shifter_1_out;
  wire [31:0] adder_2_out, EX_IR, ex_mem_1_pc_4_2, ex_mem_1_result_2, ex_mem_1_rs_2, EX_RS,
       id_ex_bubble_1_ext_2, id_ex_bubble_1_j_pc_2, id_ex_bubble_1_pc_4_2, id_ex_bubble_1_rt_2,
       id_ex_bubble_1_sign_ext_2, ID_IR, if_id_bubble_1_pc_4_out, IF_IR, MEM_IR, mem_wb_1_pc_4_2,
       mem_wb_1_rd_2, mem_wb_1_result_2, mips_alu_1_result, mips_probe_4_p1, mips_regifile_1_r1,
       mips_regifile_1_r2, multiplexer_1_out, multiplexer_2_out, multiplexer_3_out, multiplexer_8_out,
       multiplexer_9_out, multiplexer_12_out, multiplexer_13_out, PC_4, R2, RS, RT, shifter_2_out, WB_IR,
       \符号扩展_1_out_2 ;
  wire [31:16] ram_1_data_2;

  Button \u_总复位  (.out(Rst));
  Button _1 (.out(IR1));
  Button _2 (.out(IR2));
  Button _3 (.out(IR3));
  // Probe on \总周期数 
  // Probe on \总周期数 
  Button \u_继续运行  (.out(Go));
  LED #(.active("true")) led_1 (.in(W1));
  LED #(.active("true")) led_2 (.in(W2));
  LED #(.active("true")) led_3 (.in(W3));
  // Probe on IF_PC
  \气泡流水线相关处理逻辑  \u_气泡流水线相关处理逻辑_1  (
    .EX_WriteReg(id_ex_bubble_1_writereg_2), .Branch(or_3_out), .MEM_WriteReg(ex_mem_1_writereg_2),
    .Flush(\气泡流水线相关处理逻辑_1_flush ), .Stall(stall), .EX_RegWrite(id_ex_bubble_1_regwrite_2),
    .MEM_RegWrite(ex_mem_1_regwrite_2), .R1(ID_R1), .R2(ID_R2), .OP(if_id_bubble_1_rd_out),
    .func(if_id_bubble_1_rd_out_2[5:0]));
  Hex_Digit_Display hex_digit_display_1 (.value(LedData[31:28]));  // open: dp
  // Mips_Probe mips_probe_1: pin names not known; wires that end beside it: IF_IR
  Multiplexer #(.select(1), .width(32), .disabled("Z"), .enable("false")) multiplexer_1 (
    .in0(PC_4), .in1(adder_2_out), .out(multiplexer_1_out), .sel(BranchTaken));
  Multiplexer #(.select(1), .width(32), .disabled("Z"), .enable("false")) multiplexer_2 (
    .in0(multiplexer_1_out), .in1(multiplexer_3_out), .out(multiplexer_2_out), .sel(JMP));
  and and_1 (HS, not_1_out, not_2_out);
  not not_1 (not_1_out, Halt);
  not not_2 (not_2_out, stall);
  Multiplexer #(.select(1), .width(32), .disabled("Z"), .enable("false")) multiplexer_3 (
    .in0(id_ex_bubble_1_j_pc_2), .in1(EX_RS), .out(multiplexer_3_out), .sel(JR));
  Hex_Digit_Display hex_digit_display_2 (.value(LedData[27:24]));  // open: dp
  Hex_Digit_Display hex_digit_display_3 (.value(LedData[23:20]));  // open: dp
  // Probe on ID_PC
  // Mips_Probe mips_probe_2: pin names not known; wires that end beside it: ID_IR
  // Probe on multiplexer_2_out
  Register #(.width(32), .trigger("rising"), .Select("low")) PC (
    .D(multiplexer_2_out), .en(HS), .Q(IF_PC), .clk(CLK), .clr(Rst));
  Hex_Digit_Display hex_digit_display_4 (.value(LedData[15:12]));  // open: dp
  Hex_Digit_Display hex_digit_display_5 (.value(LedData[19:16]));  // open: dp
  Adder #(.width(32)) adder_1 (.a(IF_PC), .b(32'h4), .out(PC_4));  // open: cin, cout
  Hex_Digit_Display hex_digit_display_6 (.value(LedData[11:8]));  // open: dp
  Hex_Digit_Display hex_digit_display_7 (.value(LedData[7:4]));  // open: dp
  Clock #(.highDuration(1), .lowDuration(1)) clock_1 (.out(clock_1_out));
  // Probe on EX_PC
  // Mips_Probe mips_probe_3: pin names not known; wires that end beside it: clock_1_out, CLK, EX_IR
  // Mips_Probe mips_probe_4: pin names not known; wires that end beside it: mips_probe_4_p1
  ROM #(.addrWidth(10), .dataWidth(32), .Select("high")) rom_1 (.addr(IF_PC[11:2]), .data(mips_probe_4_p1));
  Hex_Digit_Display hex_digit_display_8 (.value(LedData[3:0]));  // open: dp
  or or_1 (or_1_out, Rst, or_3_out);
  IF_ID_bubble if_id_bubble_1 (
    .PC(IF_PC), .RD_in(mips_probe_4_p1), .PC_4_in(PC_4), .PC_2(ID_PC), .CLR(or_1_out),
    .RD_out({if_id_bubble_1_rd_out, if_id_bubble_1_rd_out_2}), .PC_4_out(if_id_bubble_1_pc_4_out), .en(HS),
    .CLK(CLK));  // open: INT, INT_2, PredictJump, PredictJump_2
  // Probe on RS
  // Probe on \总周期数 
  // Probe on M_PC
  // Mips_Probe mips_probe_5: pin names not known; wires that end beside it: MEM_IR
  Comparator #(.width(32), .mode("twosComplement")) comparator_1 (
    .a(RS), .b(32'ha), .eq(comparator_1_eq));  // open: gt, lt
  // Probe on \总周期数 
  // Probe on \无条件分支数 
  // Probe on \条件分支成功数 
  // Probe on \插入气泡数 
  // Probe on \LoadUse次数 
  // Probe on WB_PC
  Comparator #(.width(6), .mode("twosComplement")) comparator_2 (
    .a(6'b101001), .b(if_id_bubble_1_rd_out), .eq(sh));  // open: gt, lt
  Multiplexer #(.select(1), .width(5), .disabled("Z"), .enable("false")) multiplexer_4 (
    .in0(if_id_bubble_1_rd_out_2[20:16]), .in1(if_id_bubble_1_rd_out_2[15:11]), .out(multiplexer_4_out),
    .sel(\单周期硬布线控制器_1_regdst ));
  Shifter #(.width(28), .shift("ll")) shifter_1 (
    .in({2'b00, if_id_bubble_1_rd_out_2}), .\dist (5'b00010), .out(shifter_1_out));
  // Probe on RT
  not not_3 (not_3_out, comparator_1_eq);
  and and_2 (and_2_out, not_3_out, syscall);
  and and_3 (and_3_out, syscall, comparator_1_eq);
  // Probe on IF_PC[11:0]
  // Mips_Probe mips_probe_6: pin names not known; wires that end beside it: WB_IR
  \单周期硬布线控制器  \u_单周期硬布线控制器_1  (
    .Func(if_id_bubble_1_rd_out_2[5:0]), .OP(if_id_bubble_1_rd_out), .ALU_OP(\单周期硬布线控制器_1_alu_op ),
    .MemWrite(\单周期硬布线控制器_1_memwrite ), .ALU_SRC(\单周期硬布线控制器_1_alu_src ), .RegWrite(\单周期硬布线控制器_1_regwrite ),
    .SysCALL(\单周期硬布线控制器_1_syscall ), .SignedExt(SignedExt), .RegDst(\单周期硬布线控制器_1_regdst ),
    .JR(\单周期硬布线控制器_1_jr ), .JMP(\单周期硬布线控制器_1_jmp ), .Beq(\单周期硬布线控制器_1_beq ), .JAL(JAL),
    .Bne(\单周期硬布线控制器_1_bne ), .BGTZ(\单周期硬布线控制器_1_bgtz ), .V(\单周期硬布线控制器_1_v ), .MemToReg(\单周期硬布线控制器_1_memtoreg ));
  Multiplexer #(.select(1), .width(5), .disabled("Z"), .enable("false")) multiplexer_5 (
    .in0(if_id_bubble_1_rd_out_2[25:21]), .in1(5'b00010), .out(ID_R1), .sel(\单周期硬布线控制器_1_syscall ));
  Multiplexer #(.select(1), .width(5), .disabled("Z"), .enable("false")) multiplexer_6 (
    .in0(if_id_bubble_1_rd_out_2[20:16]), .in1(5'b00100), .out(ID_R2), .sel(\单周期硬布线控制器_1_syscall ));
  Multiplexer #(.select(1), .width(5), .disabled("Z"), .enable("false")) multiplexer_7 (
    .in0(multiplexer_4_out), .in1({5{1'b1}}), .out(WR), .sel(JAL));
  \符号扩展  \u_符号扩展_1  (.in_1(if_id_bubble_1_rd_out_2[15:0]), .out_2(\符号扩展_1_out_2 ));
  Register #(.width(32), .trigger("rising"), .Select("low")) register_1 (
    .D(RT), .en(and_2_out), .Q(LedData), .clk(CLK), .clr(Rst));
  Register #(.width(1), .trigger("rising"), .Select("low")) register_2 (
    .D(and_3_out), .en(and_3_out), .Q(Halt), .clk(CLK), .clr(Go));
  // Probe on ID_PC[11:0]
  // Probe on EX_PC[11:0]
  Multiplexer #(.select(1), .width(32), .disabled("Z"), .enable("false")) multiplexer_8 (
    .in0({{16{1'b0}}, if_id_bubble_1_rd_out_2[15:0]}), .in1(\符号扩展_1_out_2 ), .out(multiplexer_8_out),
    .sel(SignedExt));
  // Probe on M_PC[11:0]
  D_Flip_Flop #(.trigger("high"), .Pre_Clr_Positions("LEGACY"), .NegatePresetClear("false"), .enable("true"), .NewFFLayout("false")) d_ff_1 (.Q(d_ff_1_q));  // open: clk, D, Qn, preset, en, reset
  // Probe on 13'h17
  not not_4 (not_4_out, Halt);
  MIPS_Regifile mips_regifile_1 (
    .Din(RDin), .Clk(CLK), .R1(mips_regifile_1_r1), .R2(mips_regifile_1_r2), .WE(RegWrite), .W_num(WriteReg),
    .R1_num(ID_R1), .R2_num(ID_R2));
  and and_4 (and_4_out, CLK, not_5_out);
  not not_5 (not_5_out, Halt);
  // Probe on IF_PC
  // Probe on WB_PC[11:0]
  Comparator #(.width(13), .mode("twosComplement")) comparator_3 (
    .a(CNT_num), .b(13'h17), .eq(comparator_3_eq), .lt(comparator_3_lt));  // open: gt
  Clock #(.highDuration(1), .lowDuration(1)) clock_2 (.out(clock_2_out));
  or or_2 (or_2_out, Rst, \气泡流水线相关处理逻辑_1_flush );
  ID_EX_bubble id_ex_bubble_1 (
    .Beq(\单周期硬布线控制器_1_beq ), .Bgtz(\单周期硬布线控制器_1_bgtz ), .Bne(\单周期硬布线控制器_1_bne ),
    .MemToReg(\单周期硬布线控制器_1_memtoreg ), .MemWrite(\单周期硬布线控制器_1_memwrite ), .AluOP(\单周期硬布线控制器_1_alu_op ),
    .AluSrcB(\单周期硬布线控制器_1_alu_src ), .RegWrite(\单周期硬布线控制器_1_regwrite ), .JAL(JAL), .V(\单周期硬布线控制器_1_v ),
    .RS(mips_regifile_1_r1), .RT(mips_regifile_1_r2), .WriteReg(WR), .ext(multiplexer_8_out), .sh(sh),
    .Sign_ext(\符号扩展_1_out_2 ), .syscall(\单周期硬布线控制器_1_syscall ), .S(if_id_bubble_1_rd_out_2[10:6]),
    .PC(ID_PC), .PC_4(if_id_bubble_1_pc_4_out), .Beq_2(id_ex_bubble_1_beq_2), .Bgtz_2(id_ex_bubble_1_bgtz_2),
    .Bne_2(id_ex_bubble_1_bne_2), .CLR(or_2_out), .MemToReg_2(id_ex_bubble_1_memtoreg_2),
    .MemWrite_2(id_ex_bubble_1_memwrite_2), .AluOP_2(id_ex_bubble_1_aluop_2),
    .AluSrcB_2(id_ex_bubble_1_alusrcb_2), .RegWrite_2(id_ex_bubble_1_regwrite_2),
    .JAL_2(id_ex_bubble_1_jal_2), .V_2(id_ex_bubble_1_v_2), .RS_2(EX_RS), .RT_2(id_ex_bubble_1_rt_2),
    .WriteReg_2(id_ex_bubble_1_writereg_2), .ext_2(id_ex_bubble_1_ext_2), .sh_2(id_ex_bubble_1_sh_2),
    .Sign_ext_2(id_ex_bubble_1_sign_ext_2), .syscall_2(id_ex_bubble_1_syscall_2), .S_2(id_ex_bubble_1_s_2),
    .PC_2(EX_PC), .PC_4_2(id_ex_bubble_1_pc_4_2), .CLK(CLK), .JMP(\单周期硬布线控制器_1_jmp ), .JMP_2(JMP),
    .JR(\单周期硬布线控制器_1_jr ), .JR_2(JR), .J_PC({if_id_bubble_1_pc_4_out[31:28], shifter_1_out}),
    .J_PC_2(id_ex_bubble_1_j_pc_2), .en(not_4_out));  // open: RsForward, RsForward_2, RtForward, RtForward_2, PredictJump_2, PredictJump
  Counter #(.width(16), .max('hffff), .ongoal("wrap"), .trigger("rising"), .behavior("new")) counter_1 (
    .Q(\总周期数 ), .clk(and_4_out), .clr(Rst));  // open: load, D, count, carry, preset, down
  nand nand_1 (nand_1_out, d_ff_1_q, comparator_3_eq);
  Counter #(.width(13), .max('h1fff), .ongoal("stay"), .trigger("rising"), .behavior("old")) counter_2 (
    .count(comparator_3_lt), .Q(CNT_num), .clk(clock_2_out), .clr(Rst));  // open: load, D, carry, preset
  Comparator #(.width(32), .mode("twosComplement")) comparator_4 (
    .a(EX_RS), .b({32{1'b0}}), .gt(comparator_4_gt));  // open: eq, lt
  Multiplexer #(.select(1), .width(32), .disabled("Z"), .enable("false")) multiplexer_9 (
    .in0(id_ex_bubble_1_rt_2), .in1(id_ex_bubble_1_ext_2), .out(multiplexer_9_out),
    .sel(id_ex_bubble_1_alusrcb_2));
  Shifter #(.width(32), .shift("ll")) shifter_2 (
    .in(id_ex_bubble_1_sign_ext_2), .\dist (5'b00010), .out(shifter_2_out));
  assign CLK = nand_1_out ? clock_2_out : 1'bz;  // Controlled_Buffer controlled_buffer_1
  not not_6 (not_6_out, mips_alu_1_equal);
  MIPS_ALU mips_alu_1 (
    .X(EX_RS), .Y(multiplexer_9_out), .AluOP(id_ex_bubble_1_aluop_2), .Equal(mips_alu_1_equal),
    .Result(mips_alu_1_result), .shamt(multiplexer_10_out));  // open: Result_2
  Multiplexer #(.select(1), .width(5), .disabled("Z"), .enable("false")) multiplexer_10 (
    .in0(id_ex_bubble_1_s_2), .in1(EX_RS[4:0]), .out(multiplexer_10_out), .sel(id_ex_bubble_1_v_2));
  Adder #(.width(32)) adder_2 (.a(shifter_2_out), .b(id_ex_bubble_1_pc_4_2), .out(adder_2_out));  // open: cin, cout
  Counter #(.width(16), .max('hffff), .ongoal("wrap"), .trigger("rising"), .behavior("old")) counter_3 (
    .count(JMP), .Q(\无条件分支数 ), .clk(and_4_out), .clr(Rst));  // open: load, D, carry, preset
  Pull_Resistor #(.pull(1)) pull_resistor_1 (.node(CLK));
  or or_3 (or_3_out, JMP, BranchTaken);
  and and_5 (and_5_out, id_ex_bubble_1_beq_2, mips_alu_1_equal);
  or or_4 (BranchTaken, and_5_out, and_6_out, and_7_out);
  and and_6 (and_6_out, id_ex_bubble_1_bne_2, not_6_out);
  and and_7 (and_7_out, id_ex_bubble_1_bgtz_2, comparator_4_gt);
  not not_7 (not_7_out, Halt);
  EX_MEM ex_mem_1 (
    .MemToReg(id_ex_bubble_1_memtoreg_2), .MemWrite(id_ex_bubble_1_memwrite_2),
    .RegWrite(id_ex_bubble_1_regwrite_2), .JAL(id_ex_bubble_1_jal_2), .Result(mips_alu_1_result),
    .WriteReg(id_ex_bubble_1_writereg_2), .PC_4(id_ex_bubble_1_pc_4_2), .MemToReg_2(ex_mem_1_memtoreg_2),
    .MemWrite_2(MemWrite), .RegWrite_2(ex_mem_1_regwrite_2), .JAL_2(ex_mem_1_jal_2),
    .Result_2(ex_mem_1_result_2), .WriteReg_2(ex_mem_1_writereg_2), .PC_4_2(ex_mem_1_pc_4_2), .CLK(CLK),
    .RT(id_ex_bubble_1_rt_2), .RT_2(R2), .PC(EX_PC), .PC_2(M_PC), .syscall(id_ex_bubble_1_syscall_2),
    .syscall_2(ex_mem_1_syscall_2), .RS(EX_RS), .RS_2(ex_mem_1_rs_2), .sh(id_ex_bubble_1_sh_2),
    .sh_2(ex_mem_1_sh_2), .en(not_7_out));  // open: CLR
  Multiplexer #(.select(1), .width(32), .disabled("Z"), .enable("false")) multiplexer_11 (
    .in0(R2), .in1(multiplexer_12_out), .out(MDin), .sel(ex_mem_1_sh_2));
  Multiplexer #(.select(1), .width(32), .disabled("Z"), .enable("false")) multiplexer_12 (
    .in0({ram_1_data_2, R2[15:0]}), .in1({R2[15:0], ram_1_data}), .out(multiplexer_12_out),
    .sel(ex_mem_1_result_2[1]));
  Counter #(.width(16), .max('hffff), .ongoal("wrap"), .trigger("rising"), .behavior("old")) counter_4 (
    .count(BranchTaken), .Q(\条件分支成功数 ), .clk(and_4_out), .clr(Rst));  // open: load, D, carry, preset
  RAM #(.addrWidth(10), .dataWidth(32), .bus("separate"), .Select("high")) ram_1 (
    .addr(ex_mem_1_result_2[11:2]), .din(MDin), .data({ram_1_data_2, ram_1_data}), .str(MemWrite), .clk(CLK),
    .ld(ex_mem_1_memtoreg_2), .clr(Rst));  // open: sel
  Counter #(.width(16), .max('hffff), .ongoal("wrap"), .trigger("rising"), .behavior("old")) counter_5 (
    .count(stall), .Q(\插入气泡数 ), .clk(and_4_out), .clr(Rst));  // open: load, D, carry, preset
  MEM_WB mem_wb_1 (
    .MemToReg(ex_mem_1_memtoreg_2), .RegWrite(ex_mem_1_regwrite_2), .JAL(ex_mem_1_jal_2),
    .RD({ram_1_data_2, ram_1_data}), .WriteReg(ex_mem_1_writereg_2), .PC_4(ex_mem_1_pc_4_2),
    .MemToReg_2(mem_wb_1_memtoreg_2), .RegWrite_2(RegWrite), .JAL_2(mem_wb_1_jal_2), .RD_2(mem_wb_1_rd_2),
    .WriteReg_2(WriteReg), .PC_4_2(mem_wb_1_pc_4_2), .CLK(CLK), .Result(ex_mem_1_result_2),
    .Result_2(mem_wb_1_result_2), .PC(M_PC), .PC_2(WB_PC), .syscall(ex_mem_1_syscall_2), .syscall_2(syscall),
    .RT(MDin), .RT_2(RT), .RS(ex_mem_1_rs_2), .RS_2(RS), .en(not_7_out));  // open: CLR
  Multiplexer #(.select(1), .width(32), .disabled("Z"), .enable("false")) multiplexer_13 (
    .in0(mem_wb_1_result_2), .in1(mem_wb_1_rd_2), .out(multiplexer_13_out), .sel(mem_wb_1_memtoreg_2));
  Multiplexer #(.select(1), .width(32), .disabled("Z"), .enable("false")) multiplexer_14 (
    .in0(multiplexer_13_out), .in1(mem_wb_1_pc_4_2), .out(RDin), .sel(mem_wb_1_jal_2));

  // Other names for the same wires on the sheet: MEM_PC[31:0] = M_PC

  // Notes on the sheet:
  //   中断源
  //   时空图监测，可删除
  //   中断等待指示
  //   BranchTaken
  //   取指令（IF）
  //   数码管输出
  //   指令存储器
  //   PC+4
  //   contents of rom_1 (hex, n*v repeats v):
  //   20110001 8100005 20110001 20120002 20130003 8100009 20110001 20120002 20130003 810000d 20110001
  //   20120002 20130003 8100011 20110001 20120002 20130003 c1000fa 20100001 20110001 118fc0 112020
  //   20020022 c 118882 12200001 8100015 112020 20020022 c 20110001 118880 112020 20020022 c 12200001
  //   810001f 20110001 118fc0 112020 20020022 c 1188c3 112020 20020022 c 118903 112020 20020022 c 118903
  //   112020 20020022 c 118903 112020 20020022 c 118903 112020 20020022 c 118903 112020 20020022 c 118903
  //   112020 20020022 c 118903 112020 20020022 c 20100001 109fc0 139fc3 8021 2012000c 24160003 26100001
  //   3210000f 20080008 20090001 139900 2709825 132020 20020022 c 1094022 1500fff9 22100001 2018000f
  //   2188024 108700 20080008 20090001 139902 2709825 132021 20020022 c 1094022 1500fff9 108702 2c9b022
  //   12c00001 8100050 4020 1084027 84400 3508ffff 82021 20020022 c 2010ffff 20110000 ae300000 22100001
  //   22310004 ae300000 22100001 22310004 ae300000 22100001 22310004 ae300000 22100001 22310004 ae300000
  //   22100001 22310004 ae300000 22100001 22310004 ae300000 22100001 22310004 ae300000 22100001 22310004
  //   ae300000 22100001 22310004 ae300000 22100001 22310004 ae300000 22100001 22310004 ae300000 22100001
  //   22310004 ae300000 22100001 22310004 ae300000 22100001 22310004 ae300000 22100001 22310004 ae300000
  //   22100001 22310004 22100001 8020 2011003c 8e130000 8e340000 274402a 11000002 ae330000 ae140000
  //   2231fffc 1611fff8 102020 20020022 c 22100004 2011003c 1611fff2 2002000a c 20080001 20090003 20110876
  //   112020 20020022 c 200b0008 1118804 1318804 112020 20020022 c 216bffff 1560fff9 2002000a c 20080001
  //   20090003 20110876 118d00 112020 20020022 c 200b0008 1118807 1318807 112020 20020022 c 216bffff
  //   1560fff9 2002000a c 20090000 200b0020 20110001 20120001 a5310000 112020 20020022 c 2328820 21290002
  //   216bffff 1560fff8 200b0010 20090000 8d310000 112020 20020022 c 21290004 216bffff 1560fff9 2002000a c
  //   2011000f 112020 20020022 c 2231ffff 1e20fffb 2002000a c 2002000a c 20100000 22100001 102020 20020022
  //   c 22100002 102020 20020022 c 22100003 102020 20020022 c 22100004 102020 20020022 c 22100005 102020
  //   20020022 c 22100006 102020 20020022 c 22100007 102020 20020022 c 22100008 102020 20020022 20020022 c
  //   3e00008
  //   指令字
  //   OP
  //   Func
  //   rs
  //   rt
  //   rd
  //   s
  //   JMP
  //   JR
  //   OP
  //   Func
  //   RegDst
  //   译码（ID）
  //   Beq
  //   Bgtz
  //   Bne
  //   MemToReg
  //   MemWrite
  //   AluOP
  //   AluSrcB
  //   RegWrite
  //   JAL
  //   V
  //   Syscall
  //   Sign_ext
  //   控制位
  //   流水调试日志用
  //   暂停节拍，不能为0
  //   戳工具置1进入计数暂停模式，ctrl+k时钟自动运行到对应节拍暂停
  //   ctrl+k关闭时钟连续运行，将控制位置零，进入单步调试模式调试
  //   可计数暂停的时钟源
  //   执行（EX）
  //   为方便自动评测，需要输出流水线各段保存的PC值，注意是PC不是PC+4，另外ID段寄存器写入信息，Mem段内存写入信息也要输出
  //   访存（MEM）
  //   写回（WB）
endmodule
module \重定向流水线  (
  output RegWrite,
  output MemWrite,
  output [31:0] IF_PC,
  output [31:0] ID_PC,
  output [31:0] EX_PC,
  output [31:0] M_PC,
  output [31:0] WB_PC,
  output [31:0] RDin,
  output [31:0] MDin,
  output [31:0] LedData
);

  wire and_2_out, and_3_out, and_4_out, and_5_out, and_6_out, and_7_out, BranchTaken, CLK, clock_1_out,
       clock_2_out, comparator_1_eq, comparator_3_eq, comparator_3_lt, comparator_4_gt, d_ff_1_q,
       ex_mem_1_jal_2, ex_mem_1_memtoreg_2, ex_mem_1_regwrite_2, ex_mem_1_sh_2, ex_mem_1_syscall_2, Go, Halt,
       HS, id_ex_bubble_1_alusrcb_2, id_ex_bubble_1_beq_2, id_ex_bubble_1_bgtz_2, id_ex_bubble_1_bne_2,
       id_ex_bubble_1_jal_2, id_ex_bubble_1_memtoreg_2, id_ex_bubble_1_memwrite_2, id_ex_bubble_1_regwrite_2,
       id_ex_bubble_1_sh_2, id_ex_bubble_1_syscall_2, id_ex_bubble_1_v_2, IR1, IR2, IR3, JAL, JMP, JR,
       mem_wb_1_jal_2, mem_wb_1_memtoreg_2, mips_alu_1_equal, nand_1_out, not_1_out, not_2_out, not_3_out,
       not_4_out, not_5_out, not_6_out, not_7_out, or_1_out, or_2_out, or_3_out, Rst, sh, SignedExt, stall,
       syscall, W1, W2, W3, \单周期硬布线控制器_1_alu_src , \单周期硬布线控制器_1_beq , \单周期硬布线控制器_1_bgtz , \单周期硬布线控制器_1_bne ,
       \单周期硬布线控制器_1_jmp , \单周期硬布线控制器_1_jr , \单周期硬布线控制器_1_memtoreg , \单周期硬布线控制器_1_memwrite ,
       \单周期硬布线控制器_1_regdst , \单周期硬布线控制器_1_regwrite , \单周期硬布线控制器_1_syscall , \单周期硬布线控制器_1_v ,
       \重定向流水线相关处理逻辑_1_flush ;
  wire [1:0] FwdA, FwdB, \重定向流水线相关处理逻辑_1_rsfoward , \重定向流水线相关处理逻辑_1_rtfoward ;
  wire [3:0] id_ex_bubble_1_aluop_2, \单周期硬布线控制器_1_alu_op ;
  wire [4:0] ex_mem_1_writereg_2, id_ex_bubble_1_s_2, id_ex_bubble_1_writereg_2, ID_R1, ID_R2,
       multiplexer_4_out, multiplexer_10_out, WR, WriteReg;
  wire [5:0] if_id_bubble_1_rd_out;
  wire [12:0] CNT_num;
  wire [15:0] \LoadUse次数 , ram_1_data, \总周期数 , \插入气泡数 , \无条件分支数 , \条件分支成功数 ;
  wire [25:0] if_id_bubble_1_rd_out_2;
  wire [27:0] shifter_1_out;
  wire [31:0] adder_2_out, AluResult, EX_IR, ex_mem_1_pc_4_2, ex_mem_1_rs_2, EX_RS, EX_RT, EX_X, EX_Y,
       id_ex_bubble_1_ext_2, id_ex_bubble_1_j_pc_2, id_ex_bubble_1_pc_4_2, id_ex_bubble_1_sign_ext_2, ID_IR,
       if_id_bubble_1_pc_4_out, IF_IR, MEM_IR, mem_wb_1_pc_4_2, mem_wb_1_rd_2, mem_wb_1_result_2,
       mips_alu_1_result, mips_probe_4_p1, mips_regifile_1_r1, mips_regifile_1_r2, multiplexer_1_out,
       multiplexer_2_out, multiplexer_3_out, multiplexer_8_out, multiplexer_9_out, multiplexer_13_out,
       multiplexer_15_out, PC_4, R2, RS, RT, shifter_2_out, WB_IR, \符号扩展_1_out_2 ;
  wire [31:16] ram_1_data_2;

  Button \u_总复位  (.out(Rst));
  Button _1 (.out(IR1));
  Button _2 (.out(IR2));
  Button _3 (.out(IR3));
  // Probe on \总周期数 
  // Probe on \总周期数 
  Button \u_继续运行  (.out(Go));
  LED #(.active("true")) led_1 (.in(W1));
  LED #(.active("true")) led_2 (.in(W2));
  LED #(.active("true")) led_3 (.in(W3));
  // Probe on IF_PC
  \重定向流水线相关处理逻辑  \u_重定向流水线相关处理逻辑_1  (
    .R1(ID_R1), .EX_WriteReg(id_ex_bubble_1_writereg_2), .OP(if_id_bubble_1_rd_out),
    .func(if_id_bubble_1_rd_out_2[5:0]), .R2(ID_R2), .MEM_WriteReg(ex_mem_1_writereg_2), .Branch(or_3_out),
    .EX_RegWrite(id_ex_bubble_1_regwrite_2), .MEM_RegWrite(ex_mem_1_regwrite_2),
    .Flush(\重定向流水线相关处理逻辑_1_flush ), .RsFoward(\重定向流水线相关处理逻辑_1_rsfoward ), .Stall(stall),
    .RtFoward(\重定向流水线相关处理逻辑_1_rtfoward ), .EX_MemRead(id_ex_bubble_1_memtoreg_2));
  Hex_Digit_Display hex_digit_display_1 (.value(LedData[31:28]));  // open: dp
  // Mips_Probe mips_probe_1: pin names not known; wires that end beside it: IF_IR
  Multiplexer #(.select(1), .width(32), .disabled("Z"), .enable("false")) multiplexer_1 (
    .in0(PC_4), .in1(adder_2_out), .out(multiplexer_1_out), .sel(BranchTaken));
  Multiplexer #(.select(1), .width(32), .disabled("Z"), .enable("false")) multiplexer_2 (
    .in0(multiplexer_1_out), .in1(multiplexer_3_out), .out(multiplexer_2_out), .sel(JMP));
  and and_1 (HS, not_1_out, not_2_out);
  not not_1 (not_1_out, Halt);
  not not_2 (not_2_out, stall);
  Multiplexer #(.select(1), .width(32), .disabled("Z"), .enable("false")) multiplexer_3 (
    .in0(id_ex_bubble_1_j_pc_2), .in1(EX_X), .out(multiplexer_3_out), .sel(JR));
  Hex_Digit_Display hex_digit_display_2 (.value(LedData[27:24]));  // open: dp
  Hex_Digit_Display hex_digit_display_3 (.value(LedData[23:20]));  // open: dp
  // Probe on ID_PC
  // Mips_Probe mips_probe_2: pin names not known; wires that end beside it: ID_IR
  // Probe on multiplexer_2_out
  Register #(.width(32), .trigger("rising"), .Select("low")) PC (
    .D(multiplexer_2_out), .en(HS), .Q(IF_PC), .clk(CLK), .clr(Rst));
  Hex_Digit_Display hex_digit_display_4 (.value(LedData[19:16]));  // open: dp
  Hex_Digit_Display hex_digit_display_5 (.value(LedData[15:12]));  // open: dp
  Adder #(.width(32)) adder_1 (.a(IF_PC), .b(32'h4), .out(PC_4));  // open: cin, cout
  Hex_Digit_Display hex_digit_display_6 (.value(LedData[11:8]));  // open: dp
  Hex_Digit_Display hex_digit_display_7 (.value(LedData[7:4]));  // open: dp
  Clock #(.highDuration(1), .lowDuration(1)) clock_1 (.out(clock_1_out));
  // Probe on EX_PC
  // Mips_Probe mips_probe_3: pin names not known; wires that end beside it: clock_1_out, CLK, EX_IR
  // Mips_Probe mips_probe_4: pin names not known; wires that end beside it: mips_probe_4_p1
  ROM #(.addrWidth(10), .dataWidth(32), .Select("high")) rom_1 (.addr(IF_PC[11:2]), .data(mips_probe_4_p1));
  Hex_Digit_Display hex_digit_display_8 (.value(LedData[3:0]));  // open: dp
  or or_1 (or_1_out, Rst, or_3_out);
  IF_ID_bubble if_id_bubble_1 (
    .PC(IF_PC), .RD_in(mips_probe_4_p1), .PC_4_in(PC_4), .PC_2(ID_PC), .CLR(or_1_out),
    .RD_out({if_id_bubble_1_rd_out, if_id_bubble_1_rd_out_2}), .PC_4_out(if_id_bubble_1_pc_4_out), .en(HS),
    .CLK(CLK));  // open: INT, INT_2, PredictJump, PredictJump_2
  // Probe on RS
  // Probe on \总周期数 
  // Probe on M_PC
  // Mips_Probe mips_probe_5: pin names not known; wires that end beside it: MEM_IR
  Comparator #(.width(32), .mode("twosComplement")) comparator_1 (
    .a(RS), .b(32'ha), .eq(comparator_1_eq));  // open: gt, lt
  // Probe on \总周期数 
  // Probe on \无条件分支数 
  // Probe on \条件分支成功数 
  // Probe on \插入气泡数 
  // Probe on \LoadUse次数 
  // Probe on WB_PC
  Comparator #(.width(6), .mode("twosComplement")) comparator_2 (
    .a(6'b101001), .b(if_id_bubble_1_rd_out), .eq(sh));  // open: gt, lt
  Multiplexer #(.select(1), .width(5), .disabled("Z"), .enable("false")) multiplexer_4 (
    .in0(if_id_bubble_1_rd_out_2[20:16]), .in1(if_id_bubble_1_rd_out_2[15:11]), .out(multiplexer_4_out),
    .sel(\单周期硬布线控制器_1_regdst ));
  Shifter #(.width(28), .shift("ll")) shifter_1 (
    .in({2'b00, if_id_bubble_1_rd_out_2}), .\dist (5'b00010), .out(shifter_1_out));
  // Probe on RT
  not not_3 (not_3_out, comparator_1_eq);
  and and_2 (and_2_out, not_3_out, syscall);
  and and_3 (and_3_out, syscall, comparator_1_eq);
  // Probe on IF_PC[11:0]
  // Mips_Probe mips_probe_6: pin names not known; wires that end beside it: WB_IR
  \单周期硬布线控制器  \u_单周期硬布线控制器_1  (
    .Func(if_id_bubble_1_rd_out_2[5:0]), .OP(if_id_bubble_1_rd_out), .ALU_OP(\单周期硬布线控制器_1_alu_op ),
    .MemWrite(\单周期硬布线控制器_1_memwrite ), .ALU_SRC(\单周期硬布线控制器_1_alu_src ), .RegWrite(\单周期硬布线控制器_1_regwrite ),
    .SysCALL(\单周期硬布线控制器_1_syscall ), .SignedExt(SignedExt), .RegDst(\单周期硬布线控制器_1_regdst ),
    .JR(\单周期硬布线控制器_1_jr ), .JMP(\单周期硬布线控制器_1_jmp ), .Beq(\单周期硬布线控制器_1_beq ), .JAL(JAL),
    .Bne(\单周期硬布线控制器_1_bne ), .BGTZ(\单周期硬布线控制器_1_bgtz ), .V(\单周期硬布线控制器_1_v ), .MemToReg(\单周期硬布线控制器_1_memtoreg ));
  Multiplexer #(.select(1), .width(5), .disabled("Z"), .enable("false")) multiplexer_5 (
    .in0(if_id_bubble_1_rd_out_2[25:21]), .in1(5'b00010), .out(ID_R1), .sel(\单周期硬布线控制器_1_syscall ));
  Multiplexer #(.select(1), .width(5), .disabled("Z"), .enable("false")) multiplexer_6 (
    .in0(if_id_bubble_1_rd_out_2[20:16]), .in1(5'b00100), .out(ID_R2), .sel(\单周期硬布线控制器_1_syscall ));
  Multiplexer #(.select(1), .width(5), .disabled("Z"), .enable("false")) multiplexer_7 (
    .in0(multiplexer_4_out), .in1({5{1'b1}}), .out(WR), .sel(JAL));
  \符号扩展  \u_符号扩展_1  (.in_1(if_id_bubble_1_rd_out_2[15:0]), .out_2(\符号扩展_1_out_2 ));
  Register #(.width(32), .trigger("rising"), .Select("low")) register_1 (
    .D(RT), .en(and_2_out), .Q(LedData), .clk(CLK), .clr(Rst));
  Register #(.width(1), .trigger("rising"), .Select("low")) register_2 (
    .D(and_3_out), .en(and_3_out), .Q(Halt), .clk(CLK), .clr(Go));
  // Probe on ID_PC[11:0]
  // Probe on EX_PC[11:0]
  Multiplexer #(.select(1), .width(32), .disabled("Z"), .enable("false")) multiplexer_8 (
    .in0({{16{1'b0}}, if_id_bubble_1_rd_out_2[15:0]}), .in1(\符号扩展_1_out_2 ), .out(multiplexer_8_out),
    .sel(SignedExt));
  // Probe on M_PC[11:0]
  D_Flip_Flop #(.trigger("high"), .Pre_Clr_Positions("LEGACY"), .NegatePresetClear("false"), .enable("true"), .NewFFLayout("false")) d_ff_1 (.Q(d_ff_1_q));  // open: clk, D, Qn, preset, en, reset
  // Probe on 13'h33f
  not not_4 (not_4_out, Halt);
  MIPS_Regifile mips_regifile_1 (
    .Din(RDin), .Clk(CLK), .R1(mips_regifile_1_r1), .R2(mips_regifile_1_r2), .WE(RegWrite), .W_num(WriteReg),
    .R1_num(ID_R1), .R2_num(ID_R2));
  and and_4 (and_4_out, CLK, not_5_out);
  not not_5 (not_5_out, Halt);
  // Probe on IF_PC
  // Probe on WB_PC[11:0]
  Comparator #(.width(13), .mode("twosComplement")) comparator_3 (
    .a(CNT_num), .b(13'h33f), .eq(comparator_3_eq), .lt(comparator_3_lt));  // open: gt
  Clock #(.highDuration(1), .lowDuration(1)) clock_2 (.out(clock_2_out));
  or or_2 (or_2_out, Rst, \重定向流水线相关处理逻辑_1_flush );
  ID_EX_bubble id_ex_bubble_1 (
    .Beq(\单周期硬布线控制器_1_beq ), .Bgtz(\单周期硬布线控制器_1_bgtz ), .Bne(\单周期硬布线控制器_1_bne ),
    .MemToReg(\单周期硬布线控制器_1_memtoreg ), .MemWrite(\单周期硬布线控制器_1_memwrite ), .AluOP(\单周期硬布线控制器_1_alu_op ),
    .AluSrcB(\单周期硬布线控制器_1_alu_src ), .RegWrite(\单周期硬布线控制器_1_regwrite ), .JAL(JAL), .V(\单周期硬布线控制器_1_v ),
    .RS(mips_regifile_1_r1), .RT(mips_regifile_1_r2), .WriteReg(WR), .ext(multiplexer_8_out), .sh(sh),
    .Sign_ext(\符号扩展_1_out_2 ), .syscall(\单周期硬布线控制器_1_syscall ), .S(if_id_bubble_1_rd_out_2[10:6]),
    .PC(ID_PC), .PC_4(if_id_bubble_1_pc_4_out), .Beq_2(id_ex_bubble_1_beq_2), .Bgtz_2(id_ex_bubble_1_bgtz_2),
    .Bne_2(id_ex_bubble_1_bne_2), .CLR(or_2_out), .MemToReg_2(id_ex_bubble_1_memtoreg_2),
    .MemWrite_2(id_ex_bubble_1_memwrite_2), .AluOP_2(id_ex_bubble_1_aluop_2),
    .AluSrcB_2(id_ex_bubble_1_alusrcb_2), .RegWrite_2(id_ex_bubble_1_regwrite_2),
    .JAL_2(id_ex_bubble_1_jal_2), .V_2(id_ex_bubble_1_v_2), .RS_2(EX_RS), .RT_2(EX_RT),
    .WriteReg_2(id_ex_bubble_1_writereg_2), .ext_2(id_ex_bubble_1_ext_2), .sh_2(id_ex_bubble_1_sh_2),
    .Sign_ext_2(id_ex_bubble_1_sign_ext_2), .syscall_2(id_ex_bubble_1_syscall_2), .S_2(id_ex_bubble_1_s_2),
    .PC_2(EX_PC), .PC_4_2(id_ex_bubble_1_pc_4_2), .CLK(CLK), .JMP(\单周期硬布线控制器_1_jmp ), .JMP_2(JMP),
    .JR(\单周期硬布线控制器_1_jr ), .JR_2(JR), .J_PC({if_id_bubble_1_pc_4_out[31:28], shifter_1_out}),
    .J_PC_2(id_ex_bubble_1_j_pc_2), .RsForward(\重定向流水线相关处理逻辑_1_rsfoward ), .RsForward_2(FwdA),
    .RtForward(\重定向流水线相关处理逻辑_1_rtfoward ), .RtForward_2(FwdB), .en(not_4_out));  // open: PredictJump_2, PredictJump
  Counter #(.width(16), .max('hffff), .ongoal("wrap"), .trigger("rising"), .behavior("new")) counter_1 (
    .Q(\总周期数 ), .clk(and_4_out), .clr(Rst));  // open: load, D, count, carry, preset, down
  nand nand_1 (nand_1_out, d_ff_1_q, comparator_3_eq);
  Counter #(.width(13), .max('h1fff), .ongoal("stay"), .trigger("rising"), .behavior("old")) counter_2 (
    .count(comparator_3_lt), .Q(CNT_num), .clk(clock_2_out), .clr(Rst));  // open: load, D, carry, preset
  Comparator #(.width(32), .mode("twosComplement")) comparator_4 (
    .a(EX_X), .b({32{1'b0}}), .gt(comparator_4_gt));  // open: eq, lt
  Multiplexer #(.select(1), .width(32), .disabled("Z"), .enable("false")) multiplexer_9 (
    .in0(EX_Y), .in1(id_ex_bubble_1_ext_2), .out(multiplexer_9_out), .sel(id_ex_bubble_1_alusrcb_2));
  Shifter #(.width(32), .shift("ll")) shifter_2 (
    .in(id_ex_bubble_1_sign_ext_2), .\dist (5'b00010), .out(shifter_2_out));
  assign CLK = nand_1_out ? clock_2_out : 1'bz;  // Controlled_Buffer controlled_buffer_1
  not not_6 (not_6_out, mips_alu_1_equal);
  MIPS_ALU mips_alu_1 (
    .X(EX_X), .Y(multiplexer_9_out), .AluOP(id_ex_bubble_1_aluop_2), .Equal(mips_alu_1_equal),
    .Result(mips_alu_1_result), .shamt(multiplexer_10_out));  // open: Result_2
  Multiplexer #(.select(1), .width(5), .disabled("Z"), .enable("false")) multiplexer_10 (
    .in0(id_ex_bubble_1_s_2), .in1(EX_RS[4:0]), .out(multiplexer_10_out), .sel(id_ex_bubble_1_v_2));
  Adder #(.width(32)) adder_2 (.a(shifter_2_out), .b(id_ex_bubble_1_pc_4_2), .out(adder_2_out));  // open: cin, cout
  Multiplexer #(.select(2), .width(32), .disabled("Z"), .enable("false")) multiplexer_11 (
    .in0(EX_RS), .in1(RDin), .in2(AluResult), .out(EX_X), .sel(FwdA));  // open: in3
  Counter #(.width(16), .max('hffff), .ongoal("wrap"), .trigger("rising"), .behavior("old")) counter_3 (
    .count(JMP), .Q(\无条件分支数 ), .clk(and_4_out), .clr(Rst));  // open: load, D, carry, preset
  Pull_Resistor #(.pull(1)) pull_resistor_1 (.node(CLK));
  or or_3 (or_3_out, JMP, BranchTaken);
  and and_5 (and_5_out, id_ex_bubble_1_beq_2, mips_alu_1_equal);
  or or_4 (BranchTaken, and_5_out, and_6_out, and_7_out);
  and and_6 (and_6_out, id_ex_bubble_1_bne_2, not_6_out);
  and and_7 (and_7_out, id_ex_bubble_1_bgtz_2, comparator_4_gt);
  not not_7 (not_7_out, Halt);
  EX_MEM ex_mem_1 (
    .MemToReg(id_ex_bubble_1_memtoreg_2), .MemWrite(id_ex_bubble_1_memwrite_2),
    .RegWrite(id_ex_bubble_1_regwrite_2), .JAL(id_ex_bubble_1_jal_2), .Result(mips_alu_1_result),
    .WriteReg(id_ex_bubble_1_writereg_2), .PC_4(id_ex_bubble_1_pc_4_2), .MemToReg_2(ex_mem_1_memtoreg_2),
    .MemWrite_2(MemWrite), .RegWrite_2(ex_mem_1_regwrite_2), .JAL_2(ex_mem_1_jal_2), .Result_2(AluResult),
    .WriteReg_2(ex_mem_1_writereg_2), .PC_4_2(ex_mem_1_pc_4_2), .CLK(CLK), .RT(EX_Y), .RT_2(R2), .PC(EX_PC),
    .PC_2(M_PC), .syscall(id_ex_bubble_1_syscall_2), .syscall_2(ex_mem_1_syscall_2), .RS(EX_X),
    .RS_2(ex_mem_1_rs_2), .sh(id_ex_bubble_1_sh_2), .sh_2(ex_mem_1_sh_2), .en(not_7_out));  // open: CLR
  Multiplexer #(.select(1), .width(32), .disabled("Z"), .enable("false")) multiplexer_12 (
    .in0(R2), .in1(multiplexer_13_out), .out(MDin), .sel(ex_mem_1_sh_2));
  Multiplexer #(.select(1), .width(32), .disabled("Z"), .enable("false")) multiplexer_13 (
    .in0({ram_1_data_2, R2[15:0]}), .in1({R2[15:0], ram_1_data}), .out(multiplexer_13_out), .sel(AluResult[1]));
  Multiplexer #(.select(2), .width(32), .disabled("Z"), .enable("false")) multiplexer_14 (
    .in0(EX_RT), .in1(RDin), .in2(AluResult), .out(EX_Y), .sel(FwdB));  // open: in3
  Counter #(.width(16), .max('hffff), .ongoal("wrap"), .trigger("rising"), .behavior("old")) counter_4 (
    .count(BranchTaken), .Q(\条件分支成功数 ), .clk(and_4_out), .clr(Rst));  // open: load, D, carry, preset
  RAM #(.addrWidth(10), .dataWidth(32), .bus("separate"), .Select("high")) ram_1 (
    .addr(AluResult[11:2]), .din(MDin), .data({ram_1_data_2, ram_1_data}), .str(MemWrite), .clk(CLK),
    .ld(ex_mem_1_memtoreg_2), .clr(Rst));  // open: sel
  Counter #(.width(16), .max('hffff), .ongoal("wrap"), .trigger("rising"), .behavior("old")) counter_5 (
    .count(stall), .Q(\插入气泡数 ), .clk(and_4_out), .clr(Rst));  // open: load, D, carry, preset
  MEM_WB mem_wb_1 (
    .MemToReg(ex_mem_1_memtoreg_2), .RegWrite(ex_mem_1_regwrite_2), .JAL(ex_mem_1_jal_2),
    .RD({ram_1_data_2, ram_1_data}), .WriteReg(ex_mem_1_writereg_2), .PC_4(ex_mem_1_pc_4_2),
    .MemToReg_2(mem_wb_1_memtoreg_2), .RegWrite_2(RegWrite), .JAL_2(mem_wb_1_jal_2), .RD_2(mem_wb_1_rd_2),
    .WriteReg_2(WriteReg), .PC_4_2(mem_wb_1_pc_4_2), .CLK(CLK), .Result(AluResult),
    .Result_2(mem_wb_1_result_2), .PC(M_PC), .PC_2(WB_PC), .syscall(ex_mem_1_syscall_2), .syscall_2(syscall),
    .RT(MDin), .RT_2(RT), .RS(ex_mem_1_rs_2), .RS_2(RS), .en(not_7_out));  // open: CLR
  Multiplexer #(.select(1), .width(32), .disabled("Z"), .enable("false")) multiplexer_15 (
    .in0(mem_wb_1_result_2), .in1(mem_wb_1_rd_2), .out(multiplexer_15_out), .sel(mem_wb_1_memtoreg_2));
  Multiplexer #(.select(1), .width(32), .disabled("Z"), .enable("false")) multiplexer_16 (
    .in0(multiplexer_15_out), .in1(mem_wb_1_pc_4_2), .out(RDin), .sel(mem_wb_1_jal_2));
  // Probe on MDin

  // Other names for the same wires on the sheet: MEM_PC[31:0] = M_PC

  // Notes on the sheet:
  //   中断源
  //   时空图监测，可删除
  //   中断等待指示
  //   BranchTaken
  //   取指令（IF）
  //   数码管输出
  //   指令存储器
  //   PC+4
  //   contents of rom_1 (hex, n*v repeats v):
  //   20110001 8100005 20110001 20120002 20130003 8100009 20110001 20120002 20130003 810000d 20110001
  //   20120002 20130003 8100011 20110001 20120002 20130003 c1000fa 20100001 20110001 118fc0 112020
  //   20020022 c 118882 12200001 8100015 112020 20020022 c 20110001 118880 112020 20020022 c 12200001
  //   810001f 20110001 118fc0 112020 20020022 c 1188c3 112020 20020022 c 118903 112020 20020022 c 118903
  //   112020 20020022 c 118903 112020 20020022 c 118903 112020 20020022 c 118903 112020 20020022 c 118903
  //   112020 20020022 c 118903 112020 20020022 c 20100001 109fc0 139fc3 8021 2012000c 24160003 26100001
  //   3210000f 20080008 20090001 139900 2709825 132020 20020022 c 1094022 1500fff9 22100001 2018000f
  //   2188024 108700 20080008 20090001 139902 2709825 132021 20020022 c 1094022 1500fff9 108702 2c9b022
  //   12c00001 8100050 4020 1084027 84400 3508ffff 82021 20020022 c 2010ffff 20110000 ae300000 22100001
  //   22310004 ae300000 22100001 22310004 ae300000 22100001 22310004 ae300000 22100001 22310004 ae300000
  //   22100001 22310004 ae300000 22100001 22310004 ae300000 22100001 22310004 ae300000 22100001 22310004
  //   ae300000 22100001 22310004 ae300000 22100001 22310004 ae300000 22100001 22310004 ae300000 22100001
  //   22310004 ae300000 22100001 22310004 ae300000 22100001 22310004 ae300000 22100001 22310004 ae300000
  //   22100001 22310004 22100001 8020 2011003c 8e130000 8e340000 274402a 11000002 ae330000 ae140000
  //   2231fffc 1611fff8 102020 20020022 c 22100004 2011003c 1611fff2 2002000a c 20080001 20090003 20110876
  //   112020 20020022 c 200b0008 1118804 1318804 112020 20020022 c 216bffff 1560fff9 2002000a c 20080001
  //   20090003 20110876 118d00 112020 20020022 c 200b0008 1118807 1318807 112020 20020022 c 216bffff
  //   1560fff9 2002000a c 20090000 200b0020 20110001 20120001 a5310000 112020 20020022 c 2328820 21290002
  //   216bffff 1560fff8 200b0010 20090000 8d310000 112020 20020022 c 21290004 216bffff 1560fff9 2002000a c
  //   2011000f 112020 20020022 c 2231ffff 1e20fffb 2002000a c 2002000a c 20100000 22100001 102020 20020022
  //   c 22100002 102020 20020022 c 22100003 102020 20020022 c 22100004 102020 20020022 c 22100005 102020
  //   20020022 c 22100006 102020 20020022 c 22100007 102020 20020022 c 22100008 102020 20020022 20020022 c
  //   3e00008
  //   指令字
  //   OP
  //   Func
  //   rs
  //   rt
  //   rd
  //   s
  //   JMP
  //   JR
  //   OP
  //   Func
  //   RegDst
  //   译码（ID）
  //   Beq
  //   Bgtz
  //   Bne
  //   MemToReg
  //   MemWrite
  //   AluOP
  //   AluSrcB
  //   RegWrite
  //   JAL
  //   V
  //   Syscall
  //   Sign_ext
  //   控制位
  //   流水调试日志用
  //   暂停节拍，不能为0
  //   戳工具置1进入计数暂停模式，ctrl+k时钟自动运行到对应节拍暂停
  //   ctrl+k关闭时钟连续运行，将控制位置零，进入单步调试模式调试
  //   可计数暂停的时钟源
  //   执行（EX）
  //   为方便自动评测，需要输出流水线各段保存的PC值，注意是PC不是PC+4，另外ID段寄存器写入信息，Mem段内存写入信息也要输出
  //   访存（MEM）
  //   写回（WB）
endmodule

module \动态分支预测  (
  output RegWrite,
  output MemWrite,
  output [31:0] IF_PC,
  output [31:0] ID_PC,
  output [31:0] EX_PC,
  output [31:0] M_PC,
  output [31:0] WB_PC,
  output [31:0] RDin,
  output [31:0] MDin,
  output [31:0] LedData
);

  wire and_2_out, and_3_out, and_4_out, and_5_out, and_6_out, and_7_out, BranchTaken, CLK, clock_1_out,
       clock_2_out, comparator_1_eq, comparator_3_eq, comparator_3_lt, comparator_4_gt, d_ff_1_q, EX_Branch,
       ex_mem_1_jal_2, ex_mem_1_memtoreg_2, ex_mem_1_regwrite_2, ex_mem_1_sh_2, ex_mem_1_syscall_2, EX_PJ,
       Go, Halt, HS, id_ex_bubble_1_alusrcb_2, id_ex_bubble_1_beq_2, id_ex_bubble_1_bgtz_2,
       id_ex_bubble_1_bne_2, id_ex_bubble_1_jal_2, id_ex_bubble_1_memtoreg_2, id_ex_bubble_1_memwrite_2,
       id_ex_bubble_1_regwrite_2, id_ex_bubble_1_sh_2, id_ex_bubble_1_syscall_2, id_ex_bubble_1_v_2,
       if_id_bubble_1_predictjump_2, IR1, IR2, IR3, JAL, JMP, JorB, JR, mem_wb_1_jal_2, mem_wb_1_memtoreg_2,
       mips_alu_1_equal, nand_1_out, not_1_out, not_2_out, not_3_out, not_4_out, not_5_out, not_6_out,
       not_7_out, or_1_out, or_2_out, PredictJump, Rst, sh, SignedExt, stall, syscall, W1, W2, W3, xor_1_out,
       \单周期硬布线控制器_1_alu_src , \单周期硬布线控制器_1_beq , \单周期硬布线控制器_1_bgtz , \单周期硬布线控制器_1_bne , \单周期硬布线控制器_1_jmp ,
       \单周期硬布线控制器_1_jr , \单周期硬布线控制器_1_memtoreg , \单周期硬布线控制器_1_memwrite , \单周期硬布线控制器_1_regdst ,
       \单周期硬布线控制器_1_regwrite , \单周期硬布线控制器_1_syscall , \单周期硬布线控制器_1_v , \重定向流水线相关处理逻辑_1_flush ;
  wire [1:0] FwdA, FwdB, \重定向流水线相关处理逻辑_1_rsfoward , \重定向流水线相关处理逻辑_1_rtfoward ;
  wire [3:0] id_ex_bubble_1_aluop_2, \单周期硬布线控制器_1_alu_op ;
  wire [4:0] ex_mem_1_writereg_2, id_ex_bubble_1_s_2, id_ex_bubble_1_writereg_2, ID_R1, ID_R2,
       multiplexer_6_out, multiplexer_12_out, WR, WriteReg;
  wire [12:0] CNT_num;
  wire [15:0] \LoadUse次数 , ram_1_data, \总周期数 , \插入气泡数 , \无条件分支数 , \条件分支成功数 ;
  wire [27:0] shifter_1_out;
  wire [31:0] AluResult, BranchAddr, btb_1_jumpaddr, EX_IR, ex_mem_1_pc_4_2, ex_mem_1_rs_2, EX_PC_4, EX_RS,
       EX_RT, EX_X, EX_Y, id_ex_bubble_1_ext_2, id_ex_bubble_1_j_pc_2, id_ex_bubble_1_sign_ext_2, ID_IR,
       if_id_bubble_1_pc_4_out, if_id_bubble_1_rd_out, IF_IR, MEM_IR, mem_wb_1_pc_4_2, mem_wb_1_rd_2,
       mem_wb_1_result_2, mips_alu_1_result, mips_probe_3_p1, mips_regifile_1_r1, mips_regifile_1_r2,
       multiplexer_1_out, multiplexer_2_out, multiplexer_3_out, multiplexer_4_out, multiplexer_5_out,
       multiplexer_10_out, multiplexer_11_out, multiplexer_15_out, multiplexer_17_out, PC_4, R2, RS, RT,
       shifter_2_out, WB_IR, \符号扩展_1_out_2 ;
  wire [31:16] ram_1_data_2;

  Multiplexer #(.select(1), .width(32), .disabled("Z"), .enable("false")) multiplexer_1 (
    .in0(multiplexer_2_out), .in1(multiplexer_3_out), .out(multiplexer_1_out), .sel(xor_1_out));
  and and_1 (HS, not_1_out, not_2_out);
  not not_1 (not_1_out, Halt);
  Button \u_总复位  (.out(Rst));
  Button _1 (.out(IR1));
  Button _2 (.out(IR2));
  Button _3 (.out(IR3));
  // Probe on \总周期数 
  // Probe on \总周期数 
  // Probe on multiplexer_1_out
  Register #(.width(32), .trigger("rising"), .Select("low")) PC (
    .D(multiplexer_1_out), .en(HS), .Q(IF_PC), .clk(CLK), .clr(Rst));
  not not_2 (not_2_out, stall);
  Multiplexer #(.select(1), .width(32), .disabled("Z"), .enable("false")) multiplexer_2 (
    .in0(PC_4), .in1(btb_1_jumpaddr), .out(multiplexer_2_out), .sel(PredictJump));
  Multiplexer #(.select(1), .width(32), .disabled("Z"), .enable("false")) multiplexer_3 (
    .in0(EX_PC_4), .in1(multiplexer_4_out), .out(multiplexer_3_out), .sel(JorB));
  Button \u_继续运行  (.out(Go));
  LED #(.active("true")) led_1 (.in(W1));
  LED #(.active("true")) led_2 (.in(W2));
  LED #(.active("true")) led_3 (.in(W3));
  // Probe on IF_PC
  \重定向流水线相关处理逻辑  \u_重定向流水线相关处理逻辑_1  (
    .R1(ID_R1), .EX_WriteReg(id_ex_bubble_1_writereg_2), .OP(if_id_bubble_1_rd_out[31:26]),
    .func(if_id_bubble_1_rd_out[5:0]), .R2(ID_R2), .MEM_WriteReg(ex_mem_1_writereg_2), .Branch(xor_1_out),
    .EX_RegWrite(id_ex_bubble_1_regwrite_2), .MEM_RegWrite(ex_mem_1_regwrite_2),
    .Flush(\重定向流水线相关处理逻辑_1_flush ), .RsFoward(\重定向流水线相关处理逻辑_1_rsfoward ), .Stall(stall),
    .RtFoward(\重定向流水线相关处理逻辑_1_rtfoward ), .EX_MemRead(id_ex_bubble_1_memtoreg_2));
  BTB btb_1 (
    .CLK(CLK), .Rst(Rst), .PC(IF_PC), .EX_PC(EX_PC), .EX_BranchAddr(multiplexer_4_out),
    .EX_Branch(EX_Branch), .EX_BranchTaken(JorB), .PredictJump(PredictJump), .JumpAddr(btb_1_jumpaddr));
  Hex_Digit_Display hex_digit_display_1 (.value(LedData[31:28]));  // open: dp
  // Mips_Probe mips_probe_1: pin names not known; wires that end beside it: IF_IR
  Hex_Digit_Display hex_digit_display_2 (.value(LedData[23:20]));  // open: dp
  Hex_Digit_Display hex_digit_display_3 (.value(LedData[27:24]));  // open: dp
  // Probe on ID_PC
  // Mips_Probe mips_probe_2: pin names not known; wires that end beside it: ID_IR
  Hex_Digit_Display hex_digit_display_4 (.value(LedData[15:12]));  // open: dp
  Hex_Digit_Display hex_digit_display_5 (.value(LedData[19:16]));  // open: dp
  // Mips_Probe mips_probe_3: pin names not known; wires that end beside it: mips_probe_3_p1
  Hex_Digit_Display hex_digit_display_6 (.value(LedData[7:4]));  // open: dp
  Hex_Digit_Display hex_digit_display_7 (.value(LedData[11:8]));  // open: dp
  Clock #(.highDuration(1), .lowDuration(1)) clock_1 (.out(clock_1_out));
  // Probe on EX_PC
  // Mips_Probe mips_probe_4: pin names not known; wires that end beside it: clock_1_out, CLK, EX_IR
  ROM #(.addrWidth(10), .dataWidth(32), .Select("high")) rom_1 (.addr(IF_PC[11:2]), .data(mips_probe_3_p1));
  Adder #(.width(32)) adder_1 (.a(IF_PC), .b(32'h4), .out(PC_4));  // open: cin, cout
  Hex_Digit_Display hex_digit_display_8 (.value(LedData[3:0]));  // open: dp
  or or_1 (or_1_out, Rst, xor_1_out);
  IF_ID_bubble if_id_bubble_1 (
    .PC(IF_PC), .RD_in(mips_probe_3_p1), .PC_4_in(PC_4), .PC_2(ID_PC), .CLR(or_1_out),
    .RD_out(if_id_bubble_1_rd_out), .PC_4_out(if_id_bubble_1_pc_4_out), .en(HS), .CLK(CLK),
    .PredictJump(PredictJump), .PredictJump_2(if_id_bubble_1_predictjump_2));  // open: INT, INT_2
  Multiplexer #(.select(1), .width(32), .disabled("Z"), .enable("false")) multiplexer_4 (
    .in0(BranchAddr), .in1(multiplexer_5_out), .out(multiplexer_4_out), .sel(JMP));
  // Probe on RS
  // Probe on \总周期数 
  // Probe on M_PC
  // Mips_Probe mips_probe_5: pin names not known; wires that end beside it: MEM_IR
  Multiplexer #(.select(1), .width(32), .disabled("Z"), .enable("false")) multiplexer_5 (
    .in0(id_ex_bubble_1_j_pc_2), .in1(EX_X), .out(multiplexer_5_out), .sel(JR));
  Comparator #(.width(32), .mode("twosComplement")) comparator_1 (
    .a(RS), .b(32'ha), .eq(comparator_1_eq));  // open: gt, lt
  // Probe on \总周期数 
  // Probe on \无条件分支数 
  // Probe on \条件分支成功数 
  // Probe on \插入气泡数 
  // Probe on \LoadUse次数 
  // Probe on WB_PC
  Comparator #(.width(6), .mode("twosComplement")) comparator_2 (
    .a(6'b101001), .b(if_id_bubble_1_rd_out[31:26]), .eq(sh));  // open: gt, lt
  Multiplexer #(.select(1), .width(5), .disabled("Z"), .enable("false")) multiplexer_6 (
    .in0(if_id_bubble_1_rd_out[20:16]), .in1(if_id_bubble_1_rd_out[15:11]), .out(multiplexer_6_out),
    .sel(\单周期硬布线控制器_1_regdst ));
  Shifter #(.width(28), .shift("ll")) shifter_1 (
    .in({2'b00, if_id_bubble_1_rd_out[25:0]}), .\dist (5'b00010), .out(shifter_1_out));
  // Probe on RT
  not not_3 (not_3_out, comparator_1_eq);
  and and_2 (and_2_out, not_3_out, syscall);
  and and_3 (and_3_out, syscall, comparator_1_eq);
  // Probe on IF_PC[11:0]
  // Mips_Probe mips_probe_6: pin names not known; wires that end beside it: WB_IR
  \单周期硬布线控制器  \u_单周期硬布线控制器_1  (
    .Func(if_id_bubble_1_rd_out[5:0]), .OP(if_id_bubble_1_rd_out[31:26]), .ALU_OP(\单周期硬布线控制器_1_alu_op ),
    .MemWrite(\单周期硬布线控制器_1_memwrite ), .ALU_SRC(\单周期硬布线控制器_1_alu_src ), .RegWrite(\单周期硬布线控制器_1_regwrite ),
    .SysCALL(\单周期硬布线控制器_1_syscall ), .SignedExt(SignedExt), .RegDst(\单周期硬布线控制器_1_regdst ),
    .JR(\单周期硬布线控制器_1_jr ), .JMP(\单周期硬布线控制器_1_jmp ), .Beq(\单周期硬布线控制器_1_beq ), .JAL(JAL),
    .Bne(\单周期硬布线控制器_1_bne ), .BGTZ(\单周期硬布线控制器_1_bgtz ), .V(\单周期硬布线控制器_1_v ), .MemToReg(\单周期硬布线控制器_1_memtoreg ));
  Multiplexer #(.select(1), .width(5), .disabled("Z"), .enable("false")) multiplexer_7 (
    .in0(if_id_bubble_1_rd_out[25:21]), .in1(5'b00010), .out(ID_R1), .sel(\单周期硬布线控制器_1_syscall ));
  Multiplexer #(.select(1), .width(5), .disabled("Z"), .enable("false")) multiplexer_8 (
    .in0(if_id_bubble_1_rd_out[20:16]), .in1(5'b00100), .out(ID_R2), .sel(\单周期硬布线控制器_1_syscall ));
  Multiplexer #(.select(1), .width(5), .disabled("Z"), .enable("false")) multiplexer_9 (
    .in0(multiplexer_6_out), .in1({5{1'b1}}), .out(WR), .sel(JAL));
  \符号扩展  \u_符号扩展_1  (.in_1(if_id_bubble_1_rd_out[15:0]), .out_2(\符号扩展_1_out_2 ));
  Register #(.width(32), .trigger("rising"), .Select("low")) register_1 (
    .D(RT), .en(and_2_out), .Q(LedData), .clk(CLK), .clr(Rst));
  Register #(.width(1), .trigger("rising"), .Select("low")) register_2 (
    .D(and_3_out), .en(and_3_out), .Q(Halt), .clk(CLK), .clr(Go));
  // Probe on ID_PC[11:0]
  // Probe on EX_PC[11:0]
  Multiplexer #(.select(1), .width(32), .disabled("Z"), .enable("false")) multiplexer_10 (
    .in0({{16{1'b0}}, if_id_bubble_1_rd_out[15:0]}), .in1(\符号扩展_1_out_2 ), .out(multiplexer_10_out),
    .sel(SignedExt));
  // Probe on M_PC[11:0]
  D_Flip_Flop #(.trigger("high"), .Pre_Clr_Positions("LEGACY"), .NegatePresetClear("false"), .enable("true"), .NewFFLayout("false")) d_ff_1 (.Q(d_ff_1_q));  // open: clk, D, Qn, preset, en, reset
  // Probe on 13'h33f
  not not_4 (not_4_out, Halt);
  MIPS_Regifile mips_regifile_1 (
    .Din(RDin), .Clk(CLK), .R1(mips_regifile_1_r1), .R2(mips_regifile_1_r2), .WE(RegWrite), .W_num(WriteReg),
    .R1_num(ID_R1), .R2_num(ID_R2));
  and and_4 (and_4_out, CLK, not_5_out);
  not not_5 (not_5_out, Halt);
  // Probe on IF_PC
  // Probe on WB_PC[11:0]
  Comparator #(.width(13), .mode("twosComplement")) comparator_3 (
    .a(CNT_num), .b(13'h33f), .eq(comparator_3_eq), .lt(comparator_3_lt));  // open: gt
  Clock #(.highDuration(1), .lowDuration(1)) clock_2 (.out(clock_2_out));
  or or_2 (or_2_out, Rst, \重定向流水线相关处理逻辑_1_flush );
  ID_EX_bubble id_ex_bubble_1 (
    .Beq(\单周期硬布线控制器_1_beq ), .Bgtz(\单周期硬布线控制器_1_bgtz ), .Bne(\单周期硬布线控制器_1_bne ),
    .MemToReg(\单周期硬布线控制器_1_memtoreg ), .MemWrite(\单周期硬布线控制器_1_memwrite ), .AluOP(\单周期硬布线控制器_1_alu_op ),
    .AluSrcB(\单周期硬布线控制器_1_alu_src ), .RegWrite(\单周期硬布线控制器_1_regwrite ), .JAL(JAL), .V(\单周期硬布线控制器_1_v ),
    .RS(mips_regifile_1_r1), .RT(mips_regifile_1_r2), .WriteReg(WR), .ext(multiplexer_10_out), .sh(sh),
    .Sign_ext(\符号扩展_1_out_2 ), .syscall(\单周期硬布线控制器_1_syscall ), .S(if_id_bubble_1_rd_out[10:6]), .PC(ID_PC),
    .PC_4(if_id_bubble_1_pc_4_out), .Beq_2(id_ex_bubble_1_beq_2), .Bgtz_2(id_ex_bubble_1_bgtz_2),
    .Bne_2(id_ex_bubble_1_bne_2), .CLR(or_2_out), .MemToReg_2(id_ex_bubble_1_memtoreg_2),
    .MemWrite_2(id_ex_bubble_1_memwrite_2), .AluOP_2(id_ex_bubble_1_aluop_2),
    .AluSrcB_2(id_ex_bubble_1_alusrcb_2), .RegWrite_2(id_ex_bubble_1_regwrite_2),
    .JAL_2(id_ex_bubble_1_jal_2), .V_2(id_ex_bubble_1_v_2), .RS_2(EX_RS), .RT_2(EX_RT),
    .WriteReg_2(id_ex_bubble_1_writereg_2), .ext_2(id_ex_bubble_1_ext_2), .sh_2(id_ex_bubble_1_sh_2),
    .Sign_ext_2(id_ex_bubble_1_sign_ext_2), .syscall_2(id_ex_bubble_1_syscall_2), .S_2(id_ex_bubble_1_s_2),
    .PC_2(EX_PC), .PC_4_2(EX_PC_4), .CLK(CLK), .JMP(\单周期硬布线控制器_1_jmp ), .JMP_2(JMP), .JR(\单周期硬布线控制器_1_jr ),
    .JR_2(JR), .J_PC({if_id_bubble_1_pc_4_out[31:28], shifter_1_out}), .J_PC_2(id_ex_bubble_1_j_pc_2),
    .RsForward(\重定向流水线相关处理逻辑_1_rsfoward ), .RsForward_2(FwdA), .RtForward(\重定向流水线相关处理逻辑_1_rtfoward ),
    .RtForward_2(FwdB), .PredictJump_2(EX_PJ), .PredictJump(if_id_bubble_1_predictjump_2), .en(not_4_out));
  Counter #(.width(16), .max('hffff), .ongoal("wrap"), .trigger("rising"), .behavior("new")) counter_1 (
    .Q(\总周期数 ), .clk(and_4_out), .clr(Rst));  // open: load, D, count, carry, preset, down
  nand nand_1 (nand_1_out, d_ff_1_q, comparator_3_eq);
  Counter #(.width(13), .max('h1fff), .ongoal("stay"), .trigger("rising"), .behavior("old")) counter_2 (
    .count(comparator_3_lt), .Q(CNT_num), .clk(clock_2_out), .clr(Rst));  // open: load, D, carry, preset
  or or_3 (EX_Branch, JMP, id_ex_bubble_1_beq_2, id_ex_bubble_1_bgtz_2, id_ex_bubble_1_bne_2);
  Comparator #(.width(32), .mode("twosComplement")) comparator_4 (
    .a(EX_X), .b({32{1'b0}}), .gt(comparator_4_gt));  // open: eq, lt
  Multiplexer #(.select(1), .width(32), .disabled("Z"), .enable("false")) multiplexer_11 (
    .in0(EX_Y), .in1(id_ex_bubble_1_ext_2), .out(multiplexer_11_out), .sel(id_ex_bubble_1_alusrcb_2));
  Shifter #(.width(32), .shift("ll")) shifter_2 (
    .in(id_ex_bubble_1_sign_ext_2), .\dist (5'b00010), .out(shifter_2_out));
  assign CLK = nand_1_out ? clock_2_out : 1'bz;  // Controlled_Buffer controlled_buffer_1
  not not_6 (not_6_out, mips_alu_1_equal);
  MIPS_ALU mips_alu_1 (
    .X(EX_X), .Y(multiplexer_11_out), .AluOP(id_ex_bubble_1_aluop_2), .Equal(mips_alu_1_equal),
    .Result(mips_alu_1_result), .shamt(multiplexer_12_out));  // open: Result_2
  Multiplexer #(.select(1), .width(5), .disabled("Z"), .enable("false")) multiplexer_12 (
    .in0(id_ex_bubble_1_s_2), .in1(EX_RS[4:0]), .out(multiplexer_12_out), .sel(id_ex_bubble_1_v_2));
  Adder #(.width(32)) adder_2 (.a(shifter_2_out), .b(EX_PC_4), .out(BranchAddr));  // open: cin, cout
  Multiplexer #(.select(2), .width(32), .disabled("Z"), .enable("false")) multiplexer_13 (
    .in0(EX_RS), .in1(RDin), .in2(AluResult), .out(EX_X), .sel(FwdA));  // open: in3
  Counter #(.width(16), .max('hffff), .ongoal("wrap"), .trigger("rising"), .behavior("old")) counter_3 (
    .count(JMP), .Q(\无条件分支数 ), .clk(and_4_out), .clr(Rst));  // open: load, D, carry, preset
  Pull_Resistor #(.pull(1)) pull_resistor_1 (.node(CLK));
  xor xor_1 (xor_1_out, EX_PJ, JorB);
  or or_4 (JorB, JMP, BranchTaken);
  and and_5 (and_5_out, id_ex_bubble_1_beq_2, mips_alu_1_equal);
  or or_5 (BranchTaken, and_5_out, and_6_out, and_7_out);
  and and_6 (and_6_out, id_ex_bubble_1_bne_2, not_6_out);
  and and_7 (and_7_out, id_ex_bubble_1_bgtz_2, comparator_4_gt);
  EX_MEM ex_mem_1 (
    .MemToReg(id_ex_bubble_1_memtoreg_2), .MemWrite(id_ex_bubble_1_memwrite_2),
    .RegWrite(id_ex_bubble_1_regwrite_2), .JAL(id_ex_bubble_1_jal_2), .Result(mips_alu_1_result),
    .WriteReg(id_ex_bubble_1_writereg_2), .PC_4(EX_PC_4), .MemToReg_2(ex_mem_1_memtoreg_2),
    .MemWrite_2(MemWrite), .RegWrite_2(ex_mem_1_regwrite_2), .JAL_2(ex_mem_1_jal_2), .Result_2(AluResult),
    .WriteReg_2(ex_mem_1_writereg_2), .PC_4_2(ex_mem_1_pc_4_2), .CLK(CLK), .RT(EX_Y), .RT_2(R2), .PC(EX_PC),
    .PC_2(M_PC), .syscall(id_ex_bubble_1_syscall_2), .syscall_2(ex_mem_1_syscall_2), .RS(EX_X),
    .RS_2(ex_mem_1_rs_2), .sh(id_ex_bubble_1_sh_2), .sh_2(ex_mem_1_sh_2), .en(not_7_out));  // open: CLR
  not not_7 (not_7_out, Halt);
  Multiplexer #(.select(1), .width(32), .disabled("Z"), .enable("false")) multiplexer_14 (
    .in0(R2), .in1(multiplexer_15_out), .out(MDin), .sel(ex_mem_1_sh_2));
  Multiplexer #(.select(1), .width(32), .disabled("Z"), .enable("false")) multiplexer_15 (
    .in0({ram_1_data_2, R2[15:0]}), .in1({R2[15:0], ram_1_data}), .out(multiplexer_15_out), .sel(AluResult[1]));
  Multiplexer #(.select(2), .width(32), .disabled("Z"), .enable("false")) multiplexer_16 (
    .in0(EX_RT), .in1(RDin), .in2(AluResult), .out(EX_Y), .sel(FwdB));  // open: in3
  Counter #(.width(16), .max('hffff), .ongoal("wrap"), .trigger("rising"), .behavior("old")) counter_4 (
    .count(BranchTaken), .Q(\条件分支成功数 ), .clk(and_4_out), .clr(Rst));  // open: load, D, carry, preset
  RAM #(.addrWidth(10), .dataWidth(32), .bus("separate"), .Select("high")) ram_1 (
    .addr(AluResult[11:2]), .din(MDin), .data({ram_1_data_2, ram_1_data}), .str(MemWrite), .clk(CLK),
    .ld(ex_mem_1_memtoreg_2), .clr(Rst));  // open: sel
  Counter #(.width(16), .max('hffff), .ongoal("wrap"), .trigger("rising"), .behavior("old")) counter_5 (
    .count(stall), .Q(\插入气泡数 ), .clk(and_4_out), .clr(Rst));  // open: load, D, carry, preset
  MEM_WB mem_wb_1 (
    .MemToReg(ex_mem_1_memtoreg_2), .RegWrite(ex_mem_1_regwrite_2), .JAL(ex_mem_1_jal_2),
    .RD({ram_1_data_2, ram_1_data}), .WriteReg(ex_mem_1_writereg_2), .PC_4(ex_mem_1_pc_4_2),
    .MemToReg_2(mem_wb_1_memtoreg_2), .RegWrite_2(RegWrite), .JAL_2(mem_wb_1_jal_2), .RD_2(mem_wb_1_rd_2),
    .WriteReg_2(WriteReg), .PC_4_2(mem_wb_1_pc_4_2), .CLK(CLK), .Result(AluResult),
    .Result_2(mem_wb_1_result_2), .PC(M_PC), .PC_2(WB_PC), .syscall(ex_mem_1_syscall_2), .syscall_2(syscall),
    .RT(MDin), .RT_2(RT), .RS(ex_mem_1_rs_2), .RS_2(RS), .en(not_7_out));  // open: CLR
  Multiplexer #(.select(1), .width(32), .disabled("Z"), .enable("false")) multiplexer_17 (
    .in0(mem_wb_1_result_2), .in1(mem_wb_1_rd_2), .out(multiplexer_17_out), .sel(mem_wb_1_memtoreg_2));
  Multiplexer #(.select(1), .width(32), .disabled("Z"), .enable("false")) multiplexer_18 (
    .in0(multiplexer_17_out), .in1(mem_wb_1_pc_4_2), .out(RDin), .sel(mem_wb_1_jal_2));
  // Probe on MDin

  // Other names for the same wires on the sheet: MEM_PC[31:0] = M_PC

  // Notes on the sheet:
  //   BranchTaken
  //   预测失败
  //   修订地址
  //   中断源
  //   时空图监测，可删除
  //   中断等待指示
  //   取指令（IF）
  //   数码管输出
  //   指令存储器
  //   contents of rom_1 (hex, n*v repeats v):
  //   20110001 8100005 20110001 20120002 20130003 8100009 20110001 20120002 20130003 810000d 20110001
  //   20120002 20130003 8100011 20110001 20120002 20130003 c1000fa 20100001 20110001 118fc0 112020
  //   20020022 c 118882 12200001 8100015 112020 20020022 c 20110001 118880 112020 20020022 c 12200001
  //   810001f 20110001 118fc0 112020 20020022 c 1188c3 112020 20020022 c 118903 112020 20020022 c 118903
  //   112020 20020022 c 118903 112020 20020022 c 118903 112020 20020022 c 118903 112020 20020022 c 118903
  //   112020 20020022 c 118903 112020 20020022 c 20100001 109fc0 139fc3 8021 2012000c 24160003 26100001
  //   3210000f 20080008 20090001 139900 2709825 132020 20020022 c 1094022 1500fff9 22100001 2018000f
  //   2188024 108700 20080008 20090001 139902 2709825 132021 20020022 c 1094022 1500fff9 108702 2c9b022
  //   12c00001 8100050 4020 1084027 84400 3508ffff 82021 20020022 c 2010ffff 20110000 ae300000 22100001
  //   22310004 ae300000 22100001 22310004 ae300000 22100001 22310004 ae300000 22100001 22310004 ae300000
  //   22100001 22310004 ae300000 22100001 22310004 ae300000 22100001 22310004 ae300000 22100001 22310004
  //   ae300000 22100001 22310004 ae300000 22100001 22310004 ae300000 22100001 22310004 ae300000 22100001
  //   22310004 ae300000 22100001 22310004 ae300000 22100001 22310004 ae300000 22100001 22310004 ae300000
  //   22100001 22310004 22100001 8020 2011003c 8e130000 8e340000 274402a 11000002 ae330000 ae140000
  //   2231fffc 1611fff8 102020 20020022 c 22100004 2011003c 1611fff2 2002000a c 20080001 20090003 20110876
  //   112020 20020022 c 200b0008 1118804 1318804 112020 20020022 c 216bffff 1560fff9 2002000a c 20080001
  //   20090003 20110876 118d00 112020 20020022 c 200b0008 1118807 1318807 112020 20020022 c 216bffff
  //   1560fff9 2002000a c 20090000 200b0020 20110001 20120001 a5310000 112020 20020022 c 2328820 21290002
  //   216bffff 1560fff8 200b0010 20090000 8d310000 112020 20020022 c 21290004 216bffff 1560fff9 2002000a c
  //   2011000f 112020 20020022 c 2231ffff 1e20fffb 2002000a c 2002000a c 20100000 22100001 102020 20020022
  //   c 22100002 102020 20020022 c 22100003 102020 20020022 c 22100004 102020 20020022 c 22100005 102020
  //   20020022 c 22100006 102020 20020022 c 22100007 102020 20020022 c 22100008 102020 20020022 20020022 c
  //   3e00008
  //   指令字
  //   PC+4
  //   OP
  //   Func
  //   rs
  //   rt
  //   rd
  //   s
  //   JMP
  //   JR
  //   OP
  //   Func
  //   RegDst
  //   译码（ID）
  //   Beq
  //   Bgtz
  //   Bne
  //   MemToReg
  //   MemWrite
  //   AluOP
  //   AluSrcB
  //   RegWrite
  //   JAL
  //   V
  //   Syscall
  //   Sign_ext
  //   控制位
  //   流水调试日志用
  //   暂停节拍，不能为0
  //   戳工具置1进入计数暂停模式，ctrl+k时钟自动运行到对应节拍暂停
  //   ctrl+k关闭时钟连续运行，将控制位置零，进入单步调试模式调试
  //   可计数暂停的时钟源
  //   执行（EX）
  //   为方便自动评测，需要输出流水线各段保存的PC值，注意是PC不是PC+4，另外ID段寄存器写入信息，Mem段内存写入信息也要输出
  //   访存（MEM）
  //   写回（WB）
endmodule

module BTB (
  input  [31:0] PC,
  input  [31:0] EX_PC,
  input  [31:0] EX_BranchAddr,
  input  EX_Branch,
  input  CLK,
  input  Rst,
  input  EX_BranchTaken,
  output [31:0] JumpAddr,
  output PredictJump
);

  wire and_2_out, and_3_out, and_4_out, and_5_out, and_6_out, and_7_out, and_8_out, and_9_out, and_10_out,
       and_11_out, and_12_out, and_13_out, and_14_out, and_15_out, and_16_out, and_17_out, and_18_out,
       and_19_out, and_20_out, and_21_out, and_22_out, and_23_out, and_24_out, and_25_out, and_26_out,
       and_27_out, and_28_out, and_29_out, and_30_out, and_31_out, and_32_out, and_33_out, and_34_out,
       and_35_out, and_36_out, and_37_out, and_38_out, and_39_out, and_40_out, and_41_out, and_42_out,
       and_43_out, and_44_out, and_45_out, and_46_out, and_47_out, and_48_out, and_49_out, and_50_out,
       and_51_out, and_52_out, d_ff_1_q, d_ff_2_q, d_ff_3_q, d_ff_4_q, d_ff_5_q, d_ff_6_q, d_ff_7_q,
       d_ff_8_q, d_ff_9_q, d_ff_10_q, d_ff_11_q, d_ff_12_q, d_ff_13_q, d_ff_14_q, d_ff_15_q, d_ff_16_q,
       decoder_1_out0, decoder_1_out1, decoder_1_out2, decoder_1_out3, decoder_1_out4, decoder_1_out5,
       decoder_1_out6, decoder_1_out7, decoder_1_out8, decoder_1_out9, decoder_1_out10, decoder_1_out11,
       decoder_1_out12, decoder_1_out13, decoder_1_out14, decoder_1_out15, decoder_2_out0, decoder_2_out1,
       decoder_2_out2, decoder_2_out3, decoder_2_out4, decoder_2_out5, decoder_2_out6, decoder_2_out7,
       decoder_2_out8, decoder_2_out9, decoder_2_out10, decoder_2_out11, decoder_2_out12, decoder_2_out13,
       decoder_2_out14, decoder_2_out15, EX_K0, EX_K1, EX_K2, EX_K3, EX_K4, EX_K5, EX_K6, EX_K7, EX_K8,
       EX_K9, EX_K10, EX_K11, EX_K12, EX_K13, EX_K14, EX_K15, EX_L0, EX_L1, EX_L2, EX_L3, EX_L4, EX_L5,
       EX_L6, EX_L7, EX_L8, EX_L9, EX_L10, EX_L11, EX_L12, EX_L13, EX_L14, EX_L15, EX_Miss, full, K0, K1, K2,
       K3, K4, K5, K6, K7, K8, K9, K10, K11, K12, K13, K14, K15, L0, L1, L2, L3, L4, L5, L6, L7, L8, L9, L10,
       L11, L12, L13, L14, L15, Miss, multiplexer_2_out, multiplexer_3_out, multiplexer_4_out,
       multiplexer_5_out, not_1_out, not_4_out, not_5_out, not_6_out, not_7_out, not_8_out, not_9_out,
       not_10_out, not_11_out, not_12_out, not_13_out, not_14_out, not_15_out, not_16_out, not_17_out,
       not_18_out, not_19_out, not_20_out, not_21_out, or_1_out, or_2_out, or_3_out, or_4_out, or_5_out,
       or_6_out, undriven, v0, v1, v2, v3, v4, v5, v6, v7, v8, v9, v10, v11, v12, v13, v14, v15, WriteL0,
       WriteL1, WriteL2, WriteL3, WriteL4, WriteL5, WriteL6, WriteL7, WriteL8, WriteL9, WriteL10, WriteL11,
       WriteL12, WriteL13, WriteL14, WriteL15;
  wire [1:0] controlled_buffer_1_out, controlled_buffer_2_out, register_33_q, register_35_q, register_37_q,
       register_39_q, register_41_q, register_43_q, register_45_q, register_47_q, register_49_q,
       register_51_q, register_53_q, register_55_q, register_57_q, register_59_q, register_61_q,
       register_63_q, \历史位初值 , \双位预测状态转换_1_位0_2 ;
  wire [3:0] \max2_归并比较_1_max_num , \max2_归并比较_2_max_num , \max2_归并比较_3_max_num , \max2_归并比较_4_max_num ,
       \max2_归并比较_5_max_num , \max2_归并比较_6_max_num , \max2_归并比较_7_max_num , \max2_归并比较_8_max_num ,
       \max2_归并比较_9_max_num , \max2_归并比较_10_max_num , \max2_归并比较_11_max_num , \max2_归并比较_12_max_num ,
       \max2_归并比较_13_max_num , \max2_归并比较_14_max_num , \max2_归并比较_15_max_num , priority_encoder_1_out,
       priority_encoder_2_out, priority_encoder_3_out;
  wire [15:0] c0, c1, c2, c3, c4, c5, c6, c7, c8, c9, c10, c11, c12, c13, c14, c15, \max2_归并比较_1_max ,
       \max2_归并比较_2_max , \max2_归并比较_3_max , \max2_归并比较_4_max , \max2_归并比较_5_max , \max2_归并比较_6_max ,
       \max2_归并比较_7_max , \max2_归并比较_8_max , \max2_归并比较_9_max , \max2_归并比较_10_max , \max2_归并比较_11_max ,
       \max2_归并比较_12_max , \max2_归并比较_13_max , \max2_归并比较_14_max ;
  wire [31:0] register_34_q, register_36_q, register_38_q, register_40_q, register_42_q, register_44_q,
       register_46_q, register_48_q, register_50_q, register_52_q, register_54_q, register_56_q,
       register_58_q, register_60_q, register_62_q, register_64_q, tag0, tag1, tag2, tag3, tag4, tag5, tag6,
       tag7, tag8, tag9, tag10, tag11, tag12, tag13, tag14, tag15;

  Register #(.width(1), .trigger("rising"), .Select("low")) register_1 (
    .D(1'b1), .en(WriteL0), .Q(v0), .clk(CLK), .clr(Rst));
  Register #(.width(1), .trigger("rising"), .Select("low")) register_2 (
    .D(1'b1), .en(WriteL1), .Q(v1), .clk(CLK), .clr(Rst));
  Register #(.width(1), .trigger("rising"), .Select("low")) register_3 (
    .D(1'b1), .en(WriteL2), .Q(v2), .clk(CLK), .clr(Rst));
  Register #(.width(1), .trigger("rising"), .Select("low")) register_4 (
    .D(1'b1), .en(WriteL3), .Q(v3), .clk(CLK), .clr(Rst));
  Register #(.width(1), .trigger("rising"), .Select("low")) register_5 (
    .D(1'b1), .en(WriteL4), .Q(v4), .clk(CLK), .clr(Rst));
  Register #(.width(1), .trigger("rising"), .Select("low")) register_6 (
    .D(1'b1), .en(WriteL5), .Q(v5), .clk(CLK), .clr(Rst));
  Register #(.width(1), .trigger("rising"), .Select("low")) register_7 (
    .D(1'b1), .en(WriteL6), .Q(v6), .clk(CLK), .clr(Rst));
  Register #(.width(1), .trigger("rising"), .Select("low")) register_8 (
    .D(1'b1), .en(WriteL7), .Q(v7), .clk(CLK), .clr(Rst));
  Register #(.width(1), .trigger("rising"), .Select("low")) register_9 (
    .D(1'b1), .en(WriteL8), .Q(v8), .clk(CLK), .clr(Rst));
  Register #(.width(1), .trigger("rising"), .Select("low")) register_10 (
    .D(1'b1), .en(WriteL9), .Q(v9), .clk(CLK), .clr(Rst));
  Register #(.width(1), .trigger("rising"), .Select("low")) register_11 (
    .D(1'b1), .en(WriteL10), .Q(v10), .clk(CLK), .clr(Rst));
  Register #(.width(1), .trigger("rising"), .Select("low")) register_12 (
    .D(1'b1), .en(WriteL11), .Q(v11), .clk(CLK), .clr(Rst));
  Register #(.width(1), .trigger("rising"), .Select("low")) register_13 (
    .D(1'b1), .en(WriteL12), .Q(v12), .clk(CLK), .clr(Rst));
  Register #(.width(1), .trigger("rising"), .Select("low")) register_14 (
    .D(1'b1), .en(WriteL13), .Q(v13), .clk(CLK), .clr(Rst));
  Register #(.width(1), .trigger("rising"), .Select("low")) register_15 (
    .D(1'b1), .en(WriteL14), .Q(v14), .clk(CLK), .clr(Rst));
  Register #(.width(1), .trigger("rising"), .Select("low")) register_16 (
    .D(1'b1), .en(WriteL15), .Q(v15), .clk(CLK), .clr(Rst));
  // Probe on tag0
  Register #(.width(32), .trigger("rising"), .Select("low")) register_17 (
    .D(EX_PC), .en(WriteL0), .Q(tag0), .clk(CLK), .clr(undriven));
  // Probe on tag1
  Register #(.width(32), .trigger("rising"), .Select("low")) register_18 (
    .D(EX_PC), .en(WriteL1), .Q(tag1), .clk(CLK));  // open: clr
  // Probe on tag2
  Register #(.width(32), .trigger("rising"), .Select("low")) register_19 (
    .D(EX_PC), .en(WriteL2), .Q(tag2), .clk(CLK));  // open: clr
  // Probe on tag3
  Register #(.width(32), .trigger("rising"), .Select("low")) register_20 (
    .D(EX_PC), .en(WriteL3), .Q(tag3), .clk(CLK));  // open: clr
  Register #(.width(32), .trigger("rising"), .Select("low")) register_21 (
    .D(EX_PC), .en(WriteL4), .Q(tag4), .clk(CLK));  // open: clr
  Register #(.width(32), .trigger("rising"), .Select("low")) register_22 (
    .D(EX_PC), .en(WriteL5), .Q(tag5), .clk(CLK));  // open: clr
  Register #(.width(32), .trigger("rising"), .Select("low")) register_23 (
    .D(EX_PC), .en(WriteL6), .Q(tag6), .clk(CLK));  // open: clr
  Register #(.width(32), .trigger("rising"), .Select("low")) register_24 (
    .D(EX_PC), .en(WriteL7), .Q(tag7), .clk(CLK));  // open: clr
  // Probe on tag8
  Register #(.width(32), .trigger("rising"), .Select("low")) register_25 (
    .D(EX_PC), .en(WriteL8), .Q(tag8), .clk(CLK));  // open: clr
  // Probe on tag9
  Register #(.width(32), .trigger("rising"), .Select("low")) register_26 (
    .D(EX_PC), .en(WriteL9), .Q(tag9), .clk(CLK));  // open: clr
  // Probe on tag10
  Register #(.width(32), .trigger("rising"), .Select("low")) register_27 (
    .D(EX_PC), .en(WriteL10), .Q(tag10), .clk(CLK));  // open: clr
  // Probe on tag11
  Register #(.width(32), .trigger("rising"), .Select("low")) register_28 (
    .D(EX_PC), .en(WriteL11), .Q(tag11), .clk(CLK));  // open: clr
  Register #(.width(32), .trigger("rising"), .Select("low")) register_29 (
    .D(EX_PC), .en(WriteL12), .Q(tag12), .clk(CLK));  // open: clr
  Register #(.width(32), .trigger("rising"), .Select("low")) register_30 (
    .D(EX_PC), .en(WriteL13), .Q(tag13), .clk(CLK));  // open: clr
  Register #(.width(32), .trigger("rising"), .Select("low")) register_31 (
    .D(EX_PC), .en(WriteL14), .Q(tag14), .clk(CLK));  // open: clr
  Register #(.width(32), .trigger("rising"), .Select("low")) register_32 (
    .D(EX_PC), .en(WriteL15), .Q(tag15), .clk(CLK));  // open: clr
  Counter #(.width(16), .max('hffff), .ongoal("wrap"), .trigger("rising"), .behavior("new")) counter_1 (
    .Q(c0), .clk(CLK), .clr(d_ff_1_q));  // open: load, D, count, carry, preset, down
  D_Flip_Flop #(.trigger("rising"), .Pre_Clr_Positions("LEGACY"), .NegatePresetClear("false"), .enable("false"), .NewFFLayout("true")) d_ff_1 (
    .clk(CLK), .D(L0), .Q(d_ff_1_q));  // open: Qn, preset, reset
  Counter #(.width(16), .max('hffff), .ongoal("wrap"), .trigger("rising"), .behavior("new")) counter_2 (
    .Q(c1), .clk(CLK), .clr(d_ff_2_q));  // open: load, D, count, carry, preset, down
  D_Flip_Flop #(.trigger("rising"), .Pre_Clr_Positions("LEGACY"), .NegatePresetClear("false"), .enable("false"), .NewFFLayout("true")) d_ff_2 (
    .clk(CLK), .D(L1), .Q(d_ff_2_q));  // open: Qn, preset, reset
  Counter #(.width(16), .max('hffff), .ongoal("wrap"), .trigger("rising"), .behavior("new")) counter_3 (
    .Q(c2), .clk(CLK), .clr(d_ff_3_q));  // open: load, D, count, carry, preset, down
  D_Flip_Flop #(.trigger("rising"), .Pre_Clr_Positions("LEGACY"), .NegatePresetClear("false"), .enable("false"), .NewFFLayout("true")) d_ff_3 (
    .clk(CLK), .D(L2), .Q(d_ff_3_q));  // open: Qn, preset, reset
  Counter #(.width(16), .max('hffff), .ongoal("wrap"), .trigger("rising"), .behavior("new")) counter_4 (
    .Q(c3), .clk(CLK), .clr(d_ff_4_q));  // open: load, D, count, carry, preset, down
  D_Flip_Flop #(.trigger("rising"), .Pre_Clr_Positions("LEGACY"), .NegatePresetClear("false"), .enable("false"), .NewFFLayout("true")) d_ff_4 (
    .clk(CLK), .D(L3), .Q(d_ff_4_q));  // open: Qn, preset, reset
  Counter #(.width(16), .max('hffff), .ongoal("wrap"), .trigger("rising"), .behavior("new")) counter_5 (
    .Q(c4), .clk(CLK), .clr(d_ff_5_q));  // open: load, D, count, carry, preset, down
  D_Flip_Flop #(.trigger("rising"), .Pre_Clr_Positions("LEGACY"), .NegatePresetClear("false"), .enable("false"), .NewFFLayout("true")) d_ff_5 (
    .clk(CLK), .D(L4), .Q(d_ff_5_q));  // open: Qn, preset, reset
  Counter #(.width(16), .max('hffff), .ongoal("wrap"), .trigger("rising"), .behavior("new")) counter_6 (
    .Q(c5), .clk(CLK), .clr(d_ff_6_q));  // open: load, D, count, carry, preset, down
  D_Flip_Flop #(.trigger("rising"), .Pre_Clr_Positions("LEGACY"), .NegatePresetClear("false"), .enable("false"), .NewFFLayout("true")) d_ff_6 (
    .clk(CLK), .D(L5), .Q(d_ff_6_q));  // open: Qn, preset, reset
  Counter #(.width(16), .max('hffff), .ongoal("wrap"), .trigger("rising"), .behavior("new")) counter_7 (
    .Q(c6), .clk(CLK), .clr(d_ff_7_q));  // open: load, D, count, carry, preset, down
  D_Flip_Flop #(.trigger("rising"), .Pre_Clr_Positions("LEGACY"), .NegatePresetClear("false"), .enable("false"), .NewFFLayout("true")) d_ff_7 (
    .clk(CLK), .D(L6), .Q(d_ff_7_q));  // open: Qn, preset, reset
  Counter #(.width(16), .max('hffff), .ongoal("wrap"), .trigger("rising"), .behavior("new")) counter_8 (
    .Q(c7), .clk(CLK), .clr(d_ff_8_q));  // open: load, D, count, carry, preset, down
  D_Flip_Flop #(.trigger("rising"), .Pre_Clr_Positions("LEGACY"), .NegatePresetClear("false"), .enable("false"), .NewFFLayout("true")) d_ff_8 (
    .clk(CLK), .D(L6), .Q(d_ff_8_q));  // open: Qn, preset, reset
  Counter #(.width(16), .max('hffff), .ongoal("wrap"), .trigger("rising"), .behavior("new")) counter_9 (
    .Q(c8), .clk(CLK), .clr(d_ff_9_q));  // open: load, D, count, carry, preset, down
  D_Flip_Flop #(.trigger("rising"), .Pre_Clr_Positions("LEGACY"), .NegatePresetClear("false"), .enable("false"), .NewFFLayout("true")) d_ff_9 (
    .clk(CLK), .D(L8), .Q(d_ff_9_q));  // open: Qn, preset, reset
  Counter #(.width(16), .max('hffff), .ongoal("wrap"), .trigger("rising"), .behavior("new")) counter_10 (
    .Q(c9), .clk(CLK), .clr(d_ff_10_q));  // open: load, D, count, carry, preset, down
  D_Flip_Flop #(.trigger("rising"), .Pre_Clr_Positions("LEGACY"), .NegatePresetClear("false"), .enable("false"), .NewFFLayout("true")) d_ff_10 (
    .clk(CLK), .D(L9), .Q(d_ff_10_q));  // open: Qn, preset, reset
  Counter #(.width(16), .max('hffff), .ongoal("wrap"), .trigger("rising"), .behavior("new")) counter_11 (
    .Q(c10), .clk(CLK), .clr(d_ff_11_q));  // open: load, D, count, carry, preset, down
  D_Flip_Flop #(.trigger("rising"), .Pre_Clr_Positions("LEGACY"), .NegatePresetClear("false"), .enable("false"), .NewFFLayout("true")) d_ff_11 (
    .clk(CLK), .D(L10), .Q(d_ff_11_q));  // open: Qn, preset, reset
  Counter #(.width(16), .max('hffff), .ongoal("wrap"), .trigger("rising"), .behavior("new")) counter_12 (
    .Q(c11), .clk(CLK), .clr(d_ff_12_q));  // open: load, D, count, carry, preset, down
  D_Flip_Flop #(.trigger("rising"), .Pre_Clr_Positions("LEGACY"), .NegatePresetClear("false"), .enable("false"), .NewFFLayout("true")) d_ff_12 (
    .clk(CLK), .D(L11), .Q(d_ff_12_q));  // open: Qn, preset, reset
  Counter #(.width(16), .max('hffff), .ongoal("wrap"), .trigger("rising"), .behavior("new")) counter_13 (
    .Q(c12), .clk(CLK), .clr(d_ff_13_q));  // open: load, D, count, carry, preset, down
  D_Flip_Flop #(.trigger("rising"), .Pre_Clr_Positions("LEGACY"), .NegatePresetClear("false"), .enable("false"), .NewFFLayout("true")) d_ff_13 (
    .clk(CLK), .D(L12), .Q(d_ff_13_q));  // open: Qn, preset, reset
  Counter #(.width(16), .max('hffff), .ongoal("wrap"), .trigger("rising"), .behavior("new")) counter_14 (
    .Q(c13), .clk(CLK), .clr(d_ff_14_q));  // open: load, D, count, carry, preset, down
  D_Flip_Flop #(.trigger("rising"), .Pre_Clr_Positions("LEGACY"), .NegatePresetClear("false"), .enable("false"), .NewFFLayout("true")) d_ff_14 (
    .clk(CLK), .D(L13), .Q(d_ff_14_q));  // open: Qn, preset, reset
  Counter #(.width(16), .max('hffff), .ongoal("wrap"), .trigger("rising"), .behavior("new")) counter_15 (
    .Q(c14), .clk(CLK), .clr(d_ff_15_q));  // open: load, D, count, carry, preset, down
  D_Flip_Flop #(.trigger("rising"), .Pre_Clr_Positions("LEGACY"), .NegatePresetClear("false"), .enable("false"), .NewFFLayout("true")) d_ff_15 (
    .clk(CLK), .D(L14), .Q(d_ff_15_q));  // open: Qn, preset, reset
  Counter #(.width(16), .max('hffff), .ongoal("wrap"), .trigger("rising"), .behavior("new")) counter_16 (
    .Q(c15), .clk(CLK), .clr(d_ff_16_q));  // open: load, D, count, carry, preset, down
  D_Flip_Flop #(.trigger("rising"), .Pre_Clr_Positions("LEGACY"), .NegatePresetClear("false"), .enable("false"), .NewFFLayout("true")) d_ff_16 (
    .clk(CLK), .D(L15), .Q(d_ff_16_q));  // open: Qn, preset, reset
  Register #(.width(2), .trigger("rising"), .Select("low")) register_33 (
    .D(\历史位初值 ), .en(WriteL0), .Q(register_33_q), .clk(CLK));  // open: clr
  Register #(.width(32), .trigger("rising"), .Select("low")) register_34 (
    .D(EX_BranchAddr), .en(WriteL0), .Q(register_34_q), .clk(CLK));  // open: clr
  Register #(.width(2), .trigger("rising"), .Select("low")) register_35 (
    .D(\历史位初值 ), .en(WriteL1), .Q(register_35_q), .clk(CLK));  // open: clr
  Register #(.width(32), .trigger("rising"), .Select("low")) register_36 (
    .D(EX_BranchAddr), .en(WriteL1), .Q(register_36_q), .clk(CLK));  // open: clr
  Register #(.width(2), .trigger("rising"), .Select("low")) register_37 (
    .D(\历史位初值 ), .en(WriteL2), .Q(register_37_q), .clk(CLK));  // open: clr
  Register #(.width(32), .trigger("rising"), .Select("low")) register_38 (
    .D(EX_BranchAddr), .en(WriteL2), .Q(register_38_q), .clk(CLK));  // open: clr
  Register #(.width(2), .trigger("rising"), .Select("low")) register_39 (
    .D(\历史位初值 ), .en(WriteL3), .Q(register_39_q), .clk(CLK));  // open: clr
  Register #(.width(32), .trigger("rising"), .Select("low")) register_40 (
    .D(EX_BranchAddr), .en(WriteL3), .Q(register_40_q), .clk(CLK));  // open: clr
  Register #(.width(2), .trigger("rising"), .Select("low")) register_41 (
    .D(\历史位初值 ), .en(WriteL4), .Q(register_41_q), .clk(CLK));  // open: clr
  Register #(.width(32), .trigger("rising"), .Select("low")) register_42 (
    .D(EX_BranchAddr), .en(WriteL4), .Q(register_42_q), .clk(CLK));  // open: clr
  Register #(.width(2), .trigger("rising"), .Select("low")) register_43 (
    .D(\历史位初值 ), .en(WriteL5), .Q(register_43_q), .clk(CLK));  // open: clr
  Register #(.width(32), .trigger("rising"), .Select("low")) register_44 (
    .D(EX_BranchAddr), .en(WriteL5), .Q(register_44_q), .clk(CLK));  // open: clr
  Register #(.width(2), .trigger("rising"), .Select("low")) register_45 (
    .D(\历史位初值 ), .en(WriteL6), .Q(register_45_q), .clk(CLK));  // open: clr
  Register #(.width(32), .trigger("rising"), .Select("low")) register_46 (
    .D(EX_BranchAddr), .en(WriteL6), .Q(register_46_q), .clk(CLK));  // open: clr
  Register #(.width(2), .trigger("rising"), .Select("low")) register_47 (
    .D(\历史位初值 ), .en(WriteL7), .Q(register_47_q), .clk(CLK));  // open: clr
  Register #(.width(32), .trigger("rising"), .Select("low")) register_48 (
    .D(EX_BranchAddr), .en(WriteL7), .Q(register_48_q), .clk(CLK));  // open: clr
  Register #(.width(2), .trigger("rising"), .Select("low")) register_49 (
    .D(\历史位初值 ), .en(WriteL8), .Q(register_49_q), .clk(CLK));  // open: clr
  Register #(.width(32), .trigger("rising"), .Select("low")) register_50 (
    .D(EX_BranchAddr), .en(WriteL8), .Q(register_50_q), .clk(CLK));  // open: clr
  Register #(.width(2), .trigger("rising"), .Select("low")) register_51 (
    .D(\历史位初值 ), .en(WriteL9), .Q(register_51_q), .clk(CLK));  // open: clr
  Register #(.width(32), .trigger("rising"), .Select("low")) register_52 (
    .D(EX_BranchAddr), .en(WriteL9), .Q(register_52_q), .clk(CLK));  // open: clr
  Register #(.width(2), .trigger("rising"), .Select("low")) register_53 (
    .D(\历史位初值 ), .en(WriteL10), .Q(register_53_q), .clk(CLK));  // open: clr
  Register #(.width(32), .trigger("rising"), .Select("low")) register_54 (
    .D(EX_BranchAddr), .en(WriteL10), .Q(register_54_q), .clk(CLK));  // open: clr
  Register #(.width(2), .trigger("rising"), .Select("low")) register_55 (
    .D(\历史位初值 ), .en(WriteL11), .Q(register_55_q), .clk(CLK));  // open: clr
  Register #(.width(32), .trigger("rising"), .Select("low")) register_56 (
    .D(EX_BranchAddr), .en(WriteL11), .Q(register_56_q), .clk(CLK));  // open: clr
  Register #(.width(2), .trigger("rising"), .Select("low")) register_57 (
    .D(\历史位初值 ), .en(WriteL12), .Q(register_57_q), .clk(CLK));  // open: clr
  Register #(.width(32), .trigger("rising"), .Select("low")) register_58 (
    .D(EX_BranchAddr), .en(WriteL12), .Q(register_58_q), .clk(CLK));  // open: clr
  Register #(.width(2), .trigger("rising"), .Select("low")) register_59 (
    .D(\历史位初值 ), .en(WriteL13), .Q(register_59_q), .clk(CLK));  // open: clr
  Register #(.width(32), .trigger("rising"), .Select("low")) register_60 (
    .D(EX_BranchAddr), .en(WriteL13), .Q(register_60_q), .clk(CLK));  // open: clr
  Register #(.width(2), .trigger("rising"), .Select("low")) register_61 (
    .D(\历史位初值 ), .en(WriteL14), .Q(register_61_q), .clk(CLK));  // open: clr
  Register #(.width(32), .trigger("rising"), .Select("low")) register_62 (
    .D(EX_BranchAddr), .en(WriteL14), .Q(register_62_q), .clk(CLK));  // open: clr
  Register #(.width(2), .trigger("rising"), .Select("low")) register_63 (
    .D(\历史位初值 ), .en(WriteL15), .Q(register_63_q), .clk(CLK));  // open: clr
  Register #(.width(32), .trigger("rising"), .Select("low")) register_64 (
    .D(EX_BranchAddr), .en(WriteL15), .Q(register_64_q), .clk(CLK));  // open: clr
  // Probe on PC
  assign controlled_buffer_1_out = L0 ? register_33_q : 2'bz;  // Controlled_Buffer controlled_buffer_1
  assign controlled_buffer_2_out = EX_L0 ? register_33_q : 2'bz;  // Controlled_Buffer controlled_buffer_2
  assign JumpAddr = L0 ? register_34_q : 32'bz;  // Controlled_Buffer controlled_buffer_3
  assign controlled_buffer_1_out = L1 ? register_35_q : 2'bz;  // Controlled_Buffer controlled_buffer_4
  assign controlled_buffer_2_out = EX_L1 ? register_35_q : 2'bz;  // Controlled_Buffer controlled_buffer_5
  assign JumpAddr = L1 ? register_36_q : 32'bz;  // Controlled_Buffer controlled_buffer_6
  assign controlled_buffer_1_out = L2 ? register_37_q : 2'bz;  // Controlled_Buffer controlled_buffer_7
  assign controlled_buffer_2_out = EX_L2 ? register_37_q : 2'bz;  // Controlled_Buffer controlled_buffer_8
  assign JumpAddr = L2 ? register_38_q : 32'bz;  // Controlled_Buffer controlled_buffer_9
  assign controlled_buffer_2_out = EX_L3 ? register_39_q : 2'bz;  // Controlled_Buffer controlled_buffer_10
  assign JumpAddr = L3 ? register_40_q : 32'bz;  // Controlled_Buffer controlled_buffer_11
  assign controlled_buffer_1_out = L4 ? register_41_q : 2'bz;  // Controlled_Buffer controlled_buffer_12
  assign controlled_buffer_2_out = EX_L4 ? register_41_q : 2'bz;  // Controlled_Buffer controlled_buffer_13
  assign JumpAddr = L4 ? register_42_q : 32'bz;  // Controlled_Buffer controlled_buffer_14
  assign controlled_buffer_1_out = L5 ? register_43_q : 2'bz;  // Controlled_Buffer controlled_buffer_15
  assign controlled_buffer_2_out = EX_L5 ? register_43_q : 2'bz;  // Controlled_Buffer controlled_buffer_16
  assign JumpAddr = L5 ? register_44_q : 32'bz;  // Controlled_Buffer controlled_buffer_17
  assign controlled_buffer_1_out = L6 ? register_45_q : 2'bz;  // Controlled_Buffer controlled_buffer_18
  assign controlled_buffer_2_out = EX_L6 ? register_45_q : 2'bz;  // Controlled_Buffer controlled_buffer_19
  assign JumpAddr = L6 ? register_46_q : 32'bz;  // Controlled_Buffer controlled_buffer_20
  assign controlled_buffer_1_out = L7 ? register_47_q : 2'bz;  // Controlled_Buffer controlled_buffer_21
  assign controlled_buffer_2_out = EX_L7 ? register_47_q : 2'bz;  // Controlled_Buffer controlled_buffer_22
  assign JumpAddr = L7 ? register_48_q : 32'bz;  // Controlled_Buffer controlled_buffer_23
  assign controlled_buffer_1_out = L8 ? register_49_q : 2'bz;  // Controlled_Buffer controlled_buffer_24
  assign controlled_buffer_2_out = EX_L8 ? register_49_q : 2'bz;  // Controlled_Buffer controlled_buffer_25
  assign JumpAddr = L8 ? register_50_q : 32'bz;  // Controlled_Buffer controlled_buffer_26
  assign controlled_buffer_1_out = L9 ? register_51_q : 2'bz;  // Controlled_Buffer controlled_buffer_27
  assign controlled_buffer_2_out = EX_L9 ? register_51_q : 2'bz;  // Controlled_Buffer controlled_buffer_28
  assign JumpAddr = L9 ? register_52_q : 32'bz;  // Controlled_Buffer controlled_buffer_29
  assign controlled_buffer_1_out = L10 ? register_53_q : 2'bz;  // Controlled_Buffer controlled_buffer_30
  assign controlled_buffer_2_out = EX_L10 ? register_53_q : 2'bz;  // Controlled_Buffer controlled_buffer_31
  assign JumpAddr = L10 ? register_54_q : 32'bz;  // Controlled_Buffer controlled_buffer_32
  assign controlled_buffer_1_out = L11 ? register_55_q : 2'bz;  // Controlled_Buffer controlled_buffer_33
  assign controlled_buffer_2_out = EX_L11 ? register_55_q : 2'bz;  // Controlled_Buffer controlled_buffer_34
  assign JumpAddr = L11 ? register_56_q : 32'bz;  // Controlled_Buffer controlled_buffer_35
  assign controlled_buffer_1_out = L12 ? register_57_q : 2'bz;  // Controlled_Buffer controlled_buffer_36
  assign controlled_buffer_2_out = EX_L12 ? register_57_q : 2'bz;  // Controlled_Buffer controlled_buffer_37
  assign JumpAddr = L12 ? register_58_q : 32'bz;  // Controlled_Buffer controlled_buffer_38
  assign controlled_buffer_1_out = L13 ? register_59_q : 2'bz;  // Controlled_Buffer controlled_buffer_39
  assign controlled_buffer_2_out = EX_L13 ? register_59_q : 2'bz;  // Controlled_Buffer controlled_buffer_40
  assign JumpAddr = L13 ? register_60_q : 32'bz;  // Controlled_Buffer controlled_buffer_41
  assign controlled_buffer_1_out = L14 ? register_61_q : 2'bz;  // Controlled_Buffer controlled_buffer_42
  assign controlled_buffer_2_out = EX_L14 ? register_61_q : 2'bz;  // Controlled_Buffer controlled_buffer_43
  assign JumpAddr = L14 ? register_62_q : 32'bz;  // Controlled_Buffer controlled_buffer_44
  assign controlled_buffer_1_out = L15 ? register_63_q : 2'bz;  // Controlled_Buffer controlled_buffer_45
  assign controlled_buffer_2_out = EX_L15 ? register_63_q : 2'bz;  // Controlled_Buffer controlled_buffer_46
  assign JumpAddr = L15 ? register_64_q : 32'bz;  // Controlled_Buffer controlled_buffer_47
  assign controlled_buffer_1_out = L3 ? register_39_q : 2'bz;  // Controlled_Buffer controlled_buffer_48
  and and_1 (PredictJump, controlled_buffer_1_out[1], not_1_out);
  not not_1 (not_1_out, Miss);
  \双位预测状态转换  \u_双位预测状态转换_1  (
    .\位1 (controlled_buffer_2_out[1]), .\位0 (controlled_buffer_2_out[0]), .\跳转 (EX_BranchTaken),
    .\位1_2 (\双位预测状态转换_1_位0_2 [1]), .\位0_2 (\双位预测状态转换_1_位0_2 [0]));
  Priority_Encoder #(.select(4), .disabled("Z")) priority_encoder_1 (
    .in0(K15), .in1(K14), .in2(K13), .in3(K12), .in4(K11), .in5(K10), .in6(K9), .in7(K8), .in8(K7), .in9(K6),
    .in10(K5), .in11(K4), .in12(K3), .in13(K2), .in14(K1), .in15(K0), .out(priority_encoder_1_out));  // open: gs, en_out, en_in
  Multiplexer #(.select(1), .width(2), .disabled("Z"), .enable("false")) multiplexer_1 (
    .in0(\双位预测状态转换_1_位0_2 ), .in1(2'b00), .out(\历史位初值 ), .sel(EX_Miss));
  Comparator #(.width(32), .mode("twosComplement")) comparator_1 (.a(PC), .b(tag0), .eq(K0));  // open: gt, lt
  Comparator #(.width(32), .mode("twosComplement")) comparator_2 (.a(PC), .b(tag1), .eq(K1));  // open: gt, lt
  Comparator #(.width(32), .mode("twosComplement")) comparator_3 (.a(PC), .b(tag2), .eq(K2));  // open: gt, lt
  Comparator #(.width(32), .mode("twosComplement")) comparator_4 (.a(PC), .b(tag3), .eq(K3));  // open: gt, lt
  Comparator #(.width(32), .mode("twosComplement")) comparator_5 (.a(PC), .b(tag4), .eq(K4));  // open: gt, lt
  Comparator #(.width(32), .mode("twosComplement")) comparator_6 (.a(PC), .b(tag5), .eq(K5));  // open: gt, lt
  Comparator #(.width(32), .mode("twosComplement")) comparator_7 (.a(PC), .b(tag6), .eq(K6));  // open: gt, lt
  Comparator #(.width(32), .mode("twosComplement")) comparator_8 (.a(PC), .b(tag7), .eq(K7));  // open: gt, lt
  or or_1 (or_1_out, L0, L1, L2, L3, L4, L5, L6, L7);
  or or_2 (or_2_out, L8, L9, L10, L11, L12, L13, L14, L15);
  Multiplexer #(.select(4), .width(1), .disabled("Z"), .enable("false")) multiplexer_2 (
    .in0(K15), .in1(K14), .in2(K13), .in3(K12), .in4(K11), .in5(K10), .in6(K9), .in7(K8), .in8(K7), .in9(K6),
    .in10(K5), .in11(K4), .in12(K3), .in13(K2), .in14(K1), .in15(K0), .out(multiplexer_2_out),
    .sel(priority_encoder_1_out));
  not not_2 (Miss, or_3_out);
  or or_3 (or_3_out, or_1_out, or_2_out);
  Comparator #(.width(32), .mode("twosComplement")) comparator_9 (.a(PC), .b(tag8), .eq(K8));  // open: gt, lt
  Comparator #(.width(32), .mode("twosComplement")) comparator_10 (.a(PC), .b(tag9), .eq(K9));  // open: gt, lt
  Comparator #(.width(32), .mode("twosComplement")) comparator_11 (.a(PC), .b(tag10), .eq(K10));  // open: gt, lt
  Comparator #(.width(32), .mode("twosComplement")) comparator_12 (.a(PC), .b(tag11), .eq(K11));  // open: gt, lt
  Comparator #(.width(32), .mode("twosComplement")) comparator_13 (.a(PC), .b(tag12), .eq(K12));  // open: gt, lt
  Comparator #(.width(32), .mode("twosComplement")) comparator_14 (.a(PC), .b(tag13), .eq(K13));  // open: gt, lt
  Comparator #(.width(32), .mode("twosComplement")) comparator_15 (.a(PC), .b(tag14), .eq(K14));  // open: gt, lt
  Comparator #(.width(32), .mode("twosComplement")) comparator_16 (.a(PC), .b(tag15), .eq(K15));  // open: gt, lt
  Multiplexer #(.select(4), .width(1), .disabled("Z"), .enable("false")) multiplexer_3 (
    .in0(v15), .in1(v14), .in2(v13), .in3(v12), .in4(v11), .in5(v10), .in6(v9), .in7(v8), .in8(v7), .in9(v6),
    .in10(v5), .in11(v4), .in12(v3), .in13(v2), .in14(v1), .in15(v0), .out(multiplexer_3_out),
    .sel(priority_encoder_1_out));
  and and_2 (and_2_out, multiplexer_2_out, multiplexer_3_out);
  Demultiplexer #(.select(4), .width(1), .tristate("false"), .disabled("Z"), .enable("false")) demultiplexer_1 (
    .out0(L15), .out1(L14), .out2(L13), .out3(L12), .out4(L11), .out5(L10), .out6(L9), .out7(L8), .out8(L7),
    .out9(L6), .out10(L5), .out11(L4), .out12(L3), .out13(L2), .out14(L1), .out15(L0), .in(and_2_out),
    .sel(priority_encoder_1_out));
  Pull_Resistor #(.pull(0)) pull_resistor_1 (.node(L15));
  Pull_Resistor #(.pull(0)) pull_resistor_2 (.node(L14));
  Pull_Resistor #(.pull(0)) pull_resistor_3 (.node(L13));
  Pull_Resistor #(.pull(0)) pull_resistor_4 (.node(L6));
  Pull_Resistor #(.pull(0)) pull_resistor_5 (.node(L10));
  Pull_Resistor #(.pull(0)) pull_resistor_6 (.node(L9));
  Pull_Resistor #(.pull(0)) pull_resistor_7 (.node(L8));
  Pull_Resistor #(.pull(0)) pull_resistor_8 (.node(L7));
  Pull_Resistor #(.pull(0)) pull_resistor_9 (.node(L11));
  Pull_Resistor #(.pull(0)) pull_resistor_10 (.node(L5));
  Pull_Resistor #(.pull(0)) pull_resistor_11 (.node(L12));
  Pull_Resistor #(.pull(0)) pull_resistor_12 (.node(L2));
  Pull_Resistor #(.pull(0)) pull_resistor_13 (.node(L0));
  Pull_Resistor #(.pull(0)) pull_resistor_14 (.node(L1));
  Pull_Resistor #(.pull(0)) pull_resistor_15 (.node(L3));
  Pull_Resistor #(.pull(0)) pull_resistor_16 (.node(L4));
  Priority_Encoder #(.select(4), .disabled("Z")) priority_encoder_2 (
    .in0(EX_K15), .in1(EX_K14), .in2(EX_K13), .in3(EX_K12), .in4(EX_K11), .in5(EX_K10), .in6(EX_K9),
    .in7(EX_K8), .in8(EX_K7), .in9(EX_K6), .in10(EX_K5), .in11(EX_K4), .in12(EX_K3), .in13(EX_K2),
    .in14(EX_K1), .in15(EX_K0), .out(priority_encoder_2_out));  // open: gs, en_out, en_in
  \Max2_归并比较  \max2_归并比较_1  (
    .Y(c1), .X(c0), .Y_num(4'b0001), .X_num(4'b0000), .MAX(\max2_归并比较_1_max ), .MAX_num(\max2_归并比较_1_max_num ));
  Comparator #(.width(32), .mode("twosComplement")) comparator_17 (.a(EX_PC), .b(tag0), .eq(EX_K0));  // open: gt, lt
  Comparator #(.width(32), .mode("twosComplement")) comparator_18 (.a(EX_PC), .b(tag1), .eq(EX_K1));  // open: gt, lt
  Comparator #(.width(32), .mode("twosComplement")) comparator_19 (.a(EX_PC), .b(tag2), .eq(EX_K2));  // open: gt, lt
  Comparator #(.width(32), .mode("twosComplement")) comparator_20 (.a(EX_PC), .b(tag3), .eq(EX_K3));  // open: gt, lt
  Comparator #(.width(32), .mode("twosComplement")) comparator_21 (.a(EX_PC), .b(tag4), .eq(EX_K4));  // open: gt, lt
  Comparator #(.width(32), .mode("twosComplement")) comparator_22 (.a(EX_PC), .b(tag5), .eq(EX_K5));  // open: gt, lt
  Comparator #(.width(32), .mode("twosComplement")) comparator_23 (.a(EX_PC), .b(tag6), .eq(EX_K6));  // open: gt, lt
  Comparator #(.width(32), .mode("twosComplement")) comparator_24 (.a(EX_PC), .b(tag7), .eq(EX_K7));  // open: gt, lt
  \Max2_归并比较  \max2_归并比较_2  (
    .Y(c2), .X(\max2_归并比较_1_max ), .Y_num(4'b0010), .X_num(\max2_归并比较_1_max_num ), .MAX(\max2_归并比较_2_max ),
    .MAX_num(\max2_归并比较_2_max_num ));
  Multiplexer #(.select(4), .width(1), .disabled("Z"), .enable("false")) multiplexer_4 (
    .in0(EX_K15), .in1(EX_K14), .in2(EX_K13), .in3(EX_K12), .in4(EX_K11), .in5(EX_K10), .in6(EX_K9),
    .in7(EX_K8), .in8(EX_K7), .in9(EX_K6), .in10(EX_K5), .in11(EX_K4), .in12(EX_K3), .in13(EX_K2),
    .in14(EX_K1), .in15(EX_K0), .out(multiplexer_4_out), .sel(priority_encoder_2_out));
  or or_4 (or_4_out, EX_L0, EX_L1, EX_L2, EX_L3, EX_L4, EX_L5, EX_L6, EX_L7);
  or or_5 (or_5_out, EX_L8, EX_L9, EX_L10, EX_L11, EX_L12, EX_L13, EX_L14, EX_L15);
  \Max2_归并比较  \max2_归并比较_3  (
    .Y(c3), .X(\max2_归并比较_2_max ), .Y_num(4'b0011), .X_num(\max2_归并比较_2_max_num ), .MAX(\max2_归并比较_3_max ),
    .MAX_num(\max2_归并比较_3_max_num ));
  not not_3 (EX_Miss, or_6_out);
  or or_6 (or_6_out, or_4_out, or_5_out);
  \Max2_归并比较  \max2_归并比较_4  (
    .Y(c4), .X(\max2_归并比较_3_max ), .Y_num(4'b0100), .X_num(\max2_归并比较_3_max_num ), .MAX(\max2_归并比较_4_max ),
    .MAX_num(\max2_归并比较_4_max_num ));
  Comparator #(.width(32), .mode("twosComplement")) comparator_25 (.a(EX_PC), .b(tag8), .eq(EX_K8));  // open: gt, lt
  Comparator #(.width(32), .mode("twosComplement")) comparator_26 (.a(EX_PC), .b(tag9), .eq(EX_K9));  // open: gt, lt
  Comparator #(.width(32), .mode("twosComplement")) comparator_27 (.a(EX_PC), .b(tag10), .eq(EX_K10));  // open: gt, lt
  Comparator #(.width(32), .mode("twosComplement")) comparator_28 (.a(EX_PC), .b(tag11), .eq(EX_K11));  // open: gt, lt
  Comparator #(.width(32), .mode("twosComplement")) comparator_29 (.a(EX_PC), .b(tag12), .eq(EX_K12));  // open: gt, lt
  Comparator #(.width(32), .mode("twosComplement")) comparator_30 (.a(EX_PC), .b(tag13), .eq(EX_K13));  // open: gt, lt
  Comparator #(.width(32), .mode("twosComplement")) comparator_31 (.a(EX_PC), .b(tag14), .eq(EX_K14));  // open: gt, lt
  Comparator #(.width(32), .mode("twosComplement")) comparator_32 (.a(EX_PC), .b(tag15), .eq(EX_K15));  // open: gt, lt
  \Max2_归并比较  \max2_归并比较_5  (
    .Y(c5), .X(\max2_归并比较_4_max ), .Y_num(4'b0101), .X_num(\max2_归并比较_4_max_num ), .MAX(\max2_归并比较_5_max ),
    .MAX_num(\max2_归并比较_5_max_num ));
  Multiplexer #(.select(4), .width(1), .disabled("Z"), .enable("false")) multiplexer_5 (
    .in0(v15), .in1(v14), .in2(v13), .in3(v12), .in4(v11), .in5(v10), .in6(v9), .in7(v8), .in8(v7), .in9(v6),
    .in10(v5), .in11(v4), .in12(v3), .in13(v2), .in14(v1), .in15(v0), .out(multiplexer_5_out),
    .sel(priority_encoder_2_out));
  \Max2_归并比较  \max2_归并比较_6  (
    .Y(c6), .X(\max2_归并比较_5_max ), .Y_num(4'b0110), .X_num(\max2_归并比较_5_max_num ), .MAX(\max2_归并比较_6_max ),
    .MAX_num(\max2_归并比较_6_max_num ));
  and and_3 (and_3_out, multiplexer_4_out, multiplexer_5_out);
  \Max2_归并比较  \max2_归并比较_7  (
    .Y(c7), .X(\max2_归并比较_6_max ), .Y_num(4'b0111), .X_num(\max2_归并比较_6_max_num ), .MAX(\max2_归并比较_7_max ),
    .MAX_num(\max2_归并比较_7_max_num ));
  Pull_Resistor #(.pull(0)) pull_resistor_17 (.node(EX_L15));
  Demultiplexer #(.select(4), .width(1), .tristate("false"), .disabled("Z"), .enable("false")) demultiplexer_2 (
    .out0(EX_L15), .out1(EX_L14), .out2(EX_L13), .out3(EX_L12), .out4(EX_L11), .out5(EX_L10), .out6(EX_L9),
    .out7(EX_L8), .out8(EX_L7), .out9(EX_L6), .out10(EX_L5), .out11(EX_L4), .out12(EX_L3), .out13(EX_L2),
    .out14(EX_L1), .out15(EX_L0), .in(and_3_out), .sel(priority_encoder_2_out));
  not not_4 (not_4_out, v15);
  not not_5 (not_5_out, v14);
  not not_6 (not_6_out, v13);
  not not_7 (not_7_out, v12);
  not not_8 (not_8_out, v11);
  not not_9 (not_9_out, v10);
  not not_10 (not_10_out, v9);
  not not_11 (not_11_out, v8);
  not not_12 (not_12_out, v7);
  not not_13 (not_13_out, v6);
  not not_14 (not_14_out, v5);
  not not_15 (not_15_out, v4);
  not not_16 (not_16_out, v3);
  not not_17 (not_17_out, v2);
  not not_18 (not_18_out, v1);
  not not_19 (not_19_out, v0);
  \Max2_归并比较  \max2_归并比较_8  (
    .Y(c8), .X(\max2_归并比较_7_max ), .Y_num(4'b1000), .X_num(\max2_归并比较_7_max_num ), .MAX(\max2_归并比较_8_max ),
    .MAX_num(\max2_归并比较_8_max_num ));
  Pull_Resistor #(.pull(0)) pull_resistor_18 (.node(EX_L8));
  Pull_Resistor #(.pull(0)) pull_resistor_19 (.node(EX_L12));
  Pull_Resistor #(.pull(0)) pull_resistor_20 (.node(EX_L13));
  Pull_Resistor #(.pull(0)) pull_resistor_21 (.node(EX_L7));
  Pull_Resistor #(.pull(0)) pull_resistor_22 (.node(EX_L11));
  Pull_Resistor #(.pull(0)) pull_resistor_23 (.node(EX_L9));
  Pull_Resistor #(.pull(0)) pull_resistor_24 (.node(EX_L14));
  Pull_Resistor #(.pull(0)) pull_resistor_25 (.node(EX_L10));
  Pull_Resistor #(.pull(0)) pull_resistor_26 (.node(EX_L0));
  \Max2_归并比较  \max2_归并比较_9  (
    .Y(c9), .X(\max2_归并比较_8_max ), .Y_num(4'b1001), .X_num(\max2_归并比较_8_max_num ), .MAX(\max2_归并比较_9_max ),
    .MAX_num(\max2_归并比较_9_max_num ));
  \Max2_归并比较  \max2_归并比较_10  (
    .Y(c10), .X(\max2_归并比较_9_max ), .Y_num(4'b1010), .X_num(\max2_归并比较_9_max_num ), .MAX(\max2_归并比较_10_max ),
    .MAX_num(\max2_归并比较_10_max_num ));
  Pull_Resistor #(.pull(0)) pull_resistor_27 (.node(EX_L5));
  Pull_Resistor #(.pull(0)) pull_resistor_28 (.node(EX_L6));
  Pull_Resistor #(.pull(0)) pull_resistor_29 (.node(EX_L3));
  Pull_Resistor #(.pull(0)) pull_resistor_30 (.node(EX_L2));
  Pull_Resistor #(.pull(0)) pull_resistor_31 (.node(EX_L4));
  Pull_Resistor #(.pull(0)) pull_resistor_32 (.node(EX_L1));
  Priority_Encoder #(.select(4), .disabled("Z")) priority_encoder_3 (
    .in0(not_4_out), .in1(not_5_out), .in2(not_6_out), .in3(not_7_out), .in4(not_8_out), .in5(not_9_out),
    .in6(not_10_out), .in7(not_11_out), .in8(not_12_out), .in9(not_13_out), .in10(not_14_out),
    .in11(not_15_out), .in12(not_16_out), .in13(not_17_out), .in14(not_18_out), .in15(not_19_out),
    .out(priority_encoder_3_out), .en_out(full));  // open: gs, en_in
  Decoder #(.select(4), .tristate("false"), .disabled("Z"), .enable("false")) decoder_1 (
    .out0(decoder_1_out0), .out1(decoder_1_out1), .out2(decoder_1_out2), .out3(decoder_1_out3),
    .out4(decoder_1_out4), .out5(decoder_1_out5), .out6(decoder_1_out6), .out7(decoder_1_out7),
    .out8(decoder_1_out8), .out9(decoder_1_out9), .out10(decoder_1_out10), .out11(decoder_1_out11),
    .out12(decoder_1_out12), .out13(decoder_1_out13), .out14(decoder_1_out14), .out15(decoder_1_out15),
    .sel(priority_encoder_3_out));
  \Max2_归并比较  \max2_归并比较_11  (
    .Y(c11), .X(\max2_归并比较_10_max ), .Y_num(4'b1011), .X_num(\max2_归并比较_10_max_num ),
    .MAX(\max2_归并比较_11_max ), .MAX_num(\max2_归并比较_11_max_num ));
  \Max2_归并比较  \max2_归并比较_12  (
    .Y(c12), .X(\max2_归并比较_11_max ), .Y_num(4'b1100), .X_num(\max2_归并比较_11_max_num ),
    .MAX(\max2_归并比较_12_max ), .MAX_num(\max2_归并比较_12_max_num ));
  \Max2_归并比较  \max2_归并比较_13  (
    .Y(c13), .X(\max2_归并比较_12_max ), .Y_num(4'b1101), .X_num(\max2_归并比较_12_max_num ),
    .MAX(\max2_归并比较_13_max ), .MAX_num(\max2_归并比较_13_max_num ));
  \Max2_归并比较  \max2_归并比较_14  (
    .Y(c14), .X(\max2_归并比较_13_max ), .Y_num(4'b1110), .X_num(\max2_归并比较_13_max_num ),
    .MAX(\max2_归并比较_14_max ), .MAX_num(\max2_归并比较_14_max_num ));
  \Max2_归并比较  \max2_归并比较_15  (
    .Y(c15), .X(\max2_归并比较_14_max ), .Y_num(4'b1111), .X_num(\max2_归并比较_14_max_num ),
    .MAX_num(\max2_归并比较_15_max_num ));  // open: MAX
  assign WriteL15 = and_20_out ? and_4_out : 1'bz;  // Controlled_Buffer controlled_buffer_49
  and and_4 (and_4_out, EX_Branch, decoder_1_out0);
  and and_5 (and_5_out, EX_Branch, decoder_1_out1);
  assign WriteL14 = and_20_out ? and_5_out : 1'bz;  // Controlled_Buffer controlled_buffer_50
  and and_6 (and_6_out, EX_Branch, decoder_1_out2);
  assign WriteL13 = and_20_out ? and_6_out : 1'bz;  // Controlled_Buffer controlled_buffer_51
  assign WriteL12 = and_20_out ? and_7_out : 1'bz;  // Controlled_Buffer controlled_buffer_52
  and and_7 (and_7_out, EX_Branch, decoder_1_out3);
  and and_8 (and_8_out, EX_Branch, decoder_1_out4);
  assign WriteL11 = and_20_out ? and_8_out : 1'bz;  // Controlled_Buffer controlled_buffer_53
  assign WriteL10 = and_20_out ? and_9_out : 1'bz;  // Controlled_Buffer controlled_buffer_54
  and and_9 (and_9_out, EX_Branch, decoder_1_out5);
  assign WriteL9 = and_20_out ? and_10_out : 1'bz;  // Controlled_Buffer controlled_buffer_55
  and and_10 (and_10_out, EX_Branch, decoder_1_out6);
  and and_11 (and_11_out, EX_Branch, decoder_1_out7);
  assign WriteL8 = and_20_out ? and_11_out : 1'bz;  // Controlled_Buffer controlled_buffer_56
  and and_12 (and_12_out, EX_Branch, decoder_1_out8);
  assign WriteL7 = and_20_out ? and_12_out : 1'bz;  // Controlled_Buffer controlled_buffer_57
  assign WriteL6 = and_20_out ? and_13_out : 1'bz;  // Controlled_Buffer controlled_buffer_58
  and and_13 (and_13_out, EX_Branch, decoder_1_out9);
  and and_14 (and_14_out, EX_Branch, decoder_1_out10);
  assign WriteL5 = and_20_out ? and_14_out : 1'bz;  // Controlled_Buffer controlled_buffer_59
  and and_15 (and_15_out, EX_Branch, decoder_1_out11);
  assign WriteL4 = and_20_out ? and_15_out : 1'bz;  // Controlled_Buffer controlled_buffer_60
  assign WriteL3 = and_20_out ? and_16_out : 1'bz;  // Controlled_Buffer controlled_buffer_61
  and and_16 (and_16_out, EX_Branch, decoder_1_out12);
  assign WriteL2 = and_20_out ? and_17_out : 1'bz;  // Controlled_Buffer controlled_buffer_62
  and and_17 (and_17_out, EX_Branch, decoder_1_out13);
  assign WriteL1 = and_20_out ? and_18_out : 1'bz;  // Controlled_Buffer controlled_buffer_63
  and and_18 (and_18_out, EX_Branch, decoder_1_out14);
  assign WriteL0 = and_20_out ? and_19_out : 1'bz;  // Controlled_Buffer controlled_buffer_64
  and and_19 (and_19_out, EX_Branch, decoder_1_out15);
  Decoder #(.select(4), .tristate("false"), .disabled("Z"), .enable("false")) decoder_2 (
    .out0(decoder_2_out0), .out1(decoder_2_out1), .out2(decoder_2_out2), .out3(decoder_2_out3),
    .out4(decoder_2_out4), .out5(decoder_2_out5), .out6(decoder_2_out6), .out7(decoder_2_out7),
    .out8(decoder_2_out8), .out9(decoder_2_out9), .out10(decoder_2_out10), .out11(decoder_2_out11),
    .out12(decoder_2_out12), .out13(decoder_2_out13), .out14(decoder_2_out14), .out15(decoder_2_out15),
    .sel(\max2_归并比较_15_max_num ));
  not not_20 (not_20_out, full);
  and and_20 (and_20_out, not_20_out, EX_Miss);
  and and_21 (and_21_out, EX_Branch, EX_L15);
  assign WriteL15 = not_21_out ? and_21_out : 1'bz;  // Controlled_Buffer controlled_buffer_65
  assign WriteL14 = not_21_out ? and_22_out : 1'bz;  // Controlled_Buffer controlled_buffer_66
  and and_22 (and_22_out, EX_Branch, EX_L14);
  assign WriteL13 = not_21_out ? and_23_out : 1'bz;  // Controlled_Buffer controlled_buffer_67
  and and_23 (and_23_out, EX_Branch, EX_L13);
  and and_24 (and_24_out, EX_Branch, EX_L12);
  assign WriteL12 = not_21_out ? and_24_out : 1'bz;  // Controlled_Buffer controlled_buffer_68
  assign WriteL11 = not_21_out ? and_25_out : 1'bz;  // Controlled_Buffer controlled_buffer_69
  and and_25 (and_25_out, EX_Branch, EX_L11);
  and and_26 (and_26_out, EX_Branch, EX_L10);
  assign WriteL10 = not_21_out ? and_26_out : 1'bz;  // Controlled_Buffer controlled_buffer_70
  and and_27 (and_27_out, EX_Branch, EX_L9);
  assign WriteL9 = not_21_out ? and_27_out : 1'bz;  // Controlled_Buffer controlled_buffer_71
  assign WriteL8 = not_21_out ? and_28_out : 1'bz;  // Controlled_Buffer controlled_buffer_72
  and and_28 (and_28_out, EX_Branch, EX_L8);
  and and_29 (and_29_out, EX_Branch, EX_L7);
  assign WriteL7 = not_21_out ? and_29_out : 1'bz;  // Controlled_Buffer controlled_buffer_73
  and and_30 (and_30_out, EX_Branch, EX_L6);
  assign WriteL6 = not_21_out ? and_30_out : 1'bz;  // Controlled_Buffer controlled_buffer_74
  assign WriteL5 = not_21_out ? and_31_out : 1'bz;  // Controlled_Buffer controlled_buffer_75
  and and_31 (and_31_out, EX_Branch, EX_L5);
  assign WriteL4 = not_21_out ? and_32_out : 1'bz;  // Controlled_Buffer controlled_buffer_76
  and and_32 (and_32_out, EX_Branch, EX_L4);
  and and_33 (and_33_out, EX_Branch, EX_L3);
  assign WriteL3 = not_21_out ? and_33_out : 1'bz;  // Controlled_Buffer controlled_buffer_77
  and and_34 (and_34_out, EX_Branch, EX_L2);
  assign WriteL2 = not_21_out ? and_34_out : 1'bz;  // Controlled_Buffer controlled_buffer_78
  and and_35 (and_35_out, EX_Branch, EX_L1);
  assign WriteL1 = not_21_out ? and_35_out : 1'bz;  // Controlled_Buffer controlled_buffer_79
  assign WriteL0 = not_21_out ? and_36_out : 1'bz;  // Controlled_Buffer controlled_buffer_80
  and and_36 (and_36_out, EX_Branch, EX_L0);
  not not_21 (not_21_out, EX_Miss);
  and and_37 (and_37_out, EX_Branch, decoder_2_out15);
  assign WriteL15 = full ? and_37_out : 1'bz;  // Controlled_Buffer controlled_buffer_81
  assign WriteL14 = full ? and_38_out : 1'bz;  // Controlled_Buffer controlled_buffer_82
  and and_38 (and_38_out, EX_Branch, decoder_2_out14);
  and and_39 (and_39_out, EX_Branch, decoder_2_out13);
  assign WriteL13 = full ? and_39_out : 1'bz;  // Controlled_Buffer controlled_buffer_83
  assign WriteL12 = full ? and_40_out : 1'bz;  // Controlled_Buffer controlled_buffer_84
  and and_40 (and_40_out, EX_Branch, decoder_2_out12);
  assign WriteL11 = full ? and_41_out : 1'bz;  // Controlled_Buffer controlled_buffer_85
  and and_41 (and_41_out, EX_Branch, decoder_2_out11);
  assign WriteL10 = full ? and_42_out : 1'bz;  // Controlled_Buffer controlled_buffer_86
  and and_42 (and_42_out, EX_Branch, decoder_2_out10);
  assign WriteL9 = full ? and_43_out : 1'bz;  // Controlled_Buffer controlled_buffer_87
  and and_43 (and_43_out, EX_Branch, decoder_2_out9);
  and and_44 (and_44_out, EX_Branch, decoder_2_out8);
  assign WriteL8 = full ? and_44_out : 1'bz;  // Controlled_Buffer controlled_buffer_88
  and and_45 (and_45_out, EX_Branch, decoder_2_out7);
  assign WriteL7 = full ? and_45_out : 1'bz;  // Controlled_Buffer controlled_buffer_89
  and and_46 (and_46_out, EX_Branch, decoder_2_out6);
  assign WriteL6 = full ? and_46_out : 1'bz;  // Controlled_Buffer controlled_buffer_90
  assign WriteL5 = full ? and_47_out : 1'bz;  // Controlled_Buffer controlled_buffer_91
  and and_47 (and_47_out, EX_Branch, decoder_2_out5);
  and and_48 (and_48_out, EX_Branch, decoder_2_out4);
  assign WriteL4 = full ? and_48_out : 1'bz;  // Controlled_Buffer controlled_buffer_92
  assign WriteL3 = full ? and_49_out : 1'bz;  // Controlled_Buffer controlled_buffer_93
  and and_49 (and_49_out, EX_Branch, decoder_2_out3);
  assign WriteL2 = full ? and_50_out : 1'bz;  // Controlled_Buffer controlled_buffer_94
  and and_50 (and_50_out, EX_Branch, decoder_2_out2);
  assign WriteL1 = full ? and_51_out : 1'bz;  // Controlled_Buffer controlled_buffer_95
  and and_51 (and_51_out, EX_Branch, decoder_2_out1);
  assign WriteL0 = full ? and_52_out : 1'bz;  // Controlled_Buffer controlled_buffer_96
  and and_52 (and_52_out, EX_Branch, decoder_2_out0);

  // Other names for the same wires on the sheet: Blk[31:0] = EX_BranchAddr; BlkReady = EX_Branch;
  //   Data32[31:0] = JumpAddr; EX_tag[31:0] = EX_PC; tag[31:0] = PC

  // Notes on the sheet:
  //   输入引脚区
  //   请勿增改引脚，请勿修改子电路封装
  //   电路功能：利用上面给定的隧道构建8行的Cache，cache映射方式自选
  //   VALID
  //   VALID
  //   VALID
  //   VALID
  //   VALID
  //   VALID
  //   VALID
  //   VALID
  //   VALID
  //   VALID
  //   VALID
  //   VALID
  //   VALID
  //   VALID
  //   VALID
  //   VALID
  //   请在下方利用上方输入输出引脚的隧道信号构建电路，ctrl+d复制选择部件
  //   TAG
  //   TAG
  //   TAG
  //   TAG
  //   TAG
  //   TAG
  //   TAG
  //   TAG
  //   TAG
  //   TAG
  //   TAG
  //   TAG
  //   TAG
  //   TAG
  //   输出引脚区
  //   淘汰计数
  //   淘汰计数
  //   淘汰计数
  //   淘汰计数
  //   淘汰计数
  //   淘汰计数
  //   淘汰计数
  //   淘汰计数
  //   淘汰计数
  //   淘汰计数
  //   淘汰计数
  //   淘汰计数
  //   淘汰计数
  //   淘汰计数
  //   淘汰计数
  //   淘汰计数
  //   数据副本
  //   数据副本
  //   数据副本
  //   数据副本
  //   数据副本
  //   数据副本
  //   数据副本
  //   数据副本
  //   数据副本
  //   数据副本
  //   数据副本
  //   数据副本
  //   数据副本
  //   数据副本
  //   数据副本
  //   数据副本
  //   全相联cache
  //   十六路并发比较
  //   行译码信号逻辑
  //   EX十六路并发比较
  //   EX行译码信号逻辑
  //   LRU
  //   读缺失逻辑1：判断是否有空行
endmodule

module \双位预测状态转换  (
  input  \位1 ,
  input  \位0 ,
  input  \跳转 ,
  output \位1_2 ,
  output \位0_2 
);

  wire and_1_out, and_2_out, and_3_out, and_4_out, not_1_out, not_2_out, not_3_out, not_4_out, not_5_out;

  not not_1 (not_1_out, \位0 );
  not not_2 (not_2_out, \位1 );
  not not_3 (not_3_out, \位0 );
  not not_4 (not_4_out, \位0 );
  not not_5 (not_5_out, \跳转 );
  and and_1 (and_1_out, \位0 , \跳转 );
  and and_2 (and_2_out, \位1 , not_1_out);
  and and_3 (and_3_out, not_2_out, not_3_out, \跳转 );
  and and_4 (and_4_out, \位1 , not_4_out, not_5_out);
  or or_1 (\位1_2 , and_1_out, and_2_out);
  or or_2 (\位0_2 , and_3_out, and_4_out);
endmodule

// Max2
module \Max2_归并比较  (
  input  [15:0] Y,
  input  [15:0] X,
  input  [3:0] Y_num,
  input  [3:0] X_num,
  output [15:0] MAX,
  output [3:0] MAX_num
);

  wire comparator_1_eq, comparator_1_gt, or_1_out;

  Multiplexer #(.select(1), .width(16), .disabled("Z"), .enable("true")) multiplexer_1 (
    .in0(Y), .in1(X), .out(MAX), .sel(or_1_out), .en(1'b1));
  Comparator #(.width(16), .mode("unsigned")) comparator_1 (
    .a(X), .b(Y), .gt(comparator_1_gt), .eq(comparator_1_eq));  // open: lt
  or or_1 (or_1_out, comparator_1_gt, comparator_1_eq);
  Multiplexer #(.select(1), .width(4), .disabled("Z"), .enable("false")) multiplexer_2 (
    .in0(Y_num), .in1(X_num), .out(MAX_num), .sel(or_1_out));

  // Notes on the sheet:
  //   输出两个输入中的较大值，并输出较大值的2位编号
endmodule

module \中断按键参考电路  (
  input  \同步清零信号 ,
  output \与中断屏蔽位与 
);

  wire \_1号中断_out , and_1_out, clock_1_out, d_ff_1_q, or_1_out, or_2_out;

  Clock #(.highDuration(1), .lowDuration(1)) clock_1 (.out(clock_1_out));
  Button \_1号中断  (.out(\_1号中断_out ));
  LED #(.active("true")) \_1号中断等待指示灯  (.in(or_1_out));
  or or_1 (or_1_out, \与中断屏蔽位与 , d_ff_1_q);
  D_Flip_Flop #(.trigger("rising"), .Pre_Clr_Positions("LEGACY"), .NegatePresetClear("false"), .enable("true"), .NewFFLayout("false")) d_ff_1 (
    .clk(\_1号中断_out ), .D(1'b1), .Q(d_ff_1_q), .reset(\与中断屏蔽位与 ));  // open: Qn, preset, en
  or or_2 (or_2_out, d_ff_1_q, \与中断屏蔽位与 );
  and and_1 (and_1_out, or_2_out, ~\同步清零信号 );  // AND_Gate
  D_Flip_Flop #(.trigger("rising"), .Pre_Clr_Positions("LEGACY"), .NegatePresetClear("false"), .enable("true"), .NewFFLayout("false")) IR1 (
    .clk(clock_1_out), .D(and_1_out), .Q(\与中断屏蔽位与 ));  // open: Qn, preset, en, reset
  \单周期硬布线控制器  \u_单周期硬布线控制器_1  ();  // open: Func, OP, ALU_OP, MemWrite, ALU_SRC, RegWrite, SysCALL, SignedExt, RegDst, JR, JMP, Beq, JAL, Bne, BGTZ, V, MemToReg

  // Notes on the sheet:
  //   中断信号采样参考电路
  //   Reset 
endmodule
module \单周期MIPS_单级中断  (
  input  IR1,
  input  IR2,
  input  IR3,
  output RegWrite,
  output MemWrite,
  output [31:0] PC,
  output [31:0] IR,
  output [31:0] RDin,
  output [31:0] MDin,
  output [31:0] LedData
);

  wire and_2_out, and_3_out, and_4_out, and_5_out, and_6_out, and_7_out, CLK, clock_1_out, comparator_1_eq,
       comparator_2_eq, comparator_4_eq, comparator_5_eq, comparator_6_eq, comparator_7_eq, comparator_8_eq,
       comparator_10_eq, comparator_10_lt, d_ff_1_q, eret, Go, Halt, INT, IR1_t, IR2_t, IR3_t, IRA, IRB, IRC,
       JAL, JR, mips_alu_1_equal, nand_1_out, not_1_out, not_2_out, not_3_out, not_4_out, or_2_out, or_5_out,
       pos, Rst, sh, SignedExt, syscall, W1, W2, W3, \单周期硬布线控制器_1_alu_src , \单周期硬布线控制器_1_beq ,
       \单周期硬布线控制器_1_bgtz , \单周期硬布线控制器_1_bne , \单周期硬布线控制器_1_jmp , \单周期硬布线控制器_1_memtoreg ,
       \单周期硬布线控制器_1_regdst , \单周期硬布线控制器_1_v ;
  wire [3:0] \单周期硬布线控制器_1_alu_op ;
  wire [4:0] multiplexer_6_out, multiplexer_7_out, multiplexer_8_out, multiplexer_9_out, multiplexer_12_out;
  wire [12:0] CNT_num;
  wire [15:0] ram_1_data_2, \总周期数 ;
  wire [27:0] shifter_1_out;
  wire [31:0] adder_2_out, epc, INT_PC, mips_alu_1_result, multiplexer_1_out, multiplexer_2_out,
       multiplexer_3_out, multiplexer_5_out, multiplexer_10_out, multiplexer_11_out, multiplexer_14_out,
       multiplexer_15_out, next_PC, PC_4, R1, R2, shifter_2_out, \符号扩展_1_out_2 ;
  wire [31:16] ram_1_data;

  Multiplexer #(.select(1), .width(32), .disabled("Z"), .enable("false")) multiplexer_1 (
    .in0(PC_4), .in1(adder_2_out), .out(multiplexer_1_out), .sel(or_5_out));
  Multiplexer #(.select(1), .width(32), .disabled("Z"), .enable("false")) multiplexer_2 (
    .in0({PC_4[31:28], shifter_1_out}), .in1(R1), .out(multiplexer_2_out), .sel(JR));
  Multiplexer #(.select(1), .width(32), .disabled("Z"), .enable("false")) multiplexer_3 (
    .in0(multiplexer_1_out), .in1(multiplexer_2_out), .out(multiplexer_3_out), .sel(\单周期硬布线控制器_1_jmp ));
  Multiplexer #(.select(1), .width(32), .disabled("Z"), .enable("false")) multiplexer_4 (
    .in0(multiplexer_3_out), .in1(epc), .out(next_PC), .sel(eret));
  Button button_1 (.out(Rst));
  Button _1 ();  // open: out
  Button _2 ();  // open: out
  Button _3 ();  // open: out
  // Probe on next_PC
  Multiplexer #(.select(1), .width(32), .disabled("Z"), .enable("false")) multiplexer_5 (
    .in0(next_PC), .in1(INT_PC), .out(multiplexer_5_out), .sel(INT));
  \单级中断处理  \u_单级中断处理_1  (
    .CLK(CLK), .\_1号中断 (IR1_t), .w1(W1), .\_2号中断 (IR2_t), .w2(W2), .\_3号中断 (IR3_t), .w3(W3), .INT_PC(INT_PC),
    .Rst(Rst), .eret(eret), .INT(INT), .stall(1'b0));
  Button \u_继续运行  (.out(Go));
  LED #(.active("true")) led_1 (.in(W1));
  LED #(.active("true")) led_2 (.in(W2));
  LED #(.active("true")) led_3 (.in(W3));
  // Probe on multiplexer_5_out
  not not_1 (not_1_out, Halt);
  Hex_Digit_Display hex_digit_display_1 (.value(LedData[31:28]));  // open: dp
  Hex_Digit_Display hex_digit_display_2 (.value(LedData[27:24]));  // open: dp
  Comparator #(.width(6), .mode("twosComplement")) comparator_1 (
    .a(IR[31:26]), .b(6'b010000), .eq(comparator_1_eq));  // open: gt, lt
  Comparator #(.width(6), .mode("twosComplement")) comparator_2 (
    .a(IR[5:0]), .b(6'b011000), .eq(comparator_2_eq));  // open: gt, lt
  Register #(.width(32), .trigger("rising"), .Select("low")) u_PC (
    .D(multiplexer_5_out), .en(not_1_out), .Q(PC), .clk(CLK), .clr(Rst));
  Hex_Digit_Display hex_digit_display_3 (.value(LedData[19:16]));  // open: dp
  Hex_Digit_Display hex_digit_display_4 (.value(LedData[23:20]));  // open: dp
  and and_1 (eret, comparator_1_eq, comparator_2_eq);
  Adder #(.width(32)) adder_1 (.a(PC), .b(32'h4), .out(PC_4));  // open: cin, cout
  // Probe on PC_4
  Register #(.width(32), .trigger("rising"), .Select("low")) u_epc (
    .D(next_PC), .en(INT), .Q(epc), .clk(CLK), .clr(Rst));
  Hex_Digit_Display hex_digit_display_5 (.value(LedData[15:12]));  // open: dp
  Hex_Digit_Display hex_digit_display_6 (.value(LedData[11:8]));  // open: dp
  // Mips_Probe mips_probe_1: pin names not known; wires that end beside it: IR
  ROM #(.addrWidth(10), .dataWidth(32), .Select("high")) rom_1 (.addr(PC[11:2]), .data(IR));
  Hex_Digit_Display hex_digit_display_7 (.value(LedData[3:0]));  // open: dp
  Hex_Digit_Display hex_digit_display_8 (.value(LedData[7:4]));  // open: dp
  // Probe on \总周期数 
  // Probe on PC
  Comparator #(.width(6), .mode("twosComplement")) comparator_3 (
    .a(6'b101001), .b(IR[31:26]), .eq(sh));  // open: gt, lt
  Multiplexer #(.select(1), .width(5), .disabled("Z"), .enable("false")) multiplexer_6 (
    .in0(IR[25:21]), .in1(5'b00010), .out(multiplexer_6_out), .sel(syscall));
  Multiplexer #(.select(1), .width(5), .disabled("Z"), .enable("false")) multiplexer_7 (
    .in0(IR[20:16]), .in1(IR[15:11]), .out(multiplexer_7_out), .sel(\单周期硬布线控制器_1_regdst ));
  Multiplexer #(.select(1), .width(5), .disabled("Z"), .enable("false")) multiplexer_8 (
    .in0(multiplexer_7_out), .in1({5{1'b1}}), .out(multiplexer_8_out), .sel(JAL));
  \符号扩展  \u_符号扩展_1  (.in_1(IR[15:0]), .out_2(\符号扩展_1_out_2 ));
  Shifter #(.width(28), .shift("ll")) shifter_1 (.in({2'b00, IR[25:0]}), .\dist (5'b00010), .out(shifter_1_out));
  or or_1 (IR1_t, IR1, IRA);
  \单周期硬布线控制器  \u_单周期硬布线控制器_1  (
    .Func(IR[5:0]), .OP(IR[31:26]), .ALU_OP(\单周期硬布线控制器_1_alu_op ), .MemWrite(MemWrite),
    .ALU_SRC(\单周期硬布线控制器_1_alu_src ), .RegWrite(RegWrite), .SysCALL(syscall), .SignedExt(SignedExt),
    .RegDst(\单周期硬布线控制器_1_regdst ), .JR(JR), .JMP(\单周期硬布线控制器_1_jmp ), .Beq(\单周期硬布线控制器_1_beq ), .JAL(JAL),
    .Bne(\单周期硬布线控制器_1_bne ), .BGTZ(\单周期硬布线控制器_1_bgtz ), .V(\单周期硬布线控制器_1_v ), .MemToReg(\单周期硬布线控制器_1_memtoreg ));
  \MIPS_Regfile_上升沿  \mips_regfile_上升沿_1  (
    .Din(RDin), .Clk(CLK), .R1(R1), .R2(R2), .WE(RegWrite), .W_num(multiplexer_8_out),
    .R1_num(multiplexer_6_out), .R2_num(multiplexer_9_out));
  Multiplexer #(.select(1), .width(5), .disabled("Z"), .enable("false")) multiplexer_9 (
    .in0(IR[20:16]), .in1(5'b00100), .out(multiplexer_9_out), .sel(syscall));
  // Probe on multiplexer_8_out
  // Probe on IR[15:0]
  Comparator #(.width(16), .mode("twosComplement")) comparator_4 (
    .a(16'h23b), .b(\总周期数 ), .eq(comparator_4_eq));  // open: gt, lt
  Comparator #(.width(16), .mode("twosComplement")) comparator_5 (
    .a(\总周期数 ), .b(16'h1), .eq(comparator_5_eq));  // open: gt, lt
  Comparator #(.width(16), .mode("twosComplement")) comparator_6 (
    .a(\总周期数 ), .b(16'h4), .eq(comparator_6_eq));  // open: gt, lt
  Comparator #(.width(16), .mode("twosComplement")) comparator_7 (
    .a(\总周期数 ), .b(16'h7), .eq(comparator_7_eq));  // open: gt, lt
  // Probe on IR
  Multiplexer #(.select(1), .width(32), .disabled("Z"), .enable("false")) multiplexer_10 (
    .in0({{16{1'b0}}, IR[15:0]}), .in1(\符号扩展_1_out_2 ), .out(multiplexer_10_out), .sel(SignedExt));
  // Probe on \符号扩展_1_out_2 
  or or_2 (or_2_out, comparator_4_eq, comparator_5_eq);
  assign IRA = or_2_out ? ~CLK : 1'bz;  // Controlled_Inverter controlled_inverter_1
  assign IRB = comparator_6_eq ? ~CLK : 1'bz;  // Controlled_Inverter controlled_inverter_2
  assign IRC = comparator_7_eq ? ~CLK : 1'bz;  // Controlled_Inverter controlled_inverter_3
  or or_3 (IR2_t, IR2, IRB);
  Multiplexer #(.select(1), .width(32), .disabled("Z"), .enable("false")) multiplexer_11 (
    .in0(R2), .in1(multiplexer_10_out), .out(multiplexer_11_out), .sel(\单周期硬布线控制器_1_alu_src ));
  Shifter #(.width(32), .shift("ll")) shifter_2 (.in(\符号扩展_1_out_2 ), .\dist (5'b00010), .out(shifter_2_out));
  Pull_Resistor #(.pull(0)) pull_resistor_1 (.node(IRA));
  Pull_Resistor #(.pull(0)) pull_resistor_2 (.node(IRB));
  Pull_Resistor #(.pull(0)) pull_resistor_3 (.node(IRC));
  // Probe on RDin
  not not_2 (not_2_out, mips_alu_1_equal);
  MIPS_ALU mips_alu_1 (
    .X(R1), .Y(multiplexer_11_out), .AluOP(\单周期硬布线控制器_1_alu_op ), .Equal(mips_alu_1_equal),
    .Result(mips_alu_1_result), .shamt(multiplexer_12_out));  // open: Result_2
  Multiplexer #(.select(1), .width(5), .disabled("Z"), .enable("false")) multiplexer_12 (
    .in0(IR[10:6]), .in1(R1[4:0]), .out(multiplexer_12_out), .sel(\单周期硬布线控制器_1_v ));
  Adder #(.width(32)) adder_2 (.a(shifter_2_out), .b(PC_4), .out(adder_2_out));  // open: cin, cout
  or or_4 (IR3_t, IR3, IRC);
  and and_2 (and_2_out, \单周期硬布线控制器_1_beq , mips_alu_1_equal);
  and and_3 (and_3_out, \单周期硬布线控制器_1_bne , not_2_out);
  and and_4 (and_4_out, \单周期硬布线控制器_1_bgtz , pos);
  Multiplexer #(.select(1), .width(32), .disabled("Z"), .enable("false")) multiplexer_13 (
    .in0(R2), .in1(multiplexer_14_out), .out(MDin), .sel(sh));
  Multiplexer #(.select(1), .width(32), .disabled("Z"), .enable("false")) multiplexer_14 (
    .in0({ram_1_data, R2[15:0]}), .in1({R2[15:0], ram_1_data_2}), .out(multiplexer_14_out),
    .sel(mips_alu_1_result[1]));
  or or_5 (or_5_out, and_2_out, and_3_out, and_4_out);
  // Probe on R1
  Comparator #(.width(32), .mode("twosComplement")) comparator_8 (
    .a(R1), .b(32'ha), .eq(comparator_8_eq));  // open: gt, lt
  Comparator #(.width(32), .mode("twosComplement")) comparator_9 (.a(R1), .b({32{1'b0}}), .gt(pos));  // open: eq, lt
  RAM #(.addrWidth(10), .dataWidth(32), .bus("separate"), .Select("high")) ram_1 (
    .addr(mips_alu_1_result[11:2]), .din(MDin), .data({ram_1_data, ram_1_data_2}), .str(MemWrite), .clk(CLK),
    .ld(\单周期硬布线控制器_1_memtoreg ), .clr(Rst));  // open: sel
  // Probe on R2
  not not_3 (not_3_out, comparator_8_eq);
  and and_5 (and_5_out, not_3_out, syscall);
  and and_6 (and_6_out, syscall, comparator_8_eq);
  Multiplexer #(.select(1), .width(32), .disabled("Z"), .enable("false")) multiplexer_15 (
    .in0(mips_alu_1_result), .in1({ram_1_data, ram_1_data_2}), .out(multiplexer_15_out),
    .sel(\单周期硬布线控制器_1_memtoreg ));
  Register #(.width(32), .trigger("rising"), .Select("low")) register_1 (
    .D(R2), .en(and_5_out), .Q(LedData), .clk(CLK), .clr(Rst));
  Register #(.width(1), .trigger("rising"), .Select("low")) register_2 (
    .D(and_6_out), .en(and_6_out), .Q(Halt), .clk(CLK), .clr(Go));
  Multiplexer #(.select(1), .width(32), .disabled("Z"), .enable("false")) multiplexer_16 (
    .in0(multiplexer_15_out), .in1(PC_4), .out(RDin), .sel(JAL));
  and and_7 (and_7_out, CLK, not_4_out);
  not not_4 (not_4_out, Halt);
  D_Flip_Flop #(.trigger("high"), .Pre_Clr_Positions("LEGACY"), .NegatePresetClear("false"), .enable("true"), .NewFFLayout("false")) d_ff_1 (.Q(d_ff_1_q));  // open: clk, D, Qn, preset, en, reset
  Counter #(.width(16), .max('hffff), .ongoal("wrap"), .trigger("rising"), .behavior("new")) counter_1 (
    .Q(\总周期数 ), .clk(and_7_out), .clr(Rst));  // open: load, D, count, carry, preset, down
  // Probe on CNT_num
  // Probe on 13'hbb
  Comparator #(.width(13), .mode("twosComplement")) comparator_10 (
    .a(CNT_num), .b(13'hbb), .eq(comparator_10_eq), .lt(comparator_10_lt));  // open: gt
  Clock #(.highDuration(1), .lowDuration(1)) clock_1 (.out(clock_1_out));
  nand nand_1 (nand_1_out, d_ff_1_q, comparator_10_eq);
  Counter #(.width(13), .max('h1fff), .ongoal("stay"), .trigger("rising"), .behavior("old")) counter_2 (
    .count(comparator_10_lt), .Q(CNT_num), .clk(clock_1_out), .clr(Rst));  // open: load, D, carry, preset
  assign CLK = nand_1_out ? clock_1_out : 1'bz;  // Controlled_Buffer controlled_buffer_1
  Pull_Resistor #(.pull(1)) pull_resistor_4 (.node(CLK));

  // Other names for the same wires on the sheet: Func[5:0] = IR[5:0]; OP[5:0] = IR[31:26]

  // Notes on the sheet:
  //   中断源
  //   中断等待指示
  //   总复位信号应将除ROM以外所有存储组件全部清零
  //   数码管输出
  //   指令存储器
  //   PC+4
  //   指令字
  //   contents of rom_1 (hex, n*v repeats v):
  //   201d07d0 20100001 109fc0 139fc3 8021 2012000c 24160008 26100001 3210000f 20080008 20090001 139900
  //   2709825 132020 20020022 c 1094022 1500fff9 22100001 2018000f 2188024 108700 20080008 20090001 139902
  //   2709825 132021 20020022 c 1094022 1500fff9 108702 2c9b022 12c00001 8000c07 4020 1084027 84400
  //   3508ffff 82021 20020022 c 8000c01 afa20000 23bd0004 afa40000 23bd0004 afb00000 23bd0004 afb30000
  //   23bd0004 afb40000 23bd0004 afb50000 23bd0004 afb60000 23bd0004 20160001 20140003 20150001 168020
  //   108100 2149825 132020 20020022 c 1600fffa 295a022 1680fff7 23bdfffc 8fb60000 23bdfffc 8fb50000
  //   23bdfffc 8fb40000 23bdfffc 8fb30000 23bdfffc 8fb00000 23bdfffc 8fa40000 23bdfffc 8fa20000 42000018
  //   afa20000 23bd0004 afa40000 23bd0004 afb00000 23bd0004 afb30000 23bd0004 afb40000 23bd0004 afb50000
  //   23bd0004 afb60000 23bd0004 20160002 20140003 20150001 168020 108100 2149825 132020 20020022 c
  //   1600fffa 295a022 1680fff7 23bdfffc 8fb60000 23bdfffc 8fb50000 23bdfffc 8fb40000 23bdfffc 8fb30000
  //   23bdfffc 8fb00000 23bdfffc 8fa40000 23bdfffc 8fa20000 42000018 afa20000 23bd0004 afa40000 23bd0004
  //   afb00000 23bd0004 afb30000 23bd0004 afb40000 23bd0004 afb50000 23bd0004 afb60000 23bd0004 20160003
  //   20140003 20150001 168020 108100 2149825 132020 20020022 c 1600fffa 295a022 1680fff7 23bdfffc
  //   8fb60000 23bdfffc 8fb50000 23bdfffc 8fb40000 23bdfffc 8fb30000 23bdfffc 8fb00000 23bdfffc 8fa40000
  //   23bdfffc 8fa20000 42000018
  //   数码管输出应该用寄存器锁存，否则显示数据只能一闪而过
  //   OP
  //   Func
  //   rs
  //   rt
  //   rd
  //   s
  //   JMP
  //   JR
  //   OP
  //   Func
  //   RegDst
  //   单级中断测试信号模拟器
  //   Beq
  //   Bgtz
  //   Bne
  //   MemToReg
  //   MemWrite
  //   AluOP
  //   AluSrcB
  //   RegWrite
  //   JAL
  //   V
  //   Syscall
  //   Sign_ext
  //   为方便自动评测，需要输出PC，IR，寄存器堆写如数据RDin
  //   RAM写使能MemWrite、RAM写入数据MDin等信号
  //   控制位
  //   暂停节拍，不能为0
  //   用这个时钟源需要去掉电路中的其他时钟源
  //   戳工具置1进入计数暂停模式，ctrl+k时钟自动运行到对应节拍暂停
  //   ctrl+k关闭时钟连续运行，将控制位置零，进入单步调试模式调试
  //   可计数暂停的时钟源
endmodule

module \单周期MIPS_多级中断  (
  input  IR1,
  input  IR2,
  input  IR3,
  output RegWrite,
  output MemWrite,
  output [31:0] PC,
  output [31:0] IR,
  output [31:0] RDin,
  output [31:0] MDin,
  output [31:0] LedData
);

  wire and_1_out, and_2_out, and_3_out, and_4_out, and_5_out, and_6_out, and_7_out, CLK, clock_1_out,
       comparator_2_eq, comparator_4_eq, comparator_5_eq, comparator_6_eq, comparator_6_lt, comparator_7_eq,
       comparator_8_eq, comparator_9_eq, comparator_10_eq, comparator_11_eq, comparator_12_eq,
       comparator_13_eq, d_ff_1_q, eret, Go, Halt, INT, IR1_t, IR2_t, IR3_t, IRA, IRB, IRC, JAL, JR, mfc0,
       mips_alu_1_equal, mtc0, nand_1_out, not_1_out, not_2_out, not_3_out, not_4_out, not_5_out, or_1_out,
       or_5_out, or_6_out, or_7_out, pos, Rst, sh, SignedExt, syscall, W1, W2, W3, \单周期硬布线控制器_1_alu_src ,
       \单周期硬布线控制器_1_beq , \单周期硬布线控制器_1_bgtz , \单周期硬布线控制器_1_bne , \单周期硬布线控制器_1_jmp , \单周期硬布线控制器_1_memtoreg ,
       \单周期硬布线控制器_1_regdst , \单周期硬布线控制器_1_v ;
  wire [3:0] \单周期硬布线控制器_1_alu_op ;
  wire [4:0] multiplexer_6_out, multiplexer_7_out, multiplexer_8_out, multiplexer_9_out, multiplexer_12_out;
  wire [12:0] CNT_num;
  wire [15:0] ram_1_data, \总周期数 ;
  wire [27:0] shifter_1_out;
  wire [31:0] adder_2_out, epc, INT_PC, mips_alu_1_result, multiplexer_1_out, multiplexer_2_out,
       multiplexer_4_out, multiplexer_5_out, multiplexer_10_out, multiplexer_11_out, multiplexer_14_out,
       multiplexer_15_out, next_PC, PC_4, R1, R2, shifter_2_out, \符号扩展_1_out_2 ;
  wire [31:16] ram_1_data_2;

  Multiplexer #(.select(1), .width(32), .disabled("Z"), .enable("false")) multiplexer_1 (
    .in0(PC_4), .in1(adder_2_out), .out(multiplexer_1_out), .sel(or_5_out));
  Button button_1 (.out(Rst));
  Button _1 ();  // open: out
  Button _2 ();  // open: out
  Button _3 ();  // open: out
  // Probe on next_PC
  Multiplexer #(.select(1), .width(32), .disabled("Z"), .enable("false")) multiplexer_2 (
    .in0(multiplexer_1_out), .in1(multiplexer_5_out), .out(multiplexer_2_out), .sel(\单周期硬布线控制器_1_jmp ));
  Multiplexer #(.select(1), .width(32), .disabled("Z"), .enable("false")) multiplexer_3 (
    .in0(multiplexer_2_out), .in1(epc), .out(next_PC), .sel(eret));
  // Probe on INT_PC
  Button \u_继续运行  (.out(Go));
  LED #(.active("true")) led_1 (.in(W1));
  LED #(.active("true")) led_2 (.in(W2));
  LED #(.active("true")) led_3 (.in(W3));
  Multiplexer #(.select(1), .width(32), .disabled("Z"), .enable("false")) multiplexer_4 (
    .in0(next_PC), .in1(INT_PC), .out(multiplexer_4_out), .sel(INT));
  Multiplexer #(.select(1), .width(32), .disabled("Z"), .enable("false")) multiplexer_5 (
    .in0({PC_4[31:28], shifter_1_out}), .in1(R1), .out(multiplexer_5_out), .sel(JR));
  \多级中断处理  \u_多级中断处理_1  (
    .CLK(CLK), .eret(eret), .Rst(Rst), .mfc0(mfc0), .mtc0(mtc0), .\_1号中断 (IR1_t), .w1(W1), .\_2号中断 (IR2_t),
    .w2(W2), .\_3号中断 (IR3_t), .w3(W3), .INT(INT), .INT_PC(INT_PC));
  Hex_Digit_Display hex_digit_display_1 (.value(LedData[31:28]));  // open: dp
  // Probe on multiplexer_4_out
  Register #(.width(32), .trigger("rising"), .Select("low")) u_PC (
    .D(multiplexer_4_out), .en(not_1_out), .Q(PC), .clk(CLK), .clr(Rst));
  not not_1 (not_1_out, Halt);
  Hex_Digit_Display hex_digit_display_2 (.value(LedData[23:20]));  // open: dp
  Hex_Digit_Display hex_digit_display_3 (.value(LedData[27:24]));  // open: dp
  Adder #(.width(32)) adder_1 (.a(PC), .b(32'h4), .out(PC_4));  // open: cin, cout
  Hex_Digit_Display hex_digit_display_4 (.value(LedData[19:16]));  // open: dp
  Hex_Digit_Display hex_digit_display_5 (.value(LedData[15:12]));  // open: dp
  // Probe on PC_4
  and and_1 (and_1_out, INT, not_2_out);
  not not_2 (not_2_out, eret);
  or or_1 (or_1_out, INT, eret);
  Hex_Digit_Display hex_digit_display_6 (.value(LedData[7:4]));  // open: dp
  Hex_Digit_Display hex_digit_display_7 (.value(LedData[11:8]));  // open: dp
  // Mips_Probe mips_probe_1: pin names not known; wires that end beside it: IR
  ROM #(.addrWidth(10), .dataWidth(32), .Select("high")) rom_1 (.addr(PC[11:2]), .data(IR));
  // Probe on epc
  \epc硬件栈  \epc硬件栈_1  (.CLK(CLK), .INT(or_1_out), .Rst(Rst), .push_epc(next_PC), .pop_epc(epc), .PUSH(and_1_out));
  Hex_Digit_Display hex_digit_display_8 (.value(LedData[3:0]));  // open: dp
  // Probe on \总周期数 
  Comparator #(.width(6), .mode("twosComplement")) comparator_1 (
    .a(6'b101001), .b(IR[31:26]), .eq(sh));  // open: gt, lt
  Multiplexer #(.select(1), .width(5), .disabled("Z"), .enable("false")) multiplexer_6 (
    .in0(IR[20:16]), .in1(IR[15:11]), .out(multiplexer_6_out), .sel(\单周期硬布线控制器_1_regdst ));
  Shifter #(.width(28), .shift("ll")) shifter_1 (.in({2'b00, IR[25:0]}), .\dist (5'b00010), .out(shifter_1_out));
  // Probe on PC
  \单周期硬布线控制器  \u_单周期硬布线控制器_1  (
    .Func(IR[5:0]), .OP(IR[31:26]), .ALU_OP(\单周期硬布线控制器_1_alu_op ), .MemWrite(MemWrite),
    .ALU_SRC(\单周期硬布线控制器_1_alu_src ), .RegWrite(RegWrite), .SysCALL(syscall), .SignedExt(SignedExt),
    .RegDst(\单周期硬布线控制器_1_regdst ), .JR(JR), .JMP(\单周期硬布线控制器_1_jmp ), .Beq(\单周期硬布线控制器_1_beq ), .JAL(JAL),
    .Bne(\单周期硬布线控制器_1_bne ), .BGTZ(\单周期硬布线控制器_1_bgtz ), .V(\单周期硬布线控制器_1_v ), .MemToReg(\单周期硬布线控制器_1_memtoreg ));
  Multiplexer #(.select(1), .width(5), .disabled("Z"), .enable("false")) multiplexer_7 (
    .in0(IR[25:21]), .in1(5'b00010), .out(multiplexer_7_out), .sel(syscall));
  Multiplexer #(.select(1), .width(5), .disabled("Z"), .enable("false")) multiplexer_8 (
    .in0(IR[20:16]), .in1(5'b00100), .out(multiplexer_8_out), .sel(syscall));
  // Probe on multiplexer_9_out
  Multiplexer #(.select(1), .width(5), .disabled("Z"), .enable("false")) multiplexer_9 (
    .in0(multiplexer_6_out), .in1({5{1'b1}}), .out(multiplexer_9_out), .sel(JAL));
  \符号扩展  \u_符号扩展_1  (.in_1(IR[15:0]), .out_2(\符号扩展_1_out_2 ));
  // Probe on IR[15:0]
  // Probe on R1
  or or_2 (IR1_t, IR1, IRA);
  \MIPS_Regfile_上升沿  \mips_regfile_上升沿_1  (
    .Din(RDin), .Clk(CLK), .R1(R1), .R2(R2), .WE(RegWrite), .W_num(multiplexer_9_out),
    .R1_num(multiplexer_7_out), .R2_num(multiplexer_8_out));
  Comparator #(.width(32), .mode("twosComplement")) comparator_2 (
    .a(R1), .b(32'ha), .eq(comparator_2_eq));  // open: gt, lt
  // Probe on IR
  or or_3 (IR2_t, IR2, IRB);
  Multiplexer #(.select(1), .width(32), .disabled("Z"), .enable("false")) multiplexer_10 (
    .in0({{16{1'b0}}, IR[15:0]}), .in1(\符号扩展_1_out_2 ), .out(multiplexer_10_out), .sel(SignedExt));
  // Probe on \符号扩展_1_out_2 
  // Probe on R2
  not not_3 (not_3_out, comparator_2_eq);
  and and_2 (and_2_out, not_3_out, syscall);
  and and_3 (and_3_out, syscall, comparator_2_eq);
  Multiplexer #(.select(1), .width(32), .disabled("Z"), .enable("false")) multiplexer_11 (
    .in0(R2), .in1(multiplexer_10_out), .out(multiplexer_11_out), .sel(\单周期硬布线控制器_1_alu_src ));
  Multiplexer #(.select(1), .width(5), .disabled("Z"), .enable("false")) multiplexer_12 (
    .in0(IR[10:6]), .in1(R1[4:0]), .out(multiplexer_12_out), .sel(\单周期硬布线控制器_1_v ));
  Shifter #(.width(32), .shift("ll")) shifter_2 (.in(\符号扩展_1_out_2 ), .\dist (5'b00010), .out(shifter_2_out));
  Register #(.width(32), .trigger("rising"), .Select("low")) register_1 (
    .D(R2), .en(and_2_out), .Q(LedData), .clk(CLK), .clr(Rst));
  Register #(.width(1), .trigger("rising"), .Select("low")) register_2 (
    .D(and_3_out), .en(and_3_out), .Q(Halt), .clk(CLK), .clr(Go));
  // Probe on RDin
  or or_4 (IR3_t, IR3, IRC);
  and and_4 (and_4_out, \单周期硬布线控制器_1_beq , mips_alu_1_equal);
  and and_5 (and_5_out, \单周期硬布线控制器_1_bne , not_4_out);
  not not_4 (not_4_out, mips_alu_1_equal);
  MIPS_ALU mips_alu_1 (
    .X(R1), .Y(multiplexer_11_out), .AluOP(\单周期硬布线控制器_1_alu_op ), .Equal(mips_alu_1_equal),
    .Result(mips_alu_1_result), .shamt(multiplexer_12_out));  // open: Result_2
  Adder #(.width(32)) adder_2 (.a(shifter_2_out), .b(PC_4), .out(adder_2_out));  // open: cin, cout
  and and_6 (and_6_out, \单周期硬布线控制器_1_bgtz , pos);
  Multiplexer #(.select(1), .width(32), .disabled("Z"), .enable("false")) multiplexer_13 (
    .in0(R2), .in1(multiplexer_14_out), .out(MDin), .sel(sh));
  Multiplexer #(.select(1), .width(32), .disabled("Z"), .enable("false")) multiplexer_14 (
    .in0({ram_1_data_2, R2[15:0]}), .in1({R2[15:0], ram_1_data}), .out(multiplexer_14_out),
    .sel(mips_alu_1_result[1]));
  and and_7 (and_7_out, CLK, not_5_out);
  not not_5 (not_5_out, Halt);
  or or_5 (or_5_out, and_4_out, and_5_out, and_6_out);
  Counter #(.width(16), .max('hffff), .ongoal("wrap"), .trigger("rising"), .behavior("new")) counter_1 (
    .Q(\总周期数 ), .clk(and_7_out), .clr(Rst));  // open: load, D, count, carry, preset, down
  Comparator #(.width(32), .mode("twosComplement")) comparator_3 (.a(R1), .b({32{1'b0}}), .gt(pos));  // open: eq, lt
  RAM #(.addrWidth(10), .dataWidth(32), .bus("separate"), .Select("high")) ram_1 (
    .addr(mips_alu_1_result[11:2]), .din(MDin), .data({ram_1_data_2, ram_1_data}), .str(MemWrite), .clk(CLK),
    .ld(\单周期硬布线控制器_1_memtoreg ), .clr(Rst));  // open: sel
  Multiplexer #(.select(1), .width(32), .disabled("Z"), .enable("false")) multiplexer_15 (
    .in0(mips_alu_1_result), .in1({ram_1_data_2, ram_1_data}), .out(multiplexer_15_out),
    .sel(\单周期硬布线控制器_1_memtoreg ));
  Multiplexer #(.select(1), .width(32), .disabled("Z"), .enable("false")) multiplexer_16 (
    .in0(multiplexer_15_out), .in1(PC_4), .out(RDin), .sel(JAL));
  D_Flip_Flop #(.trigger("high"), .Pre_Clr_Positions("LEGACY"), .NegatePresetClear("false"), .enable("true"), .NewFFLayout("false")) d_ff_1 (.Q(d_ff_1_q));  // open: clk, D, Qn, preset, en, reset
  // Probe on 13'h21
  Comparator #(.width(16), .mode("twosComplement")) comparator_4 (
    .a(\总周期数 ), .b(16'h7), .eq(comparator_4_eq));  // open: gt, lt
  Comparator #(.width(16), .mode("twosComplement")) comparator_5 (
    .a(\总周期数 ), .b(16'h241), .eq(comparator_5_eq));  // open: gt, lt
  Comparator #(.width(13), .mode("twosComplement")) comparator_6 (
    .a(CNT_num), .b(13'h21), .eq(comparator_6_eq), .lt(comparator_6_lt));  // open: gt
  Clock #(.highDuration(1), .lowDuration(1)) clock_1 (.out(clock_1_out));
  Comparator #(.width(16), .mode("twosComplement")) comparator_7 (
    .a(16'h258), .b(\总周期数 ), .eq(comparator_7_eq));  // open: gt, lt
  or or_6 (or_6_out, comparator_7_eq, comparator_8_eq);
  Comparator #(.width(16), .mode("twosComplement")) comparator_8 (
    .a(\总周期数 ), .b(16'h1), .eq(comparator_8_eq));  // open: gt, lt
  Comparator #(.width(16), .mode("twosComplement")) comparator_9 (
    .a(\总周期数 ), .b(16'h4), .eq(comparator_9_eq));  // open: gt, lt
  or or_7 (or_7_out, comparator_4_eq, comparator_5_eq);
  Comparator #(.width(6), .mode("twosComplement")) comparator_10 (
    .a(IR[31:26]), .b(6'b010000), .eq(comparator_10_eq));  // open: gt, lt
  Comparator #(.width(6), .mode("twosComplement")) comparator_11 (
    .a(IR[5:0]), .b(6'b011000), .eq(comparator_11_eq));  // open: gt, lt
  Comparator #(.width(5), .mode("twosComplement")) comparator_12 (
    .a(IR[25:21]), .b({5{1'b0}}), .eq(comparator_12_eq));  // open: gt, lt
  Comparator #(.width(5), .mode("twosComplement")) comparator_13 (
    .a(IR[25:21]), .b(5'b00100), .eq(comparator_13_eq));  // open: gt, lt
  Counter #(.width(13), .max('h1fff), .ongoal("stay"), .trigger("rising"), .behavior("old")) counter_2 (
    .count(comparator_6_lt), .Q(CNT_num), .clk(clock_1_out), .clr(Rst));  // open: load, D, carry, preset
  Pull_Resistor #(.pull(0)) pull_resistor_1 (.node(IRA));
  assign IRA = or_6_out ? ~CLK : 1'bz;  // Controlled_Inverter controlled_inverter_1
  Pull_Resistor #(.pull(0)) pull_resistor_2 (.node(IRB));
  assign IRB = comparator_9_eq ? ~CLK : 1'bz;  // Controlled_Inverter controlled_inverter_2
  Pull_Resistor #(.pull(0)) pull_resistor_3 (.node(IRC));
  assign IRC = or_7_out ? ~CLK : 1'bz;  // Controlled_Inverter controlled_inverter_3
  and and_8 (eret, comparator_10_eq, comparator_11_eq);
  and and_9 (mfc0, comparator_10_eq, comparator_12_eq);
  and and_10 (mtc0, comparator_10_eq, comparator_13_eq);
  nand nand_1 (nand_1_out, d_ff_1_q, comparator_6_eq);
  assign CLK = nand_1_out ? clock_1_out : 1'bz;  // Controlled_Buffer controlled_buffer_1
  Pull_Resistor #(.pull(1)) pull_resistor_4 (.node(CLK));

  // Other names for the same wires on the sheet: rs[4:0] = IR[25:21]; Func[5:0] = IR[5:0]; OP[5:0] = IR[31:26]

  // Notes on the sheet:
  //   中断源
  //   中断等待指示
  //   总复位信号应将除ROM以外所有存储组件全部清零
  //   PC+4
  //   数码管输出
  //   指令存储器
  //   数码管输出应该用寄存器锁存，否则显示数据只能一闪而过
  //   指令字
  //   contents of rom_1 (hex, n*v repeats v):
  //   201d07d0 20100001 109fc0 139fc3 8021 2012000c 24160008 26100001 3210000f 20080008 20090001 139900
  //   2709825 132020 20020022 c 1094022 1500fff9 22100001 2018000f 2188024 108700 20080008 20090001 139902
  //   2709825 132021 20020022 c 1094022 1500fff9 108702 2c9b022 12c00001 8000c07 4020 1084027 84400
  //   3508ffff 82021 20020022 c 8000c01 afa20000 23bd0004 afa40000 23bd0004 afb00000 23bd0004 afb30000
  //   23bd0004 afb40000 23bd0004 afb50000 23bd0004 afb60000 23bd0004 40000000 20160001 20140003 20150001
  //   168020 108100 2149825 132020 20020022 c 1600fffa 295a022 1680fff7 40800000 23bdfffc 8fb60000
  //   23bdfffc 8fb50000 23bdfffc 8fb40000 23bdfffc 8fb30000 23bdfffc 8fb00000 23bdfffc 8fa40000 23bdfffc
  //   8fa20000 42000018 afa20000 23bd0004 afa40000 23bd0004 afb00000 23bd0004 afb30000 23bd0004 afb40000
  //   23bd0004 afb50000 23bd0004 afb60000 23bd0004 40000000 20160002 20140003 20150001 168020 108100
  //   2149825 132020 20020022 c 1600fffa 295a022 1680fff7 40800000 23bdfffc 8fb60000 23bdfffc 8fb50000
  //   23bdfffc 8fb40000 23bdfffc 8fb30000 23bdfffc 8fb00000 23bdfffc 8fa40000 23bdfffc 8fa20000 42000018
  //   afa20000 23bd0004 afa40000 23bd0004 afb00000 23bd0004 afb30000 23bd0004 afb40000 23bd0004 afb50000
  //   23bd0004 afb60000 23bd0004 40000000 20160003 20140003 20150001 168020 108100 2149825 132020 20020022
  //   c 1600fffa 295a022 1680fff7 40800000 23bdfffc 8fb60000 23bdfffc 8fb50000 23bdfffc 8fb40000 23bdfffc
  //   8fb30000 23bdfffc 8fb00000 23bdfffc 8fa40000 23bdfffc 8fa20000 42000018
  //   OP
  //   Func
  //   rs
  //   rt
  //   rd
  //   s
  //   Beq
  //   JMP
  //   Bgtz
  //   JR
  //   Bne
  //   OP
  //   JAL
  //   Func
  //   V
  //   RegDst
  //   Syscall
  //   Sign_ext
  //   MemToReg
  //   MemWrite
  //   AluOP
  //   AluSrcB
  //   RegWrite
  //   为方便自动评测，需要输出PC，IR，寄存器堆写如数据RDin
  //   RAM写使能MemWrite、RAM写入数据MDin等信号
  //   控制位
  //   暂停节拍，不能为0
  //   多级中断测试信号模拟器
  //   戳工具置1进入计数暂停模式，ctrl+k时钟自动运行到对应节拍暂停
  //   ctrl+k关闭时钟连续运行，将控制位置零，进入单步调试模式调试
  //   用这个时钟源需要去掉电路中的其他时钟源
  //   可计数暂停的时钟源
endmodule

module \单级中断处理  (
  input  CLK,
  input  eret,
  input  Rst,
  input  stall,
  input  \_1号中断 ,
  input  \_2号中断 ,
  input  \_3号中断 ,
  output INT,
  output w1,
  output [31:0] INT_PC,
  output w2,
  output w3
);

  wire and_1_out, and_2_out, and_3_out, and_4_out, and_6_out, Clr0, Clr1, Clr2, Clr3, d_ff_1_q, d_ff_2_q,
       d_ff_3_q, IR1_2_q, IR1_3_q, IR1_q, mie_qn, not_1_out, not_2_out, not_3_out, not_4_out, or_4_out,
       or_5_out, or_6_out, or_7_out, or_8_out, or_9_out, priority_encoder_1_gs;
  wire [1:0] IntNo, mause_q;

  or or_1 (w1, IR1_q, d_ff_1_q);
  or or_2 (w2, IR1_2_q, d_ff_2_q);
  or or_3 (w3, IR1_3_q, d_ff_3_q);
  D_Flip_Flop #(.trigger("rising"), .Pre_Clr_Positions("LEGACY"), .NegatePresetClear("false"), .enable("true"), .NewFFLayout("false")) d_ff_1 (
    .clk(\_1号中断 ), .D(1'b1), .Q(d_ff_1_q), .reset(or_4_out));  // open: Qn, preset, en
  or or_4 (or_4_out, IR1_q, Rst);
  D_Flip_Flop #(.trigger("rising"), .Pre_Clr_Positions("LEGACY"), .NegatePresetClear("false"), .enable("true"), .NewFFLayout("false")) d_ff_2 (
    .clk(\_2号中断 ), .D(1'b1), .Q(d_ff_2_q), .reset(or_5_out));  // open: Qn, preset, en
  or or_5 (or_5_out, IR1_2_q, Rst);
  D_Flip_Flop #(.trigger("rising"), .Pre_Clr_Positions("LEGACY"), .NegatePresetClear("false"), .enable("true"), .NewFFLayout("false")) d_ff_3 (
    .clk(\_3号中断 ), .D(1'b1), .Q(d_ff_3_q), .reset(or_6_out));  // open: Qn, preset, en
  or or_6 (or_6_out, IR1_3_q, Rst);
  or or_7 (or_7_out, d_ff_1_q, IR1_q);
  or or_8 (or_8_out, d_ff_2_q, IR1_2_q);
  or or_9 (or_9_out, d_ff_3_q, IR1_3_q);
  and and_1 (and_1_out, or_7_out, ~Clr1);  // AND_Gate
  and and_2 (and_2_out, or_8_out, ~Clr2);  // AND_Gate
  and and_3 (and_3_out, or_9_out, ~Clr3);  // AND_Gate
  D_Flip_Flop #(.trigger("rising"), .Pre_Clr_Positions("LEGACY"), .NegatePresetClear("false"), .enable("true"), .NewFFLayout("false")) IR1 (
    .clk(CLK), .D(and_1_out), .Q(IR1_q), .reset(Rst));  // open: Qn, preset, en
  D_Flip_Flop #(.trigger("rising"), .Pre_Clr_Positions("LEGACY"), .NegatePresetClear("false"), .enable("true"), .NewFFLayout("false")) IR1_2 (
    .clk(CLK), .D(and_2_out), .Q(IR1_2_q), .reset(Rst));  // open: Qn, preset, en
  D_Flip_Flop #(.trigger("rising"), .Pre_Clr_Positions("LEGACY"), .NegatePresetClear("false"), .enable("true"), .NewFFLayout("false")) IR1_3 (
    .clk(CLK), .D(and_3_out), .Q(IR1_3_q), .reset(Rst));  // open: Qn, preset, en
  not not_1 (not_1_out, stall);
  Priority_Encoder #(.select(2), .disabled("Z")) priority_encoder_1 (
    .in1(IR1_q), .in2(IR1_2_q), .in3(IR1_3_q), .out(IntNo), .gs(priority_encoder_1_gs));  // open: in0, en_out, en_in
  Multiplexer #(.select(2), .width(32), .disabled("Z"), .enable("false")) multiplexer_1 (
    .in1(32'h30ac), .in2(32'h3150), .in3(32'h31f4), .out(INT_PC), .sel(IntNo));  // open: in0
  not not_2 (not_2_out, eret);
  and and_4 (and_4_out, not_2_out, priority_encoder_1_gs);
  not not_3 (not_3_out, stall);
  D_Flip_Flop #(.trigger("rising"), .Pre_Clr_Positions("LEGACY"), .NegatePresetClear("false"), .enable("true"), .NewFFLayout("false")) mie (
    .clk(CLK), .D(and_4_out), .Qn(mie_qn), .en(not_3_out), .reset(Rst));  // open: Q, preset
  not not_4 (not_4_out, stall);
  and and_5 (INT, mie_qn, priority_encoder_1_gs);
  and and_6 (and_6_out, mie_qn, not_4_out);
  Register #(.width(2), .trigger("rising"), .Select("low")) mause (
    .D(IntNo), .en(and_6_out), .Q(mause_q), .clk(CLK), .clr(Rst));
  Decoder #(.select(2), .tristate("false"), .disabled("Z"), .enable("true")) decoder_1 (
    .out0(Clr0), .out1(Clr1), .out2(Clr2), .out3(Clr3), .sel(mause_q), .en(eret));
  Pull_Resistor #(.pull(0)) pull_resistor_1 (.node(Clr1));
  Pull_Resistor #(.pull(0)) pull_resistor_2 (.node(Clr2));
  Pull_Resistor #(.pull(0)) pull_resistor_3 (.node(Clr3));

  // Notes on the sheet:
  //   中断等待
  //   Reset 
  //   Reset 
  //   Reset 
  //   中断优先编码器
endmodule

module \多级中断处理  (
  input  CLK,
  input  eret,
  input  Rst,
  input  mfc0,
  input  mtc0,
  input  \_1号中断 ,
  input  \_2号中断 ,
  input  \_3号中断 ,
  output INT,
  output w1,
  output w2,
  output [31:0] INT_PC,
  output w3
);

  wire and_1_out, and_2_out, and_3_out, and_4_out, and_5_out, Clr0, Clr1, Clr2, Clr3, comparator_1_gt,
       d_ff_1_q, d_ff_2_q, d_ff_3_q, en, IR1_2_q, IR1_3_q, IR1_q, mie_qn, mtc0_t, not_1_out, not_2_out,
       not_3_out, or_4_out, or_5_out, or_6_out, or_7_out, or_8_out, or_9_out, or_10_out;
  wire [1:0] IntNo, mause_q, pop_num;

  or or_1 (w1, IR1_q, d_ff_1_q);
  or or_2 (w2, IR1_2_q, d_ff_2_q);
  or or_3 (w3, IR1_3_q, d_ff_3_q);
  D_Flip_Flop #(.trigger("rising"), .Pre_Clr_Positions("LEGACY"), .NegatePresetClear("false"), .enable("true"), .NewFFLayout("false")) d_ff_1 (
    .clk(\_1号中断 ), .D(1'b1), .Q(d_ff_1_q), .reset(or_4_out));  // open: Qn, preset, en
  or or_4 (or_4_out, IR1_q, Rst);
  D_Flip_Flop #(.trigger("rising"), .Pre_Clr_Positions("LEGACY"), .NegatePresetClear("false"), .enable("true"), .NewFFLayout("false")) d_ff_2 (
    .clk(\_2号中断 ), .D(1'b1), .Q(d_ff_2_q), .reset(or_5_out));  // open: Qn, preset, en
  or or_5 (or_5_out, IR1_2_q, Rst);
  D_Flip_Flop #(.trigger("rising"), .Pre_Clr_Positions("LEGACY"), .NegatePresetClear("false"), .enable("true"), .NewFFLayout("false")) d_ff_3 (
    .clk(\_3号中断 ), .D(1'b1), .Q(d_ff_3_q), .reset(or_6_out));  // open: Qn, preset, en
  or or_6 (or_6_out, IR1_3_q, Rst);
  or or_7 (or_7_out, d_ff_1_q, IR1_q);
  or or_8 (or_8_out, d_ff_2_q, IR1_2_q);
  or or_9 (or_9_out, d_ff_3_q, IR1_3_q);
  and and_1 (and_1_out, or_7_out, ~Clr1);  // AND_Gate
  and and_2 (and_2_out, or_8_out, ~Clr2);  // AND_Gate
  and and_3 (and_3_out, or_9_out, ~Clr3);  // AND_Gate
  D_Flip_Flop #(.trigger("rising"), .Pre_Clr_Positions("LEGACY"), .NegatePresetClear("false"), .enable("true"), .NewFFLayout("false")) IR1 (
    .clk(CLK), .D(and_1_out), .Q(IR1_q), .reset(Rst));  // open: Qn, preset, en
  D_Flip_Flop #(.trigger("rising"), .Pre_Clr_Positions("LEGACY"), .NegatePresetClear("false"), .enable("true"), .NewFFLayout("false")) IR1_2 (
    .clk(CLK), .D(and_2_out), .Q(IR1_2_q), .reset(Rst));  // open: Qn, preset, en
  D_Flip_Flop #(.trigger("rising"), .Pre_Clr_Positions("LEGACY"), .NegatePresetClear("false"), .enable("true"), .NewFFLayout("false")) IR1_3 (
    .clk(CLK), .D(and_3_out), .Q(IR1_3_q), .reset(Rst));  // open: Qn, preset, en
  Priority_Encoder #(.select(2), .disabled("Z")) priority_encoder_1 (
    .in1(IR1_q), .in2(IR1_2_q), .in3(IR1_3_q), .out(IntNo));  // open: in0, gs, en_out, en_in
  not not_1 (not_1_out, mfc0);
  Comparator #(.width(2), .mode("unsigned")) comparator_1 (
    .a(IntNo), .b(pop_num), .gt(comparator_1_gt));  // open: eq, lt
  Multiplexer #(.select(2), .width(32), .disabled("Z"), .enable("false")) multiplexer_1 (
    .in1(32'h30ac), .in2(32'h3158), .in3(32'h3204), .out(INT_PC), .sel(IntNo));  // open: in0
  not not_2 (not_2_out, eret);
  and and_4 (and_4_out, INT, not_2_out);
  \mcause硬件栈  \mcause硬件栈_1  (.CLK(CLK), .en(en), .RST(Rst), .push_num(IntNo), .pop_num(pop_num), .PUSH(and_4_out));
  not not_3 (not_3_out, eret);
  and and_5 (and_5_out, not_3_out, not_1_out, 1'b1);
  Pull_Resistor #(.pull(0)) pull_resistor_1 (.node(comparator_1_gt));
  Register #(.width(1), .trigger("rising"), .Select("low")) register_1 (
    .D(mtc0), .Q(mtc0_t), .clk(CLK));  // open: en, clr
  D_Flip_Flop #(.trigger("rising"), .Pre_Clr_Positions("LEGACY"), .NegatePresetClear("false"), .enable("true"), .NewFFLayout("false")) mie (
    .clk(CLK), .D(and_5_out), .Qn(mie_qn), .preset(mtc0_t), .en(or_10_out), .reset(Rst));  // open: Q
  or or_10 (or_10_out, INT, mfc0, eret);
  and and_6 (INT, mie_qn, comparator_1_gt);
  Register #(.width(2), .trigger("rising"), .Select("low")) mause (
    .D(IntNo), .en(mie_qn), .Q(mause_q), .clk(CLK), .clr(Rst));
  Decoder #(.select(2), .tristate("false"), .disabled("Z"), .enable("true")) decoder_1 (
    .out0(Clr0), .out1(Clr1), .out2(Clr2), .out3(Clr3), .sel(mause_q), .en(eret));
  or or_11 (en, INT, eret);
  Pull_Resistor #(.pull(0)) pull_resistor_2 (.node(Clr2));
  Pull_Resistor #(.pull(0)) pull_resistor_3 (.node(Clr3));
  Pull_Resistor #(.pull(0)) pull_resistor_4 (.node(Clr1));

  // Other names for the same wires on the sheet: mfc00 = mfc0

  // Notes on the sheet:
  //   中断等待
  //   Reset 
  //   Reset 
  //   Reset 
  //   中断优先编码器
endmodule

module \epc硬件栈  (
  input  CLK,
  input  INT,
  input  Rst,
  input  PUSH,
  input  [31:0] push_epc,
  output [31:0] pop_epc
);

  wire [31:0] epc_2_q, epc_3_q, epc_4_q, multiplexer_1_out, multiplexer_2_out, multiplexer_3_out;

  Register #(.width(32), .trigger("rising"), .Select("low")) epc (
    .D(epc_2_q), .Q(pop_epc), .clk(CLK), .clr(Rst));  // open: en
  Multiplexer #(.select(1), .width(32), .disabled("Z"), .enable("false")) multiplexer_1 (
    .in0(epc_3_q), .in1(push_epc), .out(multiplexer_1_out), .sel(PUSH));
  Register #(.width(32), .trigger("rising"), .Select("low")) epc_2 (
    .D(multiplexer_1_out), .en(INT), .Q(epc_2_q), .clk(CLK), .clr(Rst));
  Register #(.width(32), .trigger("rising"), .Select("low")) epc_3 (
    .D(multiplexer_2_out), .en(INT), .Q(epc_3_q), .clk(CLK), .clr(Rst));
  Multiplexer #(.select(1), .width(32), .disabled("Z"), .enable("false")) multiplexer_2 (
    .in0(epc_4_q), .in1(epc_2_q), .out(multiplexer_2_out), .sel(PUSH));
  Multiplexer #(.select(1), .width(32), .disabled("Z"), .enable("false")) multiplexer_3 (
    .in0({32{1'b0}}), .in1(epc_3_q), .out(multiplexer_3_out), .sel(PUSH));
  Register #(.width(32), .trigger("rising"), .Select("low")) epc_4 (
    .D(multiplexer_3_out), .en(INT), .Q(epc_4_q), .clk(CLK), .clr(Rst));
endmodule

// mcause
module \mcause硬件栈  (
  input  CLK,
  input  en,
  input  RST,
  input  PUSH,
  input  [1:0] push_num,
  output [1:0] pop_num
);

  wire [1:0] multiplexer_1_out, multiplexer_2_out, multiplexer_3_out, register_2_q, register_3_q;

  Multiplexer #(.select(1), .width(2), .disabled("Z"), .enable("false")) multiplexer_1 (
    .in0(register_2_q), .in1(push_num), .out(multiplexer_1_out), .sel(PUSH));
  Register #(.width(2), .trigger("rising"), .Select("low")) register_1 (
    .D(multiplexer_1_out), .en(en), .Q(pop_num), .clk(CLK), .clr(RST));
  Multiplexer #(.select(1), .width(2), .disabled("Z"), .enable("false")) multiplexer_2 (
    .in0(register_3_q), .in1(pop_num), .out(multiplexer_2_out), .sel(PUSH));
  Register #(.width(2), .trigger("rising"), .Select("low")) register_2 (
    .D(multiplexer_2_out), .en(en), .Q(register_2_q), .clk(CLK), .clr(RST));
  Register #(.width(2), .trigger("rising"), .Select("low")) register_3 (
    .D(multiplexer_3_out), .en(en), .Q(register_3_q), .clk(CLK), .clr(RST));
  Multiplexer #(.select(1), .width(2), .disabled("Z"), .enable("false")) multiplexer_3 (
    .in0(2'b00), .in1(register_2_q), .out(multiplexer_3_out), .sel(PUSH));
endmodule

module \流水线中断  (
  output RegWrite,
  output MemWrite,
  output [31:0] IF_PC,
  output [31:0] ID_PC,
  output [31:0] EX_PC,
  output [31:0] M_PC,
  output [31:0] WB_PC,
  output [31:0] RDin,
  output [31:0] MDin,
  output [31:0] LedData
);

  wire and_2_out, and_3_out, and_4_out, and_6_out, and_7_out, and_8_out, BranchTaken, CLK, clock_1_out,
       clock_2_out, comparator_1_eq, comparator_2_eq, comparator_3_eq, comparator_4_eq, comparator_6_eq,
       comparator_6_lt, comparator_7_gt, comparator_8_eq, comparator_9_eq, comparator_10_eq,
       comparator_11_eq, comparator_12_eq, comparator_13_eq, comparator_14_eq, d_ff_1_q, eret,
       ex_mem_1_jal_2, ex_mem_1_memtoreg_2, ex_mem_1_regwrite_2, ex_mem_1_sh_2, ex_mem_1_syscall_2, Go, Halt,
       HS, id_ex_bubble_1_alusrcb_2, id_ex_bubble_1_beq_2, id_ex_bubble_1_bgtz_2, id_ex_bubble_1_bne_2,
       id_ex_bubble_1_jal_2, id_ex_bubble_1_memtoreg_2, id_ex_bubble_1_memwrite_2, id_ex_bubble_1_regwrite_2,
       id_ex_bubble_1_sh_2, id_ex_bubble_1_syscall_2, id_ex_bubble_1_v_2, INT, INT1, IR1, IR2, IR3, IRA, IRB,
       IRC, JAL, JMP, JR, mem_wb_1_jal_2, mem_wb_1_memtoreg_2, mips_alu_1_equal, nand_1_out, not_1_out,
       not_2_out, not_3_out, not_4_out, not_5_out, not_6_out, not_7_out, not_8_out, not_9_out, not_10_out,
       not_11_out, not_12_out, or_1_out, or_2_out, or_3_out, or_5_out, or_6_out, or_7_out, Rst, sh,
       SignedExt, stall, syscall, W1, W2, W3, \单周期硬布线控制器_1_alu_src , \单周期硬布线控制器_1_beq , \单周期硬布线控制器_1_bgtz ,
       \单周期硬布线控制器_1_bne , \单周期硬布线控制器_1_jmp , \单周期硬布线控制器_1_jr , \单周期硬布线控制器_1_memtoreg ,
       \单周期硬布线控制器_1_memwrite , \单周期硬布线控制器_1_regdst , \单周期硬布线控制器_1_regwrite , \单周期硬布线控制器_1_syscall ,
       \单周期硬布线控制器_1_v , \气泡流水线相关处理逻辑_1_flush ;
  wire [1:0] priority_encoder_1_out;
  wire [3:0] id_ex_bubble_1_aluop_2, \单周期硬布线控制器_1_alu_op ;
  wire [4:0] ex_mem_1_writereg_2, id_ex_bubble_1_s_2, id_ex_bubble_1_writereg_2, ID_R1, ID_R2,
       multiplexer_8_out, multiplexer_13_out, WR, WriteReg;
  wire [5:0] if_id_bubble_1_rd_out;
  wire [12:0] CNT_num;
  wire [15:0] \LoadUse次数 , ram_1_data, \总周期数 , \插入气泡数 , \无条件分支数 , \条件分支成功数 ;
  wire [25:0] if_id_bubble_1_rd_out_2;
  wire [27:0] shifter_1_out;
  wire [31:0] adder_2_out, epc, EX_IR, ex_mem_1_pc_4_2, ex_mem_1_result_2, ex_mem_1_rs_2, EX_RS,
       id_ex_bubble_1_ext_2, id_ex_bubble_1_j_pc_2, id_ex_bubble_1_pc_4_2, id_ex_bubble_1_rt_2,
       id_ex_bubble_1_sign_ext_2, ID_IR, if_id_bubble_1_pc_4_out, IF_IR, INT_PC, MEM_IR, mem_wb_1_pc_4_2,
       mem_wb_1_rd_2, mem_wb_1_result_2, mips_alu_1_result, mips_regifile_1_r1, mips_regifile_1_r2,
       multiplexer_1_out, multiplexer_2_out, multiplexer_3_out, multiplexer_4_out, multiplexer_5_out,
       multiplexer_11_out, multiplexer_12_out, multiplexer_15_out, multiplexer_16_out, next_PC, PC_4, R2, RS,
       RT, shifter_2_out, WB_IR, \符号扩展_1_out_2 ;
  wire [31:16] ram_1_data_2;

  Button \u_总复位  (.out(Rst));
  Button _1 (.out(IR1));
  Button _2 (.out(IR2));
  Button _3 (.out(IR3));
  // Probe on \总周期数 
  // Probe on \总周期数 
  Multiplexer #(.select(1), .width(32), .disabled("Z"), .enable("false")) multiplexer_1 (
    .in0(PC_4), .in1(adder_2_out), .out(multiplexer_1_out), .sel(BranchTaken));
  Multiplexer #(.select(1), .width(32), .disabled("Z"), .enable("false")) multiplexer_2 (
    .in0(multiplexer_1_out), .in1(multiplexer_3_out), .out(multiplexer_2_out), .sel(JMP));
  Multiplexer #(.select(1), .width(32), .disabled("Z"), .enable("false")) multiplexer_3 (
    .in0(id_ex_bubble_1_j_pc_2), .in1(EX_RS), .out(multiplexer_3_out), .sel(JR));
  Button \u_继续运行  (.out(Go));
  LED #(.active("true")) led_1 (.in(W1));
  LED #(.active("true")) led_2 (.in(W2));
  LED #(.active("true")) led_3 (.in(W3));
  // Probe on IF_PC
  // Mips_Probe mips_probe_1: pin names not known; wires that end beside it: IF_IR
  \气泡流水线相关处理逻辑  \u_气泡流水线相关处理逻辑_1  (
    .EX_WriteReg(id_ex_bubble_1_writereg_2), .Branch(or_3_out), .MEM_WriteReg(ex_mem_1_writereg_2),
    .Flush(\气泡流水线相关处理逻辑_1_flush ), .Stall(stall), .EX_RegWrite(id_ex_bubble_1_regwrite_2),
    .MEM_RegWrite(ex_mem_1_regwrite_2), .R1(ID_R1), .R2(ID_R2), .OP(if_id_bubble_1_rd_out),
    .func(if_id_bubble_1_rd_out_2[5:0]));
  Multiplexer #(.select(1), .width(32), .disabled("Z"), .enable("false")) multiplexer_4 (
    .in0(multiplexer_2_out), .in1(epc), .out(multiplexer_4_out), .sel(eret));
  Multiplexer #(.select(1), .width(32), .disabled("Z"), .enable("false")) multiplexer_5 (
    .in0(multiplexer_4_out), .in1(INT_PC), .out(multiplexer_5_out), .sel(INT));
  not not_1 (not_1_out, comparator_1_eq);
  Comparator #(.width(32), .mode("twosComplement")) comparator_1 (
    .a(M_PC), .b({32{1'b0}}), .eq(comparator_1_eq));  // open: gt, lt
  not not_2 (not_2_out, comparator_2_eq);
  Comparator #(.width(32), .mode("twosComplement")) comparator_2 (
    .a(EX_PC), .b({32{1'b0}}), .eq(comparator_2_eq));  // open: gt, lt
  not not_3 (not_3_out, comparator_3_eq);
  Comparator #(.width(32), .mode("twosComplement")) comparator_3 (
    .a(ID_PC), .b({32{1'b0}}), .eq(comparator_3_eq));  // open: gt, lt
  Comparator #(.width(32), .mode("twosComplement")) comparator_4 (
    .a(IF_PC), .b({32{1'b0}}), .eq(comparator_4_eq));  // open: gt, lt
  not not_4 (not_4_out, comparator_4_eq);
  Priority_Encoder #(.select(2), .disabled("Z")) priority_encoder_1 (
    .in0(not_4_out), .in1(not_3_out), .in2(not_2_out), .in3(not_1_out), .out(priority_encoder_1_out));  // open: gs, en_out, en_in
  Hex_Digit_Display hex_digit_display_1 (.value(LedData[27:24]));  // open: dp
  Hex_Digit_Display hex_digit_display_2 (.value(LedData[31:28]));  // open: dp
  // Probe on multiplexer_5_out
  and and_1 (HS, not_5_out, not_6_out);
  not not_5 (not_5_out, Halt);
  not not_6 (not_6_out, stall);
  Multiplexer #(.select(2), .width(32), .disabled("Z"), .enable("false")) multiplexer_6 (
    .in0(IF_PC), .in1(ID_PC), .in2(EX_PC), .in3(M_PC), .out(next_PC), .sel(priority_encoder_1_out));
  Hex_Digit_Display hex_digit_display_3 (.value(LedData[19:16]));  // open: dp
  Hex_Digit_Display hex_digit_display_4 (.value(LedData[23:20]));  // open: dp
  // Probe on ID_PC
  // Mips_Probe mips_probe_2: pin names not known; wires that end beside it: ID_IR
  Register #(.width(32), .trigger("rising"), .Select("low")) PC (
    .D(multiplexer_5_out), .en(HS), .Q(IF_PC), .clk(CLK), .clr(Rst));
  Adder #(.width(32)) adder_1 (.a(IF_PC), .b(32'h4), .out(PC_4));  // open: cin, cout
  // Probe on next_PC
  Hex_Digit_Display hex_digit_display_5 (.value(LedData[15:12]));  // open: dp
  Hex_Digit_Display hex_digit_display_6 (.value(LedData[11:8]));  // open: dp
  // Mips_Probe mips_probe_3: pin names not known; wires that end beside it: IF_IR
  Hex_Digit_Display hex_digit_display_7 (.value(LedData[7:4]));  // open: dp
  Hex_Digit_Display hex_digit_display_8 (.value(LedData[3:0]));  // open: dp
  Clock #(.highDuration(1), .lowDuration(1)) clock_1 (.out(clock_1_out));
  // Probe on EX_PC
  // Mips_Probe mips_probe_4: pin names not known; wires that end beside it: clock_1_out, CLK, EX_IR
  ROM #(.addrWidth(10), .dataWidth(32), .Select("high")) rom_1 (.addr(IF_PC[11:2]), .data(IF_IR));
  // Probe on M_PC
  or or_1 (or_1_out, Rst, eret, or_3_out);
  IF_ID_bubble if_id_bubble_1 (
    .PC(IF_PC), .RD_in(IF_IR), .PC_4_in(PC_4), .PC_2(ID_PC), .CLR(or_1_out),
    .RD_out({if_id_bubble_1_rd_out, if_id_bubble_1_rd_out_2}), .PC_4_out(if_id_bubble_1_pc_4_out), .en(HS),
    .CLK(CLK), .INT(INT), .INT_2(INT1));  // open: PredictJump, PredictJump_2
  // Probe on \总周期数 
  // Mips_Probe mips_probe_5: pin names not known; wires that end beside it: MEM_IR
  // Probe on \总周期数 
  // Probe on \无条件分支数 
  // Probe on \条件分支成功数 
  // Probe on \插入气泡数 
  // Probe on \LoadUse次数 
  // Probe on WB_PC
  // Mips_Probe mips_probe_6: pin names not known; wires that end beside it: WB_IR
  Comparator #(.width(6), .mode("twosComplement")) comparator_5 (
    .a(6'b101001), .b(if_id_bubble_1_rd_out), .eq(sh));  // open: gt, lt
  Multiplexer #(.select(1), .width(5), .disabled("Z"), .enable("false")) multiplexer_7 (
    .in0(if_id_bubble_1_rd_out_2[25:21]), .in1(5'b00010), .out(ID_R1), .sel(\单周期硬布线控制器_1_syscall ));
  Multiplexer #(.select(1), .width(5), .disabled("Z"), .enable("false")) multiplexer_8 (
    .in0(if_id_bubble_1_rd_out_2[20:16]), .in1(if_id_bubble_1_rd_out_2[15:11]), .out(multiplexer_8_out),
    .sel(\单周期硬布线控制器_1_regdst ));
  Multiplexer #(.select(1), .width(5), .disabled("Z"), .enable("false")) multiplexer_9 (
    .in0(multiplexer_8_out), .in1({5{1'b1}}), .out(WR), .sel(JAL));
  \符号扩展  \u_符号扩展_1  (.in_1(if_id_bubble_1_rd_out_2[15:0]), .out_2(\符号扩展_1_out_2 ));
  Shifter #(.width(28), .shift("ll")) shifter_1 (
    .in({2'b00, if_id_bubble_1_rd_out_2}), .\dist (5'b00010), .out(shifter_1_out));
  // Probe on IF_PC[11:0]
  \单周期硬布线控制器  \u_单周期硬布线控制器_1  (
    .Func(if_id_bubble_1_rd_out_2[5:0]), .OP(if_id_bubble_1_rd_out), .ALU_OP(\单周期硬布线控制器_1_alu_op ),
    .MemWrite(\单周期硬布线控制器_1_memwrite ), .ALU_SRC(\单周期硬布线控制器_1_alu_src ), .RegWrite(\单周期硬布线控制器_1_regwrite ),
    .SysCALL(\单周期硬布线控制器_1_syscall ), .SignedExt(SignedExt), .RegDst(\单周期硬布线控制器_1_regdst ),
    .JR(\单周期硬布线控制器_1_jr ), .JMP(\单周期硬布线控制器_1_jmp ), .Beq(\单周期硬布线控制器_1_beq ), .JAL(JAL),
    .Bne(\单周期硬布线控制器_1_bne ), .BGTZ(\单周期硬布线控制器_1_bgtz ), .V(\单周期硬布线控制器_1_v ), .MemToReg(\单周期硬布线控制器_1_memtoreg ));
  Multiplexer #(.select(1), .width(5), .disabled("Z"), .enable("false")) multiplexer_10 (
    .in0(if_id_bubble_1_rd_out_2[20:16]), .in1(5'b00100), .out(ID_R2), .sel(\单周期硬布线控制器_1_syscall ));
  \单级中断处理  \u_单级中断处理_1  (
    .CLK(CLK), .\_1号中断 (IR1), .w1(W1), .\_2号中断 (IR2), .w2(W2), .\_3号中断 (IR3), .w3(W3), .INT_PC(INT_PC),
    .Rst(Rst), .eret(eret), .INT(INT), .stall(stall));
  // Probe on EX_PC[11:0]
  // Probe on ID_PC[11:0]
  D_Flip_Flop #(.trigger("high"), .Pre_Clr_Positions("LEGACY"), .NegatePresetClear("false"), .enable("true"), .NewFFLayout("false")) d_ff_1 (.Q(d_ff_1_q));  // open: clk, D, Qn, preset, en, reset
  not not_7 (not_7_out, Halt);
  Multiplexer #(.select(1), .width(32), .disabled("Z"), .enable("false")) multiplexer_11 (
    .in0({{16{1'b0}}, if_id_bubble_1_rd_out_2[15:0]}), .in1(\符号扩展_1_out_2 ), .out(multiplexer_11_out),
    .sel(SignedExt));
  // Probe on M_PC[11:0]
  // Probe on WB_PC[11:0]
  // Probe on 13'h79
  or or_2 (or_2_out, INT, INT1, \气泡流水线相关处理逻辑_1_flush , eret);
  MIPS_Regifile mips_regifile_1 (
    .Din(RDin), .Clk(CLK), .R1(mips_regifile_1_r1), .R2(mips_regifile_1_r2), .WE(RegWrite), .W_num(WriteReg),
    .R1_num(ID_R1), .R2_num(ID_R2));
  ID_EX_bubble id_ex_bubble_1 (
    .Beq(\单周期硬布线控制器_1_beq ), .Bgtz(\单周期硬布线控制器_1_bgtz ), .Bne(\单周期硬布线控制器_1_bne ),
    .MemToReg(\单周期硬布线控制器_1_memtoreg ), .MemWrite(\单周期硬布线控制器_1_memwrite ), .AluOP(\单周期硬布线控制器_1_alu_op ),
    .AluSrcB(\单周期硬布线控制器_1_alu_src ), .RegWrite(\单周期硬布线控制器_1_regwrite ), .JAL(JAL), .V(\单周期硬布线控制器_1_v ),
    .RS(mips_regifile_1_r1), .RT(mips_regifile_1_r2), .WriteReg(WR), .ext(multiplexer_11_out), .sh(sh),
    .Sign_ext(\符号扩展_1_out_2 ), .syscall(\单周期硬布线控制器_1_syscall ), .S(if_id_bubble_1_rd_out_2[10:6]),
    .PC(ID_PC), .PC_4(if_id_bubble_1_pc_4_out), .Beq_2(id_ex_bubble_1_beq_2), .Bgtz_2(id_ex_bubble_1_bgtz_2),
    .Bne_2(id_ex_bubble_1_bne_2), .CLR(or_2_out), .MemToReg_2(id_ex_bubble_1_memtoreg_2),
    .MemWrite_2(id_ex_bubble_1_memwrite_2), .AluOP_2(id_ex_bubble_1_aluop_2),
    .AluSrcB_2(id_ex_bubble_1_alusrcb_2), .RegWrite_2(id_ex_bubble_1_regwrite_2),
    .JAL_2(id_ex_bubble_1_jal_2), .V_2(id_ex_bubble_1_v_2), .RS_2(EX_RS), .RT_2(id_ex_bubble_1_rt_2),
    .WriteReg_2(id_ex_bubble_1_writereg_2), .ext_2(id_ex_bubble_1_ext_2), .sh_2(id_ex_bubble_1_sh_2),
    .Sign_ext_2(id_ex_bubble_1_sign_ext_2), .syscall_2(id_ex_bubble_1_syscall_2), .S_2(id_ex_bubble_1_s_2),
    .PC_2(EX_PC), .PC_4_2(id_ex_bubble_1_pc_4_2), .CLK(CLK), .JMP(\单周期硬布线控制器_1_jmp ), .JMP_2(JMP),
    .JR(\单周期硬布线控制器_1_jr ), .JR_2(JR), .J_PC({if_id_bubble_1_pc_4_out[31:28], shifter_1_out}),
    .J_PC_2(id_ex_bubble_1_j_pc_2), .en(not_7_out));  // open: RsForward, RsForward_2, RtForward, RtForward_2, PredictJump_2, PredictJump
  // Probe on IF_PC
  Comparator #(.width(13), .mode("twosComplement")) comparator_6 (
    .a(CNT_num), .b(13'h79), .eq(comparator_6_eq), .lt(comparator_6_lt));  // open: gt
  Clock #(.highDuration(1), .lowDuration(1)) clock_2 (.out(clock_2_out));
  Multiplexer #(.select(1), .width(32), .disabled("Z"), .enable("false")) multiplexer_12 (
    .in0(id_ex_bubble_1_rt_2), .in1(id_ex_bubble_1_ext_2), .out(multiplexer_12_out),
    .sel(id_ex_bubble_1_alusrcb_2));
  nand nand_1 (nand_1_out, d_ff_1_q, comparator_6_eq);
  Counter #(.width(13), .max('h1fff), .ongoal("stay"), .trigger("rising"), .behavior("old")) counter_1 (
    .count(comparator_6_lt), .Q(CNT_num), .clk(clock_2_out), .clr(Rst));  // open: load, D, carry, preset
  Comparator #(.width(32), .mode("twosComplement")) comparator_7 (
    .a(EX_RS), .b({32{1'b0}}), .gt(comparator_7_gt));  // open: eq, lt
  Multiplexer #(.select(1), .width(5), .disabled("Z"), .enable("false")) multiplexer_13 (
    .in0(id_ex_bubble_1_s_2), .in1(EX_RS[4:0]), .out(multiplexer_13_out), .sel(id_ex_bubble_1_v_2));
  Shifter #(.width(32), .shift("ll")) shifter_2 (
    .in(id_ex_bubble_1_sign_ext_2), .\dist (5'b00010), .out(shifter_2_out));
  Register #(.width(32), .trigger("rising"), .Select("low")) u_epc (
    .D(next_PC), .en(INT), .Q(epc), .clk(CLK), .clr(Rst));
  assign CLK = nand_1_out ? clock_2_out : 1'bz;  // Controlled_Buffer controlled_buffer_1
  Pull_Resistor #(.pull(1)) pull_resistor_1 (.node(CLK));
  or or_3 (or_3_out, JMP, BranchTaken);
  and and_2 (and_2_out, id_ex_bubble_1_beq_2, mips_alu_1_equal);
  and and_3 (and_3_out, id_ex_bubble_1_bne_2, not_8_out);
  not not_8 (not_8_out, mips_alu_1_equal);
  and and_4 (and_4_out, id_ex_bubble_1_bgtz_2, comparator_7_gt);
  MIPS_ALU mips_alu_1 (
    .X(EX_RS), .Y(multiplexer_12_out), .AluOP(id_ex_bubble_1_aluop_2), .Equal(mips_alu_1_equal),
    .Result(mips_alu_1_result), .shamt(multiplexer_13_out));  // open: Result_2
  Adder #(.width(32)) adder_2 (.a(shifter_2_out), .b(id_ex_bubble_1_pc_4_2), .out(adder_2_out));  // open: cin, cout
  not not_9 (not_9_out, Halt);
  or or_4 (BranchTaken, and_2_out, and_3_out, and_4_out);
  // Probe on mips_alu_1_result
  or or_5 (or_5_out, Rst, eret, INT);
  EX_MEM ex_mem_1 (
    .MemToReg(id_ex_bubble_1_memtoreg_2), .MemWrite(id_ex_bubble_1_memwrite_2),
    .RegWrite(id_ex_bubble_1_regwrite_2), .JAL(id_ex_bubble_1_jal_2), .Result(mips_alu_1_result),
    .WriteReg(id_ex_bubble_1_writereg_2), .PC_4(id_ex_bubble_1_pc_4_2), .MemToReg_2(ex_mem_1_memtoreg_2),
    .MemWrite_2(MemWrite), .RegWrite_2(ex_mem_1_regwrite_2), .JAL_2(ex_mem_1_jal_2),
    .Result_2(ex_mem_1_result_2), .WriteReg_2(ex_mem_1_writereg_2), .PC_4_2(ex_mem_1_pc_4_2), .CLK(CLK),
    .RT(id_ex_bubble_1_rt_2), .RT_2(R2), .PC(EX_PC), .PC_2(M_PC), .syscall(id_ex_bubble_1_syscall_2),
    .syscall_2(ex_mem_1_syscall_2), .RS(EX_RS), .RS_2(ex_mem_1_rs_2), .sh(id_ex_bubble_1_sh_2),
    .sh_2(ex_mem_1_sh_2), .CLR(or_5_out), .en(not_9_out));
  Comparator #(.width(6), .mode("twosComplement")) comparator_8 (
    .a(IF_IR[31:26]), .b(6'b010000), .eq(comparator_8_eq));  // open: gt, lt
  Comparator #(.width(6), .mode("twosComplement")) comparator_9 (
    .a(IF_IR[5:0]), .b(6'b011000), .eq(comparator_9_eq));  // open: gt, lt
  Multiplexer #(.select(1), .width(32), .disabled("Z"), .enable("false")) multiplexer_14 (
    .in0(R2), .in1(multiplexer_15_out), .out(MDin), .sel(ex_mem_1_sh_2));
  Multiplexer #(.select(1), .width(32), .disabled("Z"), .enable("false")) multiplexer_15 (
    .in0({ram_1_data_2, R2[15:0]}), .in1({R2[15:0], ram_1_data}), .out(multiplexer_15_out),
    .sel(ex_mem_1_result_2[1]));
  and and_5 (eret, comparator_8_eq, comparator_9_eq);
  Register #(.width(1), .trigger("rising"), .Select("low")) epc_2 (.D(eret));  // open: en, Q, clk, clr
  Comparator #(.width(16), .mode("twosComplement")) comparator_10 (
    .a(16'h23b), .b(\总周期数 ), .eq(comparator_10_eq));  // open: gt, lt
  Comparator #(.width(16), .mode("twosComplement")) comparator_11 (
    .a(\总周期数 ), .b(16'h1), .eq(comparator_11_eq));  // open: gt, lt
  Comparator #(.width(16), .mode("twosComplement")) comparator_12 (
    .a(\总周期数 ), .b(16'h4), .eq(comparator_12_eq));  // open: gt, lt
  Comparator #(.width(16), .mode("twosComplement")) comparator_13 (
    .a(\总周期数 ), .b(16'h7), .eq(comparator_13_eq));  // open: gt, lt
  or or_6 (or_6_out, comparator_10_eq, comparator_11_eq);
  Controlled_Inverter #(.width(1), .negatecontrol("false")) controlled_inverter_1 (
    .in(CLK), .en(or_6_out));  // open: out
  Controlled_Inverter #(.width(1), .negatecontrol("false")) controlled_inverter_2 (
    .in(CLK), .en(comparator_12_eq));  // open: out
  Controlled_Inverter #(.width(1), .negatecontrol("false")) controlled_inverter_3 (
    .in(CLK), .en(comparator_13_eq));  // open: out
  RAM #(.addrWidth(10), .dataWidth(32), .bus("separate"), .Select("high")) ram_1 (
    .addr(ex_mem_1_result_2[11:2]), .din(MDin), .data({ram_1_data_2, ram_1_data}), .str(MemWrite), .clk(CLK),
    .ld(ex_mem_1_memtoreg_2), .clr(Rst));  // open: sel
  Pull_Resistor #(.pull(0)) pull_resistor_2 (.node(IRA));
  Pull_Resistor #(.pull(0)) pull_resistor_3 (.node(IRB));
  Pull_Resistor #(.pull(0)) pull_resistor_4 (.node(IRC));
  not not_10 (not_10_out, Halt);
  or or_7 (or_7_out, Rst, eret, INT1);
  MEM_WB mem_wb_1 (
    .MemToReg(ex_mem_1_memtoreg_2), .RegWrite(ex_mem_1_regwrite_2), .JAL(ex_mem_1_jal_2),
    .RD({ram_1_data_2, ram_1_data}), .WriteReg(ex_mem_1_writereg_2), .PC_4(ex_mem_1_pc_4_2),
    .MemToReg_2(mem_wb_1_memtoreg_2), .RegWrite_2(RegWrite), .JAL_2(mem_wb_1_jal_2), .RD_2(mem_wb_1_rd_2),
    .WriteReg_2(WriteReg), .PC_4_2(mem_wb_1_pc_4_2), .CLK(CLK), .Result(ex_mem_1_result_2),
    .Result_2(mem_wb_1_result_2), .PC(M_PC), .PC_2(WB_PC), .syscall(ex_mem_1_syscall_2), .syscall_2(syscall),
    .RT(MDin), .RT_2(RT), .RS(ex_mem_1_rs_2), .RS_2(RS), .CLR(or_7_out), .en(not_10_out));
  Multiplexer #(.select(1), .width(32), .disabled("Z"), .enable("false")) multiplexer_16 (
    .in0(mem_wb_1_result_2), .in1(mem_wb_1_rd_2), .out(multiplexer_16_out), .sel(mem_wb_1_memtoreg_2));
  // Probe on RS
  Comparator #(.width(32), .mode("twosComplement")) comparator_14 (
    .a(RS), .b(32'ha), .eq(comparator_14_eq));  // open: gt, lt
  // Probe on RT
  not not_11 (not_11_out, comparator_14_eq);
  and and_6 (and_6_out, not_11_out, syscall);
  and and_7 (and_7_out, syscall, comparator_14_eq);
  Multiplexer #(.select(1), .width(32), .disabled("Z"), .enable("false")) multiplexer_17 (
    .in0(multiplexer_16_out), .in1(mem_wb_1_pc_4_2), .out(RDin), .sel(mem_wb_1_jal_2));
  Register #(.width(32), .trigger("rising"), .Select("low")) register_1 (
    .D(RT), .en(and_6_out), .Q(LedData), .clk(CLK), .clr(Rst));
  Register #(.width(1), .trigger("rising"), .Select("low")) register_2 (
    .D(and_7_out), .en(and_7_out), .Q(Halt), .clk(CLK), .clr(Go));
  and and_8 (and_8_out, CLK, not_12_out);
  not not_12 (not_12_out, Halt);
  Counter #(.width(16), .max('hffff), .ongoal("wrap"), .trigger("rising"), .behavior("new")) counter_2 (
    .Q(\总周期数 ), .clk(and_8_out), .clr(Rst));  // open: load, D, count, carry, preset, down
  Counter #(.width(16), .max('hffff), .ongoal("wrap"), .trigger("rising"), .behavior("old")) counter_3 (
    .count(JMP), .Q(\无条件分支数 ), .clk(and_8_out), .clr(Rst));  // open: load, D, carry, preset
  Counter #(.width(16), .max('hffff), .ongoal("wrap"), .trigger("rising"), .behavior("old")) counter_4 (
    .count(BranchTaken), .Q(\条件分支成功数 ), .clk(and_8_out), .clr(Rst));  // open: load, D, carry, preset
  Counter #(.width(16), .max('hffff), .ongoal("wrap"), .trigger("rising"), .behavior("old")) counter_5 (
    .count(stall), .Q(\插入气泡数 ), .clk(and_8_out), .clr(Rst));  // open: load, D, carry, preset

  // Other names for the same wires on the sheet: MEM_PC[31:0] = M_PC

  // Notes on the sheet:
  //   中断源
  //   时空图监测，可删除
  //   BranchTaken
  //   中断等待指示
  //   取指令（IF）
  //   数码管输出
  //   指令存储器
  //   PC+4
  //   contents of rom_1 (hex, n*v repeats v):
  //   201d07d0 20100001 109fc0 139fc3 8021 2012000c 24160008 26100001 3210000f 20080008 20090001 139900
  //   2709825 132020 20020022 c 1094022 1500fff9 22100001 2018000f 2188024 108700 20080008 20090001 139902
  //   2709825 132021 20020022 c 1094022 1500fff9 108702 2c9b022 12c00001 8000c07 4020 1084027 84400
  //   3508ffff 82021 20020022 c 8000c01 afa20000 23bd0004 afa40000 23bd0004 afb00000 23bd0004 afb30000
  //   23bd0004 afb40000 23bd0004 afb50000 23bd0004 afb60000 23bd0004 20160001 20140003 20150001 168020
  //   108100 2149825 132020 20020022 c 1600fffa 295a022 1680fff7 23bdfffc 8fb60000 23bdfffc 8fb50000
  //   23bdfffc 8fb40000 23bdfffc 8fb30000 23bdfffc 8fb00000 23bdfffc 8fa40000 23bdfffc 8fa20000 42000018
  //   afa20000 23bd0004 afa40000 23bd0004 afb00000 23bd0004 afb30000 23bd0004 afb40000 23bd0004 afb50000
  //   23bd0004 afb60000 23bd0004 20160002 20140003 20150001 168020 108100 2149825 132020 20020022 c
  //   1600fffa 295a022 1680fff7 23bdfffc 8fb60000 23bdfffc 8fb50000 23bdfffc 8fb40000 23bdfffc 8fb30000
  //   23bdfffc 8fb00000 23bdfffc 8fa40000 23bdfffc 8fa20000 42000018 afa20000 23bd0004 afa40000 23bd0004
  //   afb00000 23bd0004 afb30000 23bd0004 afb40000 23bd0004 afb50000 23bd0004 afb60000 23bd0004 20160003
  //   20140003 20150001 168020 108100 2149825 132020 20020022 c 1600fffa 295a022 1680fff7 23bdfffc
  //   8fb60000 23bdfffc 8fb50000 23bdfffc 8fb40000 23bdfffc 8fb30000 23bdfffc 8fb00000 23bdfffc 8fa40000
  //   23bdfffc 8fa20000 42000018
  //   指令字
  //   OP
  //   Func
  //   rs
  //   rt
  //   rd
  //   s
  //   JMP
  //   JR
  //   OP
  //   Func
  //   RegDst
  //   译码（ID）
  //   Beq
  //   Bgtz
  //   Bne
  //   MemToReg
  //   MemWrite
  //   AluOP
  //   AluSrcB
  //   RegWrite
  //   JAL
  //   V
  //   Syscall
  //   Sign_ext
  //   控制位
  //   流水调试日志用
  //   暂停节拍，不能为0
  //   戳工具置1进入计数暂停模式，ctrl+k时钟自动运行到对应节拍暂停
  //   ctrl+k关闭时钟连续运行，将控制位置零，进入单步调试模式调试
  //   执行（EX）
  //   可计数暂停的时钟源
  //   为方便自动评测，需要输出流水线各段保存的PC值，注意是PC不是PC+4，另外ID段寄存器写入信息，Mem段内存写入信息也要输出
  //   单级中断测试信号模拟器
  //   访存（MEM）
  //   写回（WB）
endmodule

module \封装正确性测试  (
);

  wire IR1, IR2, IR3, MemW, RegW;
  wire [31:0] EX_PC, ID_PC, IF_PC, IR, LED, MDin, MDinr, MEM_PC, PC, RDin, RDinr, WB_PC;

  \单周期MIPS  \u_单周期mips_1  (
    .IR1(IR1), .IR2(IR2), .IR3(IR3), .RegWrite(RegW), .MemWrite(MemW), .PC(PC), .IR(IR), .RDin(RDin),
    .MDin(MDin), .LedData(LED));
  \气泡流水线  \u_气泡流水线_1  (
    .RegWrite(RegW), .MemWrite(MemW), .IF_PC(IF_PC), .ID_PC(ID_PC), .EX_PC(EX_PC), .M_PC(MEM_PC),
    .WB_PC(WB_PC), .RDin(RDinr), .MDin(MDinr), .LedData(LED));
  \单周期MIPS_单级中断  \u_单周期mips_单级中断_1  (
    .IR1(IR1), .IR2(IR2), .IR3(IR3), .RegWrite(RegW), .MemWrite(MemW), .PC(PC), .IR(IR), .RDin(RDin),
    .MDin(MDin), .LedData(LED));
  \理想流水线  \u_理想流水线_1  (
    .RegWrite(RegW), .MemWrite(MemW), .IF_PC(IF_PC), .ID_PC(ID_PC), .EX_PC(EX_PC), .M_PC(MEM_PC),
    .WB_PC(WB_PC), .RDin(RDinr), .MDin(MDinr), .LedData(LED));
  \重定向流水线  \u_重定向流水线_1  (
    .RegWrite(RegW), .MemWrite(MemW), .IF_PC(IF_PC), .ID_PC(ID_PC), .EX_PC(EX_PC), .M_PC(MEM_PC),
    .WB_PC(WB_PC), .RDin(RDinr), .MDin(MDinr), .LedData(LED));
  \单周期MIPS_多级中断  \u_单周期mips_多级中断_1  (
    .IR1(IR1), .IR2(IR2), .IR3(IR3), .RegWrite(RegW), .MemWrite(MemW), .PC(PC), .IR(IR), .RDin(RDin),
    .MDin(MDin), .LedData(LED));

  // Notes on the sheet:
  //   单周期封装测试
  //   气泡流水封装测试
  //   单周期+单级中断封装测试
  //   请检查上面封装有无位宽不匹配，引脚标签是否和连接的标签相对应，否则无法在educoder平台上正确测试
  //   理想流水封装测试
  //   重定向流水封装测试
  //   单周期+多级中断封装测试
endmodule

module \符号扩展  (
  input  [15:0] in_1,
  output [31:0] out_2
);


  assign out_2 = {{17{in_1[15]}}, in_1[14:0]};
endmodule

module IF_ID_bubble (
  input  CLR,
  input  [31:0] PC,
  input  [31:0] RD_in,
  input  [31:0] PC_4_in,
  input  INT,
  input  PredictJump,
  input  en,
  input  CLK,
  output [31:0] PC_2,
  output [31:0] RD_out,
  output [31:0] PC_4_out,
  output INT_2,
  output PredictJump_2
);

  wire multiplexer_4_out, multiplexer_5_out;
  wire [31:0] multiplexer_1_out, multiplexer_2_out, multiplexer_3_out;

  Pull_Resistor #(.pull(0)) pull_resistor_1 (.node(CLR));
  Multiplexer #(.select(1), .width(32), .disabled("Z"), .enable("false")) multiplexer_1 (
    .in0(PC), .in1({32{1'b0}}), .out(multiplexer_1_out), .sel(CLR));
  Multiplexer #(.select(1), .width(32), .disabled("Z"), .enable("false")) multiplexer_2 (
    .in0(RD_in), .in1({32{1'b0}}), .out(multiplexer_2_out), .sel(CLR));
  Multiplexer #(.select(1), .width(32), .disabled("Z"), .enable("false")) multiplexer_3 (
    .in0(PC_4_in), .in1({32{1'b0}}), .out(multiplexer_3_out), .sel(CLR));
  Multiplexer #(.select(1), .width(1), .disabled("Z"), .enable("false")) multiplexer_4 (
    .in0(INT), .in1(1'b0), .out(multiplexer_4_out), .sel(CLR));
  Multiplexer #(.select(1), .width(1), .disabled("Z"), .enable("false")) multiplexer_5 (
    .in0(PredictJump), .in1(1'b0), .out(multiplexer_5_out), .sel(CLR));
  Pull_Resistor #(.pull(0)) pull_resistor_2 (.node(en));
  Register #(.width(32), .trigger("rising"), .Select("low")) register_1 (
    .D(multiplexer_1_out), .en(en), .Q(PC_2), .clk(CLK));  // open: clr
  Register #(.width(32), .trigger("rising"), .Select("low")) register_2 (
    .D(multiplexer_2_out), .en(en), .Q(RD_out), .clk(CLK));  // open: clr
  Register #(.width(32), .trigger("rising"), .Select("low")) register_3 (
    .D(multiplexer_3_out), .en(en), .Q(PC_4_out), .clk(CLK));  // open: clr
  Register #(.width(1), .trigger("rising"), .Select("low")) register_4 (
    .D(multiplexer_4_out), .en(en), .Q(INT_2), .clk(CLK));  // open: clr
  Register #(.width(1), .trigger("rising"), .Select("low")) register_5 (
    .D(multiplexer_5_out), .en(en), .Q(PredictJump_2), .clk(CLK));  // open: clr
endmodule

module ID_EX_bubble (
  input  en,
  input  JR,
  input  JMP,
  input  Beq,
  input  Bgtz,
  input  Bne,
  input  CLR,
  input  MemToReg,
  input  MemWrite,
  input  [3:0] AluOP,
  input  AluSrcB,
  input  RegWrite,
  input  JAL,
  input  V,
  input  PredictJump,
  input  [31:0] RS,
  input  [31:0] J_PC,
  input  [31:0] RT,
  input  [4:0] WriteReg,
  input  [1:0] RsForward,
  input  [31:0] ext,
  input  [1:0] RtForward,
  input  sh,
  input  [31:0] Sign_ext,
  input  syscall,
  input  [4:0] S,
  input  [31:0] PC,
  input  [31:0] PC_4,
  input  CLK,
  output JR_2,
  output JMP_2,
  output Beq_2,
  output Bgtz_2,
  output Bne_2,
  output MemToReg_2,
  output MemWrite_2,
  output [3:0] AluOP_2,
  output AluSrcB_2,
  output RegWrite_2,
  output JAL_2,
  output V_2,
  output PredictJump_2,
  output [31:0] RS_2,
  output [31:0] J_PC_2,
  output [31:0] RT_2,
  output [4:0] WriteReg_2,
  output [1:0] RsForward_2,
  output [31:0] ext_2,
  output [1:0] RtForward_2,
  output sh_2,
  output [31:0] Sign_ext_2,
  output syscall_2,
  output [4:0] S_2,
  output [31:0] PC_2,
  output [31:0] PC_4_2
);

  wire multiplexer_1_out, multiplexer_2_out, multiplexer_3_out, multiplexer_4_out, multiplexer_5_out,
       multiplexer_6_out, multiplexer_7_out, multiplexer_9_out, multiplexer_10_out, multiplexer_11_out,
       multiplexer_12_out, multiplexer_20_out, multiplexer_24_out, multiplexer_25_out;
  wire [1:0] multiplexer_22_out, multiplexer_23_out;
  wire [3:0] multiplexer_8_out;
  wire [4:0] multiplexer_15_out, multiplexer_18_out;
  wire [31:0] multiplexer_13_out, multiplexer_14_out, multiplexer_16_out, multiplexer_17_out,
       multiplexer_19_out, multiplexer_21_out, multiplexer_26_out;

  Multiplexer #(.select(1), .width(1), .disabled("Z"), .enable("false")) multiplexer_1 (
    .in0(JR), .in1(1'b0), .out(multiplexer_1_out), .sel(CLR));
  Multiplexer #(.select(1), .width(1), .disabled("Z"), .enable("false")) multiplexer_2 (
    .in0(JMP), .in1(1'b0), .out(multiplexer_2_out), .sel(CLR));
  Multiplexer #(.select(1), .width(1), .disabled("Z"), .enable("false")) multiplexer_3 (
    .in0(Beq), .in1(1'b0), .out(multiplexer_3_out), .sel(CLR));
  Multiplexer #(.select(1), .width(1), .disabled("Z"), .enable("false")) multiplexer_4 (
    .in0(Bgtz), .in1(1'b0), .out(multiplexer_4_out), .sel(CLR));
  Multiplexer #(.select(1), .width(1), .disabled("Z"), .enable("false")) multiplexer_5 (
    .in0(Bne), .in1(1'b0), .out(multiplexer_5_out), .sel(CLR));
  Multiplexer #(.select(1), .width(1), .disabled("Z"), .enable("false")) multiplexer_6 (
    .in0(MemToReg), .in1(1'b0), .out(multiplexer_6_out), .sel(CLR));
  Multiplexer #(.select(1), .width(1), .disabled("Z"), .enable("false")) multiplexer_7 (
    .in0(MemWrite), .in1(1'b0), .out(multiplexer_7_out), .sel(CLR));
  Multiplexer #(.select(1), .width(4), .disabled("Z"), .enable("false")) multiplexer_8 (
    .in0(AluOP), .in1(4'b0000), .out(multiplexer_8_out), .sel(CLR));
  Multiplexer #(.select(1), .width(1), .disabled("Z"), .enable("false")) multiplexer_9 (
    .in0(AluSrcB), .in1(1'b0), .out(multiplexer_9_out), .sel(CLR));
  Multiplexer #(.select(1), .width(1), .disabled("Z"), .enable("false")) multiplexer_10 (
    .in0(RegWrite), .in1(1'b0), .out(multiplexer_10_out), .sel(CLR));
  Multiplexer #(.select(1), .width(1), .disabled("Z"), .enable("false")) multiplexer_11 (
    .in0(JAL), .in1(1'b0), .out(multiplexer_11_out), .sel(CLR));
  Multiplexer #(.select(1), .width(1), .disabled("Z"), .enable("false")) multiplexer_12 (
    .in0(V), .in1(1'b0), .out(multiplexer_12_out), .sel(CLR));
  Multiplexer #(.select(1), .width(32), .disabled("Z"), .enable("false")) multiplexer_13 (
    .in0(RS), .in1({32{1'b0}}), .out(multiplexer_13_out), .sel(CLR));
  Multiplexer #(.select(1), .width(32), .disabled("Z"), .enable("false")) multiplexer_14 (
    .in0(RT), .in1({32{1'b0}}), .out(multiplexer_14_out), .sel(CLR));
  Multiplexer #(.select(1), .width(5), .disabled("Z"), .enable("false")) multiplexer_15 (
    .in0(WriteReg), .in1({5{1'b0}}), .out(multiplexer_15_out), .sel(CLR));
  Multiplexer #(.select(1), .width(32), .disabled("Z"), .enable("false")) multiplexer_16 (
    .in0(ext), .in1({32{1'b0}}), .out(multiplexer_16_out), .sel(CLR));
  Multiplexer #(.select(1), .width(32), .disabled("Z"), .enable("false")) multiplexer_17 (
    .in0(Sign_ext), .in1({32{1'b0}}), .out(multiplexer_17_out), .sel(CLR));
  Multiplexer #(.select(1), .width(5), .disabled("Z"), .enable("false")) multiplexer_18 (
    .in0(S), .in1({5{1'b0}}), .out(multiplexer_18_out), .sel(CLR));
  Multiplexer #(.select(1), .width(32), .disabled("Z"), .enable("false")) multiplexer_19 (
    .in0(PC_4), .in1({32{1'b0}}), .out(multiplexer_19_out), .sel(CLR));
  Register #(.width(1), .trigger("rising"), .Select("low")) register_1 (
    .D(multiplexer_1_out), .en(en), .Q(JR_2), .clk(CLK));  // open: clr
  Register #(.width(1), .trigger("rising"), .Select("low")) register_2 (
    .D(multiplexer_2_out), .en(en), .Q(JMP_2), .clk(CLK));  // open: clr
  Register #(.width(1), .trigger("rising"), .Select("low")) register_3 (
    .D(multiplexer_3_out), .en(en), .Q(Beq_2), .clk(CLK));  // open: clr
  Register #(.width(1), .trigger("rising"), .Select("low")) register_4 (
    .D(multiplexer_4_out), .en(en), .Q(Bgtz_2), .clk(CLK));  // open: clr
  Register #(.width(1), .trigger("rising"), .Select("low")) register_5 (
    .D(multiplexer_5_out), .en(en), .Q(Bne_2), .clk(CLK));  // open: clr
  Register #(.width(1), .trigger("rising"), .Select("low")) register_6 (
    .D(multiplexer_6_out), .en(en), .Q(MemToReg_2), .clk(CLK));  // open: clr
  Register #(.width(1), .trigger("rising"), .Select("low")) register_7 (
    .D(multiplexer_7_out), .en(en), .Q(MemWrite_2), .clk(CLK));  // open: clr
  Register #(.width(4), .trigger("rising"), .Select("low")) register_8 (
    .D(multiplexer_8_out), .en(en), .Q(AluOP_2), .clk(CLK));  // open: clr
  Register #(.width(1), .trigger("rising"), .Select("low")) register_9 (
    .D(multiplexer_9_out), .en(en), .Q(AluSrcB_2), .clk(CLK));  // open: clr
  Register #(.width(1), .trigger("rising"), .Select("low")) register_10 (
    .D(multiplexer_10_out), .en(en), .Q(RegWrite_2), .clk(CLK));  // open: clr
  Register #(.width(1), .trigger("rising"), .Select("low")) register_11 (
    .D(multiplexer_11_out), .en(en), .Q(JAL_2), .clk(CLK));  // open: clr
  Register #(.width(1), .trigger("rising"), .Select("low")) register_12 (
    .D(multiplexer_12_out), .en(en), .Q(V_2), .clk(CLK));  // open: clr
  Register #(.width(32), .trigger("rising"), .Select("low")) register_13 (
    .D(multiplexer_13_out), .en(en), .Q(RS_2), .clk(CLK));  // open: clr
  Register #(.width(32), .trigger("rising"), .Select("low")) register_14 (
    .D(multiplexer_14_out), .en(en), .Q(RT_2), .clk(CLK));  // open: clr
  Register #(.width(5), .trigger("rising"), .Select("low")) register_15 (
    .D(multiplexer_15_out), .en(en), .Q(WriteReg_2), .clk(CLK));  // open: clr
  Register #(.width(32), .trigger("rising"), .Select("low")) register_16 (
    .D(multiplexer_16_out), .en(en), .Q(ext_2), .clk(CLK));  // open: clr
  Register #(.width(32), .trigger("rising"), .Select("low")) register_17 (
    .D(multiplexer_17_out), .en(en), .Q(Sign_ext_2), .clk(CLK));  // open: clr
  Register #(.width(5), .trigger("rising"), .Select("low")) register_18 (
    .D(multiplexer_18_out), .en(en), .Q(S_2), .clk(CLK));  // open: clr
  Register #(.width(32), .trigger("rising"), .Select("low")) register_19 (
    .D(multiplexer_19_out), .en(en), .Q(PC_4_2), .clk(CLK));  // open: clr
  Pull_Resistor #(.pull(0)) pull_resistor_1 (.node(CLR));
  Multiplexer #(.select(1), .width(1), .disabled("Z"), .enable("false")) multiplexer_20 (
    .in0(PredictJump), .in1(1'b0), .out(multiplexer_20_out), .sel(CLR));
  Multiplexer #(.select(1), .width(32), .disabled("Z"), .enable("false")) multiplexer_21 (
    .in0(J_PC), .in1({32{1'b0}}), .out(multiplexer_21_out), .sel(CLR));
  Multiplexer #(.select(1), .width(2), .disabled("Z"), .enable("false")) multiplexer_22 (
    .in0(RsForward), .in1(2'b00), .out(multiplexer_22_out), .sel(CLR));
  Multiplexer #(.select(1), .width(2), .disabled("Z"), .enable("false")) multiplexer_23 (
    .in0(RtForward), .in1(2'b00), .out(multiplexer_23_out), .sel(CLR));
  Multiplexer #(.select(1), .width(1), .disabled("Z"), .enable("false")) multiplexer_24 (
    .in0(sh), .in1(1'b0), .out(multiplexer_24_out), .sel(CLR));
  Multiplexer #(.select(1), .width(1), .disabled("Z"), .enable("false")) multiplexer_25 (
    .in0(syscall), .in1(1'b0), .out(multiplexer_25_out), .sel(CLR));
  Multiplexer #(.select(1), .width(32), .disabled("Z"), .enable("false")) multiplexer_26 (
    .in0(PC), .in1({32{1'b0}}), .out(multiplexer_26_out), .sel(CLR));
  Register #(.width(1), .trigger("rising"), .Select("low")) register_20 (
    .D(multiplexer_20_out), .en(en), .Q(PredictJump_2), .clk(CLK));  // open: clr
  Register #(.width(32), .trigger("rising"), .Select("low")) register_21 (
    .D(multiplexer_21_out), .en(en), .Q(J_PC_2), .clk(CLK));  // open: clr
  Register #(.width(2), .trigger("rising"), .Select("low")) register_22 (
    .D(multiplexer_22_out), .en(en), .Q(RsForward_2), .clk(CLK));  // open: clr
  Register #(.width(2), .trigger("rising"), .Select("low")) register_23 (
    .D(multiplexer_23_out), .en(en), .Q(RtForward_2), .clk(CLK));  // open: clr
  Register #(.width(1), .trigger("rising"), .Select("low")) register_24 (
    .D(multiplexer_24_out), .en(en), .Q(sh_2), .clk(CLK));  // open: clr
  Register #(.width(1), .trigger("rising"), .Select("low")) register_25 (
    .D(multiplexer_25_out), .en(en), .Q(syscall_2), .clk(CLK));  // open: clr
  Register #(.width(32), .trigger("rising"), .Select("low")) register_26 (
    .D(multiplexer_26_out), .en(en), .Q(PC_2), .clk(CLK));  // open: clr
endmodule

module IF_ID (
  input  [31:0] PC,
  input  [31:0] RD_in,
  input  [31:0] PC_4_in,
  input  CLK,
  output [31:0] PC_2,
  output [31:0] RD_out,
  output [31:0] PC_4_out
);

  Register #(.width(32), .trigger("rising"), .Select("low")) register_1 (.D(PC), .Q(PC_2), .clk(CLK));  // open: en, clr
  Register #(.width(32), .trigger("rising"), .Select("low")) register_2 (
    .D(RD_in), .Q(RD_out), .clk(CLK));  // open: en, clr
  Register #(.width(32), .trigger("rising"), .Select("low")) register_3 (
    .D(PC_4_in), .Q(PC_4_out), .clk(CLK));  // open: en, clr
endmodule

module ID_EX (
  input  Beq,
  input  Bgtz,
  input  Bne,
  input  MemToReg,
  input  MemWrite,
  input  [3:0] AluOP,
  input  AluSrcB,
  input  RegWrite,
  input  JAL,
  input  V,
  input  [31:0] RS,
  input  [31:0] RT,
  input  [4:0] WriteReg,
  input  [31:0] ext,
  input  sh,
  input  [31:0] Sign_ext,
  input  syscall,
  input  [4:0] S,
  input  [31:0] PC,
  input  [31:0] PC_4,
  input  CLK,
  output Beq_2,
  output Bgtz_2,
  output Bne_2,
  output MemToReg_2,
  output MemWrite_2,
  output [3:0] AluOP_2,
  output AluSrcB_2,
  output RegWrite_2,
  output JAL_2,
  output V_2,
  output [31:0] RS_2,
  output [31:0] RT_2,
  output [4:0] WriteReg_2,
  output [31:0] ext_2,
  output sh_2,
  output [31:0] Sign_ext_2,
  output syscall_2,
  output [4:0] S_2,
  output [31:0] PC_2,
  output [31:0] PC_4_2
);

  Register #(.width(1), .trigger("rising"), .Select("low")) register_1 (
    .D(Beq), .Q(Beq_2), .clk(CLK));  // open: en, clr
  Register #(.width(1), .trigger("rising"), .Select("low")) register_2 (
    .D(Bgtz), .Q(Bgtz_2), .clk(CLK));  // open: en, clr
  Register #(.width(1), .trigger("rising"), .Select("low")) register_3 (
    .D(Bne), .Q(Bne_2), .clk(CLK));  // open: en, clr
  Register #(.width(1), .trigger("rising"), .Select("low")) register_4 (
    .D(MemToReg), .Q(MemToReg_2), .clk(CLK));  // open: en, clr
  Register #(.width(1), .trigger("rising"), .Select("low")) register_5 (
    .D(MemWrite), .Q(MemWrite_2), .clk(CLK));  // open: en, clr
  Register #(.width(4), .trigger("rising"), .Select("low")) register_6 (
    .D(AluOP), .Q(AluOP_2), .clk(CLK));  // open: en, clr
  Register #(.width(1), .trigger("rising"), .Select("low")) register_7 (
    .D(AluSrcB), .Q(AluSrcB_2), .clk(CLK));  // open: en, clr
  Register #(.width(1), .trigger("rising"), .Select("low")) register_8 (
    .D(RegWrite), .Q(RegWrite_2), .clk(CLK));  // open: en, clr
  Register #(.width(1), .trigger("rising"), .Select("low")) register_9 (
    .D(JAL), .Q(JAL_2), .clk(CLK));  // open: en, clr
  Register #(.width(1), .trigger("rising"), .Select("low")) register_10 (.D(V), .Q(V_2), .clk(CLK));  // open: en, clr
  Register #(.width(32), .trigger("rising"), .Select("low")) register_11 (
    .D(RS), .Q(RS_2), .clk(CLK));  // open: en, clr
  Register #(.width(32), .trigger("rising"), .Select("low")) register_12 (
    .D(RT), .Q(RT_2), .clk(CLK));  // open: en, clr
  Register #(.width(5), .trigger("rising"), .Select("low")) register_13 (
    .D(WriteReg), .Q(WriteReg_2), .clk(CLK));  // open: en, clr
  Register #(.width(32), .trigger("rising"), .Select("low")) register_14 (
    .D(ext), .Q(ext_2), .clk(CLK));  // open: en, clr
  Register #(.width(32), .trigger("rising"), .Select("low")) register_15 (
    .D(Sign_ext), .Q(Sign_ext_2), .clk(CLK));  // open: en, clr
  Register #(.width(5), .trigger("rising"), .Select("low")) register_16 (.D(S), .Q(S_2), .clk(CLK));  // open: en, clr
  Register #(.width(32), .trigger("rising"), .Select("low")) register_17 (
    .D(PC_4), .Q(PC_4_2), .clk(CLK));  // open: en, clr
  Register #(.width(1), .trigger("rising"), .Select("low")) register_18 (.D(sh), .Q(sh_2), .clk(CLK));  // open: en, clr
  Register #(.width(1), .trigger("rising"), .Select("low")) register_19 (
    .D(syscall), .Q(syscall_2), .clk(CLK));  // open: en, clr
  Register #(.width(32), .trigger("rising"), .Select("low")) register_20 (
    .D(PC), .Q(PC_2), .clk(CLK));  // open: en, clr
endmodule

module EX_MEM (
  input  en,
  input  syscall,
  input  CLR,
  input  [31:0] PC,
  input  MemToReg,
  input  MemWrite,
  input  RegWrite,
  input  JAL,
  input  [31:0] Result,
  input  [4:0] WriteReg,
  input  [31:0] PC_4,
  input  sh,
  input  [31:0] RT,
  input  [31:0] RS,
  input  CLK,
  output syscall_2,
  output [31:0] PC_2,
  output MemToReg_2,
  output MemWrite_2,
  output RegWrite_2,
  output JAL_2,
  output [31:0] Result_2,
  output [4:0] WriteReg_2,
  output [31:0] PC_4_2,
  output sh_2,
  output [31:0] RT_2,
  output [31:0] RS_2
);

  wire multiplexer_1_out, multiplexer_3_out, multiplexer_4_out, multiplexer_5_out, multiplexer_6_out,
       multiplexer_11_out;
  wire [4:0] multiplexer_8_out;
  wire [31:0] multiplexer_2_out, multiplexer_7_out, multiplexer_9_out, multiplexer_10_out, multiplexer_12_out;

  Multiplexer #(.select(1), .width(1), .disabled("Z"), .enable("false")) multiplexer_1 (
    .in0(syscall), .in1(1'b0), .out(multiplexer_1_out), .sel(CLR));
  Multiplexer #(.select(1), .width(32), .disabled("Z"), .enable("false")) multiplexer_2 (
    .in0(PC), .in1({32{1'b0}}), .out(multiplexer_2_out), .sel(CLR));
  Multiplexer #(.select(1), .width(1), .disabled("Z"), .enable("false")) multiplexer_3 (
    .in0(MemToReg), .in1(1'b0), .out(multiplexer_3_out), .sel(CLR));
  Multiplexer #(.select(1), .width(1), .disabled("Z"), .enable("false")) multiplexer_4 (
    .in0(MemWrite), .in1(1'b0), .out(multiplexer_4_out), .sel(CLR));
  Multiplexer #(.select(1), .width(1), .disabled("Z"), .enable("false")) multiplexer_5 (
    .in0(RegWrite), .in1(1'b0), .out(multiplexer_5_out), .sel(CLR));
  Multiplexer #(.select(1), .width(1), .disabled("Z"), .enable("false")) multiplexer_6 (
    .in0(JAL), .in1(1'b0), .out(multiplexer_6_out), .sel(CLR));
  Multiplexer #(.select(1), .width(32), .disabled("Z"), .enable("false")) multiplexer_7 (
    .in0(Result), .in1({32{1'b0}}), .out(multiplexer_7_out), .sel(CLR));
  Multiplexer #(.select(1), .width(5), .disabled("Z"), .enable("false")) multiplexer_8 (
    .in0(WriteReg), .in1({5{1'b0}}), .out(multiplexer_8_out), .sel(CLR));
  Multiplexer #(.select(1), .width(32), .disabled("Z"), .enable("false")) multiplexer_9 (
    .in0(PC_4), .in1({32{1'b0}}), .out(multiplexer_9_out), .sel(CLR));
  Multiplexer #(.select(1), .width(32), .disabled("Z"), .enable("false")) multiplexer_10 (
    .in0(RT), .in1({32{1'b0}}), .out(multiplexer_10_out), .sel(CLR));
  Register #(.width(1), .trigger("rising"), .Select("low")) register_1 (
    .D(multiplexer_1_out), .en(en), .Q(syscall_2), .clk(CLK));  // open: clr
  Register #(.width(32), .trigger("rising"), .Select("low")) register_2 (
    .D(multiplexer_2_out), .en(en), .Q(PC_2), .clk(CLK));  // open: clr
  Register #(.width(1), .trigger("rising"), .Select("low")) register_3 (
    .D(multiplexer_3_out), .en(en), .Q(MemToReg_2), .clk(CLK));  // open: clr
  Register #(.width(1), .trigger("rising"), .Select("low")) register_4 (
    .D(multiplexer_4_out), .en(en), .Q(MemWrite_2), .clk(CLK));  // open: clr
  Register #(.width(1), .trigger("rising"), .Select("low")) register_5 (
    .D(multiplexer_5_out), .en(en), .Q(RegWrite_2), .clk(CLK));  // open: clr
  Register #(.width(1), .trigger("rising"), .Select("low")) register_6 (
    .D(multiplexer_6_out), .en(en), .Q(JAL_2), .clk(CLK));  // open: clr
  Register #(.width(32), .trigger("rising"), .Select("low")) register_7 (
    .D(multiplexer_7_out), .en(en), .Q(Result_2), .clk(CLK));  // open: clr
  Register #(.width(5), .trigger("rising"), .Select("low")) register_8 (
    .D(multiplexer_8_out), .en(en), .Q(WriteReg_2), .clk(CLK));  // open: clr
  Register #(.width(32), .trigger("rising"), .Select("low")) register_9 (
    .D(multiplexer_9_out), .en(en), .Q(PC_4_2), .clk(CLK));  // open: clr
  Register #(.width(32), .trigger("rising"), .Select("low")) register_10 (
    .D(multiplexer_10_out), .en(en), .Q(RT_2), .clk(CLK));  // open: clr
  Pull_Resistor #(.pull(0)) pull_resistor_1 (.node(CLR));
  Multiplexer #(.select(1), .width(1), .disabled("Z"), .enable("false")) multiplexer_11 (
    .in0(sh), .in1(1'b0), .out(multiplexer_11_out), .sel(CLR));
  Multiplexer #(.select(1), .width(32), .disabled("Z"), .enable("false")) multiplexer_12 (
    .in0(RS), .in1({32{1'b0}}), .out(multiplexer_12_out), .sel(CLR));
  Register #(.width(1), .trigger("rising"), .Select("low")) register_11 (
    .D(multiplexer_11_out), .en(en), .Q(sh_2), .clk(CLK));  // open: clr
  Register #(.width(32), .trigger("rising"), .Select("low")) register_12 (
    .D(multiplexer_12_out), .en(en), .Q(RS_2), .clk(CLK));  // open: clr
endmodule

module MEM_WB (
  input  en,
  input  syscall,
  input  CLR,
  input  [31:0] PC,
  input  MemToReg,
  input  RegWrite,
  input  JAL,
  input  [31:0] RD,
  input  [4:0] WriteReg,
  input  [31:0] RS,
  input  [31:0] PC_4,
  input  [31:0] RT,
  input  [31:0] Result,
  input  CLK,
  output syscall_2,
  output [31:0] PC_2,
  output MemToReg_2,
  output RegWrite_2,
  output JAL_2,
  output [31:0] RD_2,
  output [4:0] WriteReg_2,
  output [31:0] RS_2,
  output [31:0] PC_4_2,
  output [31:0] RT_2,
  output [31:0] Result_2
);

  wire multiplexer_1_out, multiplexer_3_out, multiplexer_4_out, multiplexer_5_out;
  wire [4:0] multiplexer_7_out;
  wire [31:0] multiplexer_2_out, multiplexer_6_out, multiplexer_8_out, multiplexer_9_out, multiplexer_10_out,
       multiplexer_11_out;

  Multiplexer #(.select(1), .width(1), .disabled("Z"), .enable("false")) multiplexer_1 (
    .in0(syscall), .in1(1'b0), .out(multiplexer_1_out), .sel(CLR));
  Multiplexer #(.select(1), .width(32), .disabled("Z"), .enable("false")) multiplexer_2 (
    .in0(PC), .in1({32{1'b0}}), .out(multiplexer_2_out), .sel(CLR));
  Multiplexer #(.select(1), .width(1), .disabled("Z"), .enable("false")) multiplexer_3 (
    .in0(MemToReg), .in1(1'b0), .out(multiplexer_3_out), .sel(CLR));
  Multiplexer #(.select(1), .width(1), .disabled("Z"), .enable("false")) multiplexer_4 (
    .in0(RegWrite), .in1(1'b0), .out(multiplexer_4_out), .sel(CLR));
  Multiplexer #(.select(1), .width(1), .disabled("Z"), .enable("false")) multiplexer_5 (
    .in0(JAL), .in1(1'b0), .out(multiplexer_5_out), .sel(CLR));
  Multiplexer #(.select(1), .width(32), .disabled("Z"), .enable("false")) multiplexer_6 (
    .in0(RD), .in1({32{1'b0}}), .out(multiplexer_6_out), .sel(CLR));
  Multiplexer #(.select(1), .width(5), .disabled("Z"), .enable("false")) multiplexer_7 (
    .in0(WriteReg), .in1({5{1'b0}}), .out(multiplexer_7_out), .sel(CLR));
  Multiplexer #(.select(1), .width(32), .disabled("Z"), .enable("false")) multiplexer_8 (
    .in0(PC_4), .in1({32{1'b0}}), .out(multiplexer_8_out), .sel(CLR));
  Multiplexer #(.select(1), .width(32), .disabled("Z"), .enable("false")) multiplexer_9 (
    .in0(Result), .in1({32{1'b0}}), .out(multiplexer_9_out), .sel(CLR));
  Register #(.width(1), .trigger("rising"), .Select("low")) register_1 (
    .D(multiplexer_1_out), .en(en), .Q(syscall_2), .clk(CLK));  // open: clr
  Register #(.width(32), .trigger("rising"), .Select("low")) register_2 (
    .D(multiplexer_2_out), .en(en), .Q(PC_2), .clk(CLK));  // open: clr
  Register #(.width(1), .trigger("rising"), .Select("low")) register_3 (
    .D(multiplexer_3_out), .en(en), .Q(MemToReg_2), .clk(CLK));  // open: clr
  Register #(.width(1), .trigger("rising"), .Select("low")) register_4 (
    .D(multiplexer_4_out), .en(en), .Q(RegWrite_2), .clk(CLK));  // open: clr
  Register #(.width(1), .trigger("rising"), .Select("low")) register_5 (
    .D(multiplexer_5_out), .en(en), .Q(JAL_2), .clk(CLK));  // open: clr
  Register #(.width(32), .trigger("rising"), .Select("low")) register_6 (
    .D(multiplexer_6_out), .en(en), .Q(RD_2), .clk(CLK));  // open: clr
  Register #(.width(5), .trigger("rising"), .Select("low")) register_7 (
    .D(multiplexer_7_out), .en(en), .Q(WriteReg_2), .clk(CLK));  // open: clr
  Register #(.width(32), .trigger("rising"), .Select("low")) register_8 (
    .D(multiplexer_8_out), .en(en), .Q(PC_4_2), .clk(CLK));  // open: clr
  Register #(.width(32), .trigger("rising"), .Select("low")) register_9 (
    .D(multiplexer_9_out), .en(en), .Q(Result_2), .clk(CLK));  // open: clr
  Pull_Resistor #(.pull(0)) pull_resistor_1 (.node(CLR));
  Register #(.width(32), .trigger("rising"), .Select("low")) register_10 (
    .D(multiplexer_10_out), .en(en), .Q(RS_2), .clk(CLK));  // open: clr
  Multiplexer #(.select(1), .width(32), .disabled("Z"), .enable("false")) multiplexer_10 (
    .in0(RS), .in1({32{1'b0}}), .out(multiplexer_10_out), .sel(CLR));
  Multiplexer #(.select(1), .width(32), .disabled("Z"), .enable("false")) multiplexer_11 (
    .in0(RT), .in1({32{1'b0}}), .out(multiplexer_11_out), .sel(CLR));
  Register #(.width(32), .trigger("rising"), .Select("low")) register_11 (
    .D(multiplexer_11_out), .en(en), .Q(RT_2), .clk(CLK));  // open: clr
endmodule

module \气泡流水线相关处理逻辑  (
  input  EX_RegWrite,
  input  [5:0] OP,
  input  [5:0] func,
  input  MEM_RegWrite,
  input  [4:0] R1,
  input  [4:0] EX_WriteReg,
  input  Branch,
  input  [4:0] R2,
  input  [4:0] MEM_WriteReg,
  output Flush,
  output Stall
);

  wire and_2_out, and_3_out, and_4_out, and_5_out, DataHazzard, not_1_out, not_2_out, not_3_out, rs__0,
       rs__EX_WR, rs__MEM_WR, rt__0, rt__EX_WR, rt__MEM_WR, rused_1_rsused, rused_1_rtused;

  or or_1 (Flush, Branch, DataHazzard);
  and and_1 (Stall, DataHazzard, not_1_out);
  not not_1 (not_1_out, Branch);
  RUsed rused_1 (
    .OP0(OP[0]), .OP1(OP[1]), .OP2(OP[2]), .OP3(OP[3]), .OP4(OP[4]), .OP5(OP[5]), .F0(func[0]), .F1(func[1]),
    .F2(func[2]), .F3(func[3]), .F4(func[4]), .F5(func[5]), .RsUsed(rused_1_rsused), .RtUsed(rused_1_rtused));
  not not_2 (not_2_out, rs__0);
  not not_3 (not_3_out, rt__0);
  and and_2 (and_2_out, rused_1_rsused, not_2_out, EX_RegWrite, rs__EX_WR);
  and and_3 (and_3_out, rused_1_rsused, not_2_out, MEM_RegWrite, rs__MEM_WR);
  and and_4 (and_4_out, rused_1_rtused, not_3_out, EX_RegWrite, rt__EX_WR);
  and and_5 (and_5_out, rused_1_rtused, not_3_out, MEM_RegWrite, rt__MEM_WR);
  or or_2 (DataHazzard, and_2_out, and_3_out, and_4_out, and_5_out);
  Comparator #(.width(5), .mode("twosComplement")) comparator_1 (.a(R1), .b({5{1'b0}}), .eq(rs__0));  // open: gt, lt
  Comparator #(.width(5), .mode("twosComplement")) comparator_2 (
    .a(R1), .b(EX_WriteReg), .eq(rs__EX_WR));  // open: gt, lt
  Comparator #(.width(5), .mode("twosComplement")) comparator_3 (
    .a(R1), .b(MEM_WriteReg), .eq(rs__MEM_WR));  // open: gt, lt
  Comparator #(.width(5), .mode("twosComplement")) comparator_4 (.a(R2), .b({5{1'b0}}), .eq(rt__0));  // open: gt, lt
  Comparator #(.width(5), .mode("twosComplement")) comparator_5 (
    .a(R2), .b(EX_WriteReg), .eq(rt__EX_WR));  // open: gt, lt
  Comparator #(.width(5), .mode("twosComplement")) comparator_6 (
    .a(R2), .b(MEM_WriteReg), .eq(rt__MEM_WR));  // open: gt, lt

  // Notes on the sheet:
  //   OP
endmodule

module \重定向流水线相关处理逻辑  (
  input  [4:0] R1,
  input  EX_MemRead,
  input  [4:0] EX_WriteReg,
  input  [5:0] OP,
  input  [5:0] func,
  input  [4:0] R2,
  input  [4:0] MEM_WriteReg,
  input  Branch,
  input  EX_RegWrite,
  input  MEM_RegWrite,
  output Flush,
  output [1:0] RsFoward,
  output Stall,
  output [1:0] RtFoward
);

  wire and_1_out, and_2_out, and_3_out, and_4_out, and_5_out, and_6_out, LoadUse, not_1_out, not_2_out,
       not_3_out, not_4_out, not_5_out, rs__0, rs__EX_WR, rs__MEM_WR, RsUsed, rt__0, rt__EX_WR, rt__MEM_WR,
       RtUsed;
  wire [1:0] multiplexer_1_out, multiplexer_2_out;

  RUsed rused_1 (
    .OP0(OP[0]), .OP1(OP[1]), .OP2(OP[2]), .OP3(OP[3]), .OP4(OP[4]), .OP5(OP[5]), .F0(func[0]), .F1(func[1]),
    .F2(func[2]), .F3(func[3]), .F4(func[4]), .F5(func[5]), .RsUsed(RsUsed), .RtUsed(RtUsed));
  not not_1 (not_1_out, rs__0);
  not not_2 (not_2_out, rt__0);
  and and_1 (and_1_out, RsUsed, not_1_out, EX_RegWrite, rs__EX_WR);
  and and_2 (and_2_out, RsUsed, not_1_out, MEM_RegWrite, rs__MEM_WR);
  and and_3 (and_3_out, RtUsed, not_2_out, EX_RegWrite, rt__EX_WR);
  and and_4 (and_4_out, RtUsed, not_2_out, MEM_RegWrite, rt__MEM_WR);
  not not_3 (not_3_out, rs__0);
  not not_4 (not_4_out, rt__0);
  Multiplexer #(.select(1), .width(2), .disabled("Z"), .enable("false")) multiplexer_1 (
    .in0(2'b00), .in1(2'b01), .out(multiplexer_1_out), .sel(and_2_out));
  Multiplexer #(.select(1), .width(2), .disabled("Z"), .enable("false")) multiplexer_2 (
    .in0(2'b00), .in1(2'b01), .out(multiplexer_2_out), .sel(and_4_out));
  and and_5 (and_5_out, RsUsed, not_3_out, EX_MemRead, rs__EX_WR);
  and and_6 (and_6_out, RtUsed, not_4_out, EX_MemRead, rt__EX_WR);
  or or_1 (LoadUse, and_5_out, and_6_out);
  Multiplexer #(.select(1), .width(2), .disabled("Z"), .enable("false")) multiplexer_3 (
    .in0(multiplexer_1_out), .in1(2'b10), .out(RsFoward), .sel(and_1_out));
  Multiplexer #(.select(1), .width(2), .disabled("Z"), .enable("false")) multiplexer_4 (
    .in0(multiplexer_2_out), .in1(2'b10), .out(RtFoward), .sel(and_3_out));
  Comparator #(.width(5), .mode("twosComplement")) comparator_1 (.a(R1), .b({5{1'b0}}), .eq(rs__0));  // open: gt, lt
  Comparator #(.width(5), .mode("twosComplement")) comparator_2 (
    .a(R1), .b(EX_WriteReg), .eq(rs__EX_WR));  // open: gt, lt
  Comparator #(.width(5), .mode("twosComplement")) comparator_3 (
    .a(R1), .b(MEM_WriteReg), .eq(rs__MEM_WR));  // open: gt, lt
  Comparator #(.width(5), .mode("twosComplement")) comparator_4 (.a(R2), .b({5{1'b0}}), .eq(rt__0));  // open: gt, lt
  Comparator #(.width(5), .mode("twosComplement")) comparator_5 (
    .a(R2), .b(EX_WriteReg), .eq(rt__EX_WR));  // open: gt, lt
  Comparator #(.width(5), .mode("twosComplement")) comparator_6 (
    .a(R2), .b(MEM_WriteReg), .eq(rt__MEM_WR));  // open: gt, lt
  or or_2 (Flush, Branch, LoadUse);
  and and_7 (Stall, LoadUse, not_5_out);
  not not_5 (not_5_out, Branch);

  // Notes on the sheet:
  //   OP
endmodule
module RUsed (
  input  OP0,
  input  OP1,
  input  OP2,
  input  OP3,
  input  OP4,
  input  OP5,
  input  F0,
  input  F1,
  input  F2,
  input  F3,
  input  F4,
  input  F5,
  output RsUsed,
  output RtUsed
);

  wire and_1_out, and_2_out, and_3_out, and_4_out, and_5_out, and_6_out, and_7_out, and_8_out, and_9_out,
       and_10_out, and_11_out, and_12_out, and_13_out, and_14_out, and_15_out, and_16_out, and_17_out,
       and_18_out, and_19_out, and_20_out, and_21_out, and_22_out, and_23_out, and_24_out, and_25_out,
       and_26_out, and_27_out, and_28_out, and_29_out, and_30_out, and_31_out, and_32_out, and_33_out,
       and_34_out, and_35_out, and_36_out, and_37_out, and_38_out, and_39_out, and_40_out, and_41_out,
       not_1_out, not_2_out, not_3_out, not_4_out, not_5_out, not_6_out, not_7_out, not_8_out, not_9_out,
       not_10_out, not_11_out, not_12_out, not_13_out, not_14_out, not_15_out, not_16_out, not_17_out,
       not_18_out, not_19_out, not_20_out, not_21_out, not_22_out, not_23_out, not_24_out, not_25_out,
       not_26_out, not_27_out, not_28_out, not_29_out, not_30_out, not_31_out, not_32_out, not_33_out,
       not_34_out, not_35_out, not_36_out, not_37_out, not_38_out, not_39_out, not_40_out, not_41_out,
       not_42_out, not_43_out, not_44_out, not_45_out, not_46_out, not_47_out, not_48_out, not_49_out,
       not_50_out, not_51_out, not_52_out, not_53_out, not_54_out, not_55_out, not_56_out, not_57_out,
       not_58_out, not_59_out, not_60_out, not_61_out, not_62_out, not_63_out, not_64_out, not_65_out,
       not_66_out, not_67_out, not_68_out, not_69_out, not_70_out, not_71_out, not_72_out, not_73_out,
       not_74_out, not_75_out, not_76_out, not_77_out, not_78_out, not_79_out, not_80_out, not_81_out,
       not_82_out, not_83_out, not_84_out, not_85_out, not_86_out, not_87_out, not_88_out, not_89_out,
       not_90_out, not_91_out, not_92_out, not_93_out, not_94_out, not_95_out, not_96_out, not_97_out,
       not_98_out, not_99_out, not_100_out, not_101_out, not_102_out, not_103_out, not_104_out, not_105_out,
       not_106_out, not_107_out, not_108_out, not_109_out, not_110_out, not_111_out, not_112_out,
       not_113_out, not_114_out, not_115_out, not_116_out, not_117_out, not_118_out, not_119_out,
       not_120_out, not_121_out, not_122_out, not_123_out, not_124_out, not_125_out, not_126_out,
       not_127_out, not_128_out, not_129_out, not_130_out, not_131_out, not_132_out, not_133_out,
       not_134_out, not_135_out, not_136_out, not_137_out, not_138_out, not_139_out, not_140_out,
       not_141_out, not_142_out, not_143_out, not_144_out, not_145_out, not_146_out, not_147_out,
       not_148_out, not_149_out, not_150_out, not_151_out, not_152_out, not_153_out, not_154_out,
       not_155_out, not_156_out, not_157_out, not_158_out, not_159_out, not_160_out, not_161_out,
       not_162_out, not_163_out, not_164_out, not_165_out, not_166_out, not_167_out, not_168_out,
       not_169_out, not_170_out, not_171_out, not_172_out, not_173_out, not_174_out, not_175_out,
       not_176_out, not_177_out, not_178_out, not_179_out, not_180_out, not_181_out, not_182_out,
       not_183_out, not_184_out, not_185_out, not_186_out, not_187_out, not_188_out, not_189_out,
       not_190_out, not_191_out, not_192_out, not_193_out, not_194_out, not_195_out, not_196_out,
       not_197_out, not_198_out, not_199_out, not_200_out, not_201_out, not_202_out, not_203_out,
       not_204_out, not_205_out, not_206_out, not_207_out, not_208_out, not_209_out, not_210_out,
       not_211_out, not_212_out, not_213_out, not_214_out, not_215_out, not_216_out, not_217_out,
       not_218_out, not_219_out, not_220_out, not_221_out, not_222_out, not_223_out, not_224_out,
       not_225_out, not_226_out, not_227_out, not_228_out, not_229_out, not_230_out, not_231_out,
       not_232_out, not_233_out, not_234_out, not_235_out, not_236_out, not_237_out, not_238_out,
       not_239_out, not_240_out, not_241_out, not_242_out, not_243_out, not_244_out, not_245_out,
       not_246_out, not_247_out, not_248_out, not_249_out, not_250_out, not_251_out, not_252_out,
       not_253_out, not_254_out, not_255_out, not_256_out, not_257_out, not_258_out, not_259_out,
       not_260_out, not_261_out, not_262_out, not_263_out, not_264_out, not_265_out, not_266_out,
       not_267_out, not_268_out, not_269_out, not_270_out, not_271_out, not_272_out, not_273_out,
       not_274_out, not_275_out, not_276_out, not_277_out, not_278_out, not_279_out, not_280_out,
       not_281_out, not_282_out, not_283_out, not_284_out, not_285_out, not_286_out, not_287_out,
       not_288_out, not_289_out, not_290_out, not_291_out, not_292_out, not_293_out, not_294_out,
       not_295_out, not_296_out, not_297_out, not_298_out, not_299_out, not_300_out, not_301_out,
       not_302_out, not_303_out, not_304_out, not_305_out, not_306_out, not_307_out, not_308_out;

  not not_1 (not_1_out, OP5);
  not not_2 (not_2_out, OP4);
  not not_3 (not_3_out, OP3);
  not not_4 (not_4_out, OP2);
  not not_5 (not_5_out, OP1);
  not not_6 (not_6_out, OP0);
  not not_7 (not_7_out, F4);
  not not_8 (not_8_out, F3);
  not not_9 (not_9_out, F2);
  not not_10 (not_10_out, F1);
  not not_11 (not_11_out, F0);
  not not_12 (not_12_out, OP5);
  not not_13 (not_13_out, OP4);
  not not_14 (not_14_out, OP3);
  not not_15 (not_15_out, OP2);
  not not_16 (not_16_out, OP1);
  not not_17 (not_17_out, OP0);
  not not_18 (not_18_out, F4);
  not not_19 (not_19_out, F3);
  not not_20 (not_20_out, F2);
  not not_21 (not_21_out, F1);
  not not_22 (not_22_out, OP5);
  not not_23 (not_23_out, OP4);
  not not_24 (not_24_out, OP3);
  not not_25 (not_25_out, OP2);
  not not_26 (not_26_out, OP1);
  not not_27 (not_27_out, OP0);
  not not_28 (not_28_out, F4);
  not not_29 (not_29_out, F3);
  not not_30 (not_30_out, F2);
  not not_31 (not_31_out, F0);
  not not_32 (not_32_out, OP5);
  not not_33 (not_33_out, OP4);
  not not_34 (not_34_out, OP3);
  not not_35 (not_35_out, OP2);
  not not_36 (not_36_out, OP1);
  not not_37 (not_37_out, OP0);
  not not_38 (not_38_out, F4);
  not not_39 (not_39_out, F3);
  not not_40 (not_40_out, F1);
  not not_41 (not_41_out, F0);
  not not_42 (not_42_out, OP5);
  not not_43 (not_43_out, OP4);
  not not_44 (not_44_out, OP3);
  not not_45 (not_45_out, OP2);
  not not_46 (not_46_out, OP1);
  not not_47 (not_47_out, OP0);
  not not_48 (not_48_out, F4);
  not not_49 (not_49_out, F3);
  not not_50 (not_50_out, F1);
  not not_51 (not_51_out, OP5);
  not not_52 (not_52_out, OP4);
  not not_53 (not_53_out, OP3);
  not not_54 (not_54_out, OP2);
  not not_55 (not_55_out, OP1);
  not not_56 (not_56_out, OP0);
  not not_57 (not_57_out, F4);
  not not_58 (not_58_out, F3);
  not not_59 (not_59_out, OP5);
  not not_60 (not_60_out, OP4);
  not not_61 (not_61_out, OP3);
  not not_62 (not_62_out, OP2);
  not not_63 (not_63_out, OP1);
  not not_64 (not_64_out, OP0);
  not not_65 (not_65_out, F4);
  not not_66 (not_66_out, F2);
  not not_67 (not_67_out, F0);
  not not_68 (not_68_out, OP5);
  not not_69 (not_69_out, OP4);
  not not_70 (not_70_out, OP3);
  not not_71 (not_71_out, OP2);
  not not_72 (not_72_out, OP1);
  not not_73 (not_73_out, OP0);
  not not_74 (not_74_out, F4);
  not not_75 (not_75_out, F2);
  not not_76 (not_76_out, OP5);
  not not_77 (not_77_out, OP4);
  not not_78 (not_78_out, OP3);
  not not_79 (not_79_out, OP2);
  not not_80 (not_80_out, OP1);
  not not_81 (not_81_out, OP0);
  not not_82 (not_82_out, F5);
  not not_83 (not_83_out, F4);
  not not_84 (not_84_out, F2);
  not not_85 (not_85_out, F1);
  not not_86 (not_86_out, F0);
  not not_87 (not_87_out, OP5);
  not not_88 (not_88_out, OP4);
  not not_89 (not_89_out, OP3);
  not not_90 (not_90_out, OP2);
  not not_91 (not_91_out, OP1);
  not not_92 (not_92_out, OP0);
  not not_93 (not_93_out, F5);
  not not_94 (not_94_out, F4);
  not not_95 (not_95_out, F1);
  not not_96 (not_96_out, F0);
  not not_97 (not_97_out, OP5);
  not not_98 (not_98_out, OP4);
  not not_99 (not_99_out, OP3);
  not not_100 (not_100_out, OP1);
  not not_101 (not_101_out, OP0);
  not not_102 (not_102_out, OP5);
  not not_103 (not_103_out, OP4);
  not not_104 (not_104_out, OP3);
  not not_105 (not_105_out, OP1);
  not not_106 (not_106_out, OP5);
  not not_107 (not_107_out, OP4);
  not not_108 (not_108_out, OP2);
  not not_109 (not_109_out, OP1);
  not not_110 (not_110_out, OP0);
  not not_111 (not_111_out, OP5);
  not not_112 (not_112_out, OP4);
  not not_113 (not_113_out, OP1);
  not not_114 (not_114_out, OP0);
  not not_115 (not_115_out, OP5);
  not not_116 (not_116_out, OP4);
  not not_117 (not_117_out, OP2);
  not not_118 (not_118_out, OP1);
  not not_119 (not_119_out, OP5);
  not not_120 (not_120_out, OP4);
  not not_121 (not_121_out, OP2);
  not not_122 (not_122_out, OP0);
  not not_123 (not_123_out, OP5);
  not not_124 (not_124_out, OP4);
  not not_125 (not_125_out, OP1);
  not not_126 (not_126_out, OP4);
  not not_127 (not_127_out, OP3);
  not not_128 (not_128_out, OP2);
  not not_129 (not_129_out, OP4);
  not not_130 (not_130_out, OP2);
  not not_131 (not_131_out, OP5);
  not not_132 (not_132_out, OP4);
  not not_133 (not_133_out, OP3);
  not not_134 (not_134_out, OP2);
  not not_135 (not_135_out, OP1);
  not not_136 (not_136_out, OP0);
  not not_137 (not_137_out, F5);
  not not_138 (not_138_out, F4);
  not not_139 (not_139_out, F3);
  not not_140 (not_140_out, F1);
  not not_141 (not_141_out, F0);
  not not_142 (not_142_out, OP5);
  not not_143 (not_143_out, OP4);
  not not_144 (not_144_out, OP3);
  not not_145 (not_145_out, OP2);
  not not_146 (not_146_out, OP1);
  not not_147 (not_147_out, OP0);
  not not_148 (not_148_out, F5);
  not not_149 (not_149_out, F4);
  not not_150 (not_150_out, F3);
  not not_151 (not_151_out, OP4);
  not not_152 (not_152_out, OP2);
  not not_153 (not_153_out, OP1);
  not not_154 (not_154_out, OP5);
  not not_155 (not_155_out, OP4);
  not not_156 (not_156_out, OP3);
  not not_157 (not_157_out, OP5);
  not not_158 (not_158_out, OP4);
  not not_159 (not_159_out, OP3);
  not not_160 (not_160_out, OP2);
  not not_161 (not_161_out, OP1);
  not not_162 (not_162_out, OP0);
  not not_163 (not_163_out, F5);
  not not_164 (not_164_out, F4);
  not not_165 (not_165_out, F3);
  not not_166 (not_166_out, F2);
  not not_167 (not_167_out, F1);
  not not_168 (not_168_out, F0);
  not not_169 (not_169_out, OP5);
  not not_170 (not_170_out, OP4);
  not not_171 (not_171_out, OP3);
  not not_172 (not_172_out, OP2);
  not not_173 (not_173_out, OP1);
  not not_174 (not_174_out, OP0);
  not not_175 (not_175_out, F5);
  not not_176 (not_176_out, F4);
  not not_177 (not_177_out, F3);
  not not_178 (not_178_out, F2);
  not not_179 (not_179_out, OP5);
  not not_180 (not_180_out, OP4);
  not not_181 (not_181_out, OP3);
  not not_182 (not_182_out, OP2);
  not not_183 (not_183_out, OP1);
  not not_184 (not_184_out, OP0);
  not not_185 (not_185_out, F5);
  not not_186 (not_186_out, F4);
  not not_187 (not_187_out, F3);
  not not_188 (not_188_out, F2);
  not not_189 (not_189_out, F0);
  not not_190 (not_190_out, OP5);
  not not_191 (not_191_out, OP4);
  not not_192 (not_192_out, OP3);
  not not_193 (not_193_out, OP2);
  not not_194 (not_194_out, OP1);
  not not_195 (not_195_out, OP0);
  not not_196 (not_196_out, F4);
  not not_197 (not_197_out, F3);
  not not_198 (not_198_out, F2);
  not not_199 (not_199_out, F1);
  not not_200 (not_200_out, F0);
  not not_201 (not_201_out, OP5);
  not not_202 (not_202_out, OP4);
  not not_203 (not_203_out, OP3);
  not not_204 (not_204_out, OP2);
  not not_205 (not_205_out, OP1);
  not not_206 (not_206_out, OP0);
  not not_207 (not_207_out, F4);
  not not_208 (not_208_out, F3);
  not not_209 (not_209_out, F2);
  not not_210 (not_210_out, F1);
  not not_211 (not_211_out, OP5);
  not not_212 (not_212_out, OP4);
  not not_213 (not_213_out, OP3);
  not not_214 (not_214_out, OP2);
  not not_215 (not_215_out, OP1);
  not not_216 (not_216_out, OP0);
  not not_217 (not_217_out, F4);
  not not_218 (not_218_out, F3);
  not not_219 (not_219_out, F2);
  not not_220 (not_220_out, F0);
  not not_221 (not_221_out, OP5);
  not not_222 (not_222_out, OP4);
  not not_223 (not_223_out, OP3);
  not not_224 (not_224_out, OP2);
  not not_225 (not_225_out, OP1);
  not not_226 (not_226_out, OP0);
  not not_227 (not_227_out, F4);
  not not_228 (not_228_out, F3);
  not not_229 (not_229_out, F1);
  not not_230 (not_230_out, F0);
  not not_231 (not_231_out, OP5);
  not not_232 (not_232_out, OP4);
  not not_233 (not_233_out, OP3);
  not not_234 (not_234_out, OP2);
  not not_235 (not_235_out, OP1);
  not not_236 (not_236_out, OP0);
  not not_237 (not_237_out, F4);
  not not_238 (not_238_out, F3);
  not not_239 (not_239_out, F1);
  not not_240 (not_240_out, OP5);
  not not_241 (not_241_out, OP4);
  not not_242 (not_242_out, OP3);
  not not_243 (not_243_out, OP2);
  not not_244 (not_244_out, OP1);
  not not_245 (not_245_out, OP0);
  not not_246 (not_246_out, F4);
  not not_247 (not_247_out, F3);
  not not_248 (not_248_out, OP5);
  not not_249 (not_249_out, OP4);
  not not_250 (not_250_out, OP3);
  not not_251 (not_251_out, OP2);
  not not_252 (not_252_out, OP1);
  not not_253 (not_253_out, OP0);
  not not_254 (not_254_out, F4);
  not not_255 (not_255_out, F2);
  not not_256 (not_256_out, F0);
  not not_257 (not_257_out, OP5);
  not not_258 (not_258_out, OP4);
  not not_259 (not_259_out, OP3);
  not not_260 (not_260_out, OP2);
  not not_261 (not_261_out, OP1);
  not not_262 (not_262_out, OP0);
  not not_263 (not_263_out, F4);
  not not_264 (not_264_out, F2);
  not not_265 (not_265_out, OP5);
  not not_266 (not_266_out, OP4);
  not not_267 (not_267_out, OP3);
  not not_268 (not_268_out, OP2);
  not not_269 (not_269_out, OP1);
  not not_270 (not_270_out, OP0);
  not not_271 (not_271_out, F5);
  not not_272 (not_272_out, F4);
  not not_273 (not_273_out, F1);
  not not_274 (not_274_out, F0);
  not not_275 (not_275_out, OP5);
  not not_276 (not_276_out, OP4);
  not not_277 (not_277_out, OP3);
  not not_278 (not_278_out, OP1);
  not not_279 (not_279_out, OP0);
  not not_280 (not_280_out, OP5);
  not not_281 (not_281_out, OP4);
  not not_282 (not_282_out, OP3);
  not not_283 (not_283_out, OP1);
  not not_284 (not_284_out, OP4);
  not not_285 (not_285_out, OP2);
  not not_286 (not_286_out, OP5);
  not not_287 (not_287_out, OP4);
  not not_288 (not_288_out, OP3);
  not not_289 (not_289_out, OP2);
  not not_290 (not_290_out, OP1);
  not not_291 (not_291_out, OP0);
  not not_292 (not_292_out, F5);
  not not_293 (not_293_out, F4);
  not not_294 (not_294_out, F3);
  not not_295 (not_295_out, F1);
  not not_296 (not_296_out, F0);
  not not_297 (not_297_out, OP5);
  not not_298 (not_298_out, OP4);
  not not_299 (not_299_out, OP3);
  not not_300 (not_300_out, OP2);
  not not_301 (not_301_out, OP1);
  not not_302 (not_302_out, OP0);
  not not_303 (not_303_out, F5);
  not not_304 (not_304_out, F4);
  not not_305 (not_305_out, F3);
  not not_306 (not_306_out, OP4);
  not not_307 (not_307_out, OP2);
  not not_308 (not_308_out, OP1);
  and and_1 (and_1_out, not_1_out, not_2_out, not_3_out, not_4_out, not_5_out, not_6_out, F5, not_7_out, not_8_out, not_9_out, not_10_out, not_11_out);
  and and_2 (and_2_out, not_12_out, not_13_out, not_14_out, not_15_out, not_16_out, not_17_out, F5, not_18_out, not_19_out, not_20_out, not_21_out, F0);
  and and_3 (and_3_out, not_22_out, not_23_out, not_24_out, not_25_out, not_26_out, not_27_out, F5, not_28_out, not_29_out, not_30_out, F1, not_31_out);
  and and_4 (and_4_out, not_32_out, not_33_out, not_34_out, not_35_out, not_36_out, not_37_out, F5, not_38_out, not_39_out, F2, not_40_out, not_41_out);
  and and_5 (and_5_out, not_42_out, not_43_out, not_44_out, not_45_out, not_46_out, not_47_out, F5, not_48_out, not_49_out, F2, not_50_out, F0);
  and and_6 (and_6_out, not_51_out, not_52_out, not_53_out, not_54_out, not_55_out, not_56_out, F5, not_57_out, not_58_out, F2, F1, F0);
  and and_7 (and_7_out, not_59_out, not_60_out, not_61_out, not_62_out, not_63_out, not_64_out, F5, not_65_out, F3, not_66_out, F1, not_67_out);
  and and_8 (and_8_out, not_68_out, not_69_out, not_70_out, not_71_out, not_72_out, not_73_out, F5, not_74_out, F3, not_75_out, F1, F0);
  and and_9 (and_9_out, not_76_out, not_77_out, not_78_out, not_79_out, not_80_out, not_81_out, not_82_out, not_83_out, F3, not_84_out, not_85_out, not_86_out);
  and and_10 (and_10_out, not_87_out, not_88_out, not_89_out, not_90_out, not_91_out, not_92_out, not_93_out, not_94_out, F3, F2, not_95_out, not_96_out);
  and and_11 (and_11_out, not_97_out, not_98_out, not_99_out, OP2, not_100_out, not_101_out);
  and and_12 (and_12_out, not_102_out, not_103_out, not_104_out, OP2, not_105_out, OP0);
  and and_13 (and_13_out, not_106_out, not_107_out, OP3, not_108_out, not_109_out, not_110_out);
  and and_14 (and_14_out, not_111_out, not_112_out, OP3, OP2, not_113_out, not_114_out);
  and and_15 (and_15_out, not_115_out, not_116_out, OP3, not_117_out, not_118_out, OP0);
  and and_16 (and_16_out, not_119_out, not_120_out, OP3, not_121_out, OP1, not_122_out);
  and and_17 (and_17_out, not_123_out, not_124_out, OP3, OP2, not_125_out, OP0);
  and and_18 (and_18_out, OP5, not_126_out, not_127_out, not_128_out, OP1, OP0);
  and and_19 (and_19_out, OP5, not_129_out, OP3, not_130_out, OP1, OP0);
  and and_20 (and_20_out, not_131_out, not_132_out, not_133_out, not_134_out, not_135_out, not_136_out, not_137_out, not_138_out, not_139_out, F2, not_140_out, not_141_out);
  and and_21 (and_21_out, not_142_out, not_143_out, not_144_out, not_145_out, not_146_out, not_147_out, not_148_out, not_149_out, not_150_out, F2, F1, F0);
  and and_22 (and_22_out, OP5, not_151_out, OP3, not_152_out, not_153_out, OP0);
  and and_23 (and_23_out, not_154_out, not_155_out, not_156_out, OP2, OP1, OP0);
  and and_24 (and_24_out, not_157_out, not_158_out, not_159_out, not_160_out, not_161_out, not_162_out, not_163_out, not_164_out, not_165_out, not_166_out, not_167_out, not_168_out);
  and and_25 (and_25_out, not_169_out, not_170_out, not_171_out, not_172_out, not_173_out, not_174_out, not_175_out, not_176_out, not_177_out, not_178_out, F1, F0);
  and and_26 (and_26_out, not_179_out, not_180_out, not_181_out, not_182_out, not_183_out, not_184_out, not_185_out, not_186_out, not_187_out, not_188_out, F1, not_189_out);
  and and_27 (and_27_out, not_190_out, not_191_out, not_192_out, not_193_out, not_194_out, not_195_out, F5, not_196_out, not_197_out, not_198_out, not_199_out, not_200_out);
  and and_28 (and_28_out, not_201_out, not_202_out, not_203_out, not_204_out, not_205_out, not_206_out, F5, not_207_out, not_208_out, not_209_out, not_210_out, F0);
  and and_29 (and_29_out, not_211_out, not_212_out, not_213_out, not_214_out, not_215_out, not_216_out, F5, not_217_out, not_218_out, not_219_out, F1, not_220_out);
  and and_30 (and_30_out, not_221_out, not_222_out, not_223_out, not_224_out, not_225_out, not_226_out, F5, not_227_out, not_228_out, F2, not_229_out, not_230_out);
  and and_31 (and_31_out, not_231_out, not_232_out, not_233_out, not_234_out, not_235_out, not_236_out, F5, not_237_out, not_238_out, F2, not_239_out, F0);
  and and_32 (and_32_out, not_240_out, not_241_out, not_242_out, not_243_out, not_244_out, not_245_out, F5, not_246_out, not_247_out, F2, F1, F0);
  and and_33 (and_33_out, not_248_out, not_249_out, not_250_out, not_251_out, not_252_out, not_253_out, F5, not_254_out, F3, not_255_out, F1, not_256_out);
  and and_34 (and_34_out, not_257_out, not_258_out, not_259_out, not_260_out, not_261_out, not_262_out, F5, not_263_out, F3, not_264_out, F1, F0);
  and and_35 (and_35_out, not_265_out, not_266_out, not_267_out, not_268_out, not_269_out, not_270_out, not_271_out, not_272_out, F3, F2, not_273_out, not_274_out);
  and and_36 (and_36_out, not_275_out, not_276_out, not_277_out, OP2, not_278_out, not_279_out);
  and and_37 (and_37_out, not_280_out, not_281_out, not_282_out, OP2, not_283_out, OP0);
  and and_38 (and_38_out, OP5, not_284_out, OP3, not_285_out, OP1, OP0);
  and and_39 (and_39_out, not_286_out, not_287_out, not_288_out, not_289_out, not_290_out, not_291_out, not_292_out, not_293_out, not_294_out, F2, not_295_out, not_296_out);
  and and_40 (and_40_out, not_297_out, not_298_out, not_299_out, not_300_out, not_301_out, not_302_out, not_303_out, not_304_out, not_305_out, F2, F1, F0);
  and and_41 (and_41_out, OP5, not_306_out, OP3, not_307_out, not_308_out, OP0);
  or or_1 (RsUsed, and_1_out, and_2_out, and_3_out, and_4_out, and_5_out, and_6_out, and_7_out, and_8_out, and_9_out, and_10_out, and_11_out, and_12_out, and_13_out, and_14_out, and_15_out, and_16_out, and_17_out, and_18_out, and_19_out, and_20_out, and_21_out, and_22_out, and_23_out);
  or or_2 (RtUsed, and_24_out, and_25_out, and_26_out, and_27_out, and_28_out, and_29_out, and_30_out, and_31_out, and_32_out, and_33_out, and_34_out, and_35_out, and_36_out, and_37_out, and_38_out, and_39_out, and_40_out, and_41_out);
endmodule
